// Logisim project 实验电路-软件2307-20231601-张子琪.circ as structural Verilog: 36 circuits, main circuit 实验3-算术逻辑运算单元ALU
module \实验1_7段数码管显示译码器不显示_9的组件  (
  input  B3,
  input  B2,
  input  B1,
  input  B0,
  output a,
  output b,
  output c,
  output d,
  output e,
  output f,
  output g
);

  wire and_1_out, and_2_out, and_3_out, and_4_out, and_5_out, and_6_out, and_7_out, and_8_out, and_9_out,
       and_10_out, and_11_out, and_12_out, and_13_out, and_14_out, and_15_out, and_16_out, and_17_out,
       and_18_out, and_19_out, and_20_out, and_21_out, and_22_out, and_23_out, and_24_out, and_25_out,
       and_26_out, not_1_out, not_2_out, not_3_out, not_4_out, not_5_out, not_6_out, not_7_out, not_8_out,
       not_9_out, not_10_out, not_11_out, not_12_out, not_13_out, not_14_out, not_15_out, not_16_out,
       not_17_out, not_18_out, not_19_out, not_20_out, not_21_out, not_22_out, not_23_out, not_24_out,
       not_25_out, not_26_out, not_27_out, not_28_out, not_29_out, not_30_out, not_31_out, not_32_out,
       not_33_out, not_34_out, not_35_out, not_36_out, not_37_out, not_38_out, not_39_out, not_40_out,
       not_41_out, not_42_out, not_43_out, not_44_out, not_45_out, not_46_out, not_47_out, not_48_out,
       not_49_out, not_50_out, not_51_out, not_52_out;

  not not_1 (not_1_out, B3);
  not not_2 (not_2_out, B2);
  and and_1 (and_1_out, not_1_out, not_2_out, not_3_out);
  not not_3 (not_3_out, B0);
  not not_4 (not_4_out, B3);
  and and_2 (and_2_out, not_4_out, B1);
  not not_5 (not_5_out, B3);
  and and_3 (and_3_out, not_5_out, B2, B0);
  and and_4 (and_4_out, B3, not_6_out, not_7_out);
  not not_6 (not_6_out, B2);
  not not_7 (not_7_out, B1);
  not not_8 (not_8_out, B3);
  and and_5 (and_5_out, not_8_out, not_9_out);
  not not_9 (not_9_out, B2);
  not not_10 (not_10_out, B3);
  and and_6 (and_6_out, not_10_out, not_11_out, not_12_out);
  not not_11 (not_11_out, B1);
  not not_12 (not_12_out, B0);
  not not_13 (not_13_out, B2);
  and and_7 (and_7_out, not_13_out, not_14_out);
  not not_14 (not_14_out, B1);
  not not_15 (not_15_out, B3);
  and and_8 (and_8_out, not_15_out, B1, B0);
  not not_16 (not_16_out, B2);
  and and_9 (and_9_out, not_16_out, not_17_out);
  not not_17 (not_17_out, B1);
  not not_18 (not_18_out, B3);
  and and_10 (and_10_out, not_18_out, B0);
  not not_19 (not_19_out, B3);
  and and_11 (and_11_out, not_19_out, B2);
  not not_20 (not_20_out, B3);
  not not_21 (not_21_out, B2);
  not not_22 (not_22_out, B0);
  not not_23 (not_23_out, B3);
  not not_24 (not_24_out, B2);
  not not_25 (not_25_out, B3);
  not not_26 (not_26_out, B0);
  not not_27 (not_27_out, B3);
  not not_28 (not_28_out, B1);
  not not_29 (not_29_out, B2);
  not not_30 (not_30_out, B1);
  not not_31 (not_31_out, B2);
  and and_12 (and_12_out, not_31_out, not_32_out, not_33_out);
  not not_32 (not_32_out, B1);
  not not_33 (not_33_out, B0);
  not not_34 (not_34_out, B3);
  and and_13 (and_13_out, not_34_out, B1, not_35_out);
  not not_35 (not_35_out, B0);
  not not_36 (not_36_out, B3);
  not not_37 (not_37_out, B1);
  and and_14 (and_14_out, not_36_out, not_37_out, not_38_out);
  not not_38 (not_38_out, B0);
  not not_39 (not_39_out, B3);
  and and_15 (and_15_out, not_39_out, B2, not_40_out);
  not not_40 (not_40_out, B1);
  not not_41 (not_41_out, B3);
  and and_16 (and_16_out, not_41_out, B2, not_42_out);
  not not_42 (not_42_out, B0);
  and and_17 (and_17_out, B3, not_43_out, not_44_out);
  not not_43 (not_43_out, B2);
  not not_44 (not_44_out, B1);
  not not_45 (not_45_out, B3);
  and and_18 (and_18_out, not_45_out, not_46_out, B1);
  not not_46 (not_46_out, B2);
  not not_47 (not_47_out, B3);
  and and_19 (and_19_out, not_47_out, B2, not_48_out);
  not not_48 (not_48_out, B1);
  not not_49 (not_49_out, B3);
  and and_20 (and_20_out, not_49_out, B2, not_50_out);
  not not_50 (not_50_out, B0);
  and and_21 (and_21_out, B3, not_51_out, not_52_out);
  not not_51 (not_51_out, B2);
  not not_52 (not_52_out, B1);
  or or_1 (a, and_1_out, and_2_out, and_3_out, and_4_out);
  or or_2 (b, and_5_out, and_6_out, and_7_out, and_8_out);
  or or_3 (c, and_9_out, and_10_out, and_11_out);
  and and_22 (and_22_out, not_20_out, not_21_out, not_22_out);
  and and_23 (and_23_out, not_23_out, not_24_out, B1);
  and and_24 (and_24_out, not_25_out, B1, not_26_out);
  and and_25 (and_25_out, not_27_out, B2, not_28_out, B0);
  and and_26 (and_26_out, B3, not_29_out, not_30_out);
  or or_4 (e, and_12_out, and_13_out);
  or or_5 (f, and_14_out, and_15_out, and_16_out, and_17_out);
  or or_6 (g, and_18_out, and_19_out, and_20_out, and_21_out);
  or or_7 (d, and_22_out, and_23_out, and_24_out, and_25_out, and_26_out);
endmodule

module \实验1_7段数码管显示译码器_不显示_9  (
);

  wire clock_1_out, \实验1_7段数码管显示译码器不显示_9的组件_1_a , \实验1_7段数码管显示译码器不显示_9的组件_1_b , \实验1_7段数码管显示译码器不显示_9的组件_1_c ,
       \实验1_7段数码管显示译码器不显示_9的组件_1_d , \实验1_7段数码管显示译码器不显示_9的组件_1_e , \实验1_7段数码管显示译码器不显示_9的组件_1_f ,
       \实验1_7段数码管显示译码器不显示_9的组件_1_g ;
  wire [3:0] counter_1_q;

  Counter #(.width(4), .max('hf), .ongoal("wrap"), .trigger("rising"), .behavior("new")) counter_1 (
    .D(counter_1_q), .Q(counter_1_q), .clk(clock_1_out));  // open: load, count, carry, clr, preset, down
  Clock #(.highDuration(8), .lowDuration(8)) clock_1 (.out(clock_1_out));
  \实验1_7段数码管显示译码器不显示_9的组件  \u_实验1_7段数码管显示译码器不显示_9的组件_1  (
    .B3(counter_1_q[3]), .B2(counter_1_q[2]), .B1(counter_1_q[1]), .a(\实验1_7段数码管显示译码器不显示_9的组件_1_a ),
    .B0(counter_1_q[0]), .b(\实验1_7段数码管显示译码器不显示_9的组件_1_b ), .c(\实验1_7段数码管显示译码器不显示_9的组件_1_c ),
    .d(\实验1_7段数码管显示译码器不显示_9的组件_1_d ), .e(\实验1_7段数码管显示译码器不显示_9的组件_1_e ), .f(\实验1_7段数码管显示译码器不显示_9的组件_1_f ),
    .g(\实验1_7段数码管显示译码器不显示_9的组件_1_g ));
  _7_Segment_Display #(.active("true")) u_7_segment_display_1 (
    .g(\实验1_7段数码管显示译码器不显示_9的组件_1_g ), .f(\实验1_7段数码管显示译码器不显示_9的组件_1_f ), .a(\实验1_7段数码管显示译码器不显示_9的组件_1_a ),
    .b(\实验1_7段数码管显示译码器不显示_9的组件_1_b ), .e(\实验1_7段数码管显示译码器不显示_9的组件_1_e ), .d(\实验1_7段数码管显示译码器不显示_9的组件_1_d ),
    .c(\实验1_7段数码管显示译码器不显示_9的组件_1_c ));  // open: dp
endmodule

module \实验1_7段数码管显示译码器组件_显示0_F  (
  input  B3,
  input  B2,
  input  B1,
  input  B0,
  output a,
  output b,
  output c,
  output d,
  output e,
  output f,
  output g
);

  wire and_1_out, and_2_out, and_3_out, and_4_out, and_5_out, and_6_out, and_7_out, and_8_out, and_9_out,
       and_10_out, and_11_out, and_12_out, and_13_out, and_14_out, and_15_out, and_16_out, and_17_out,
       and_18_out, and_19_out, and_20_out, and_21_out, and_22_out, and_23_out, and_24_out, and_25_out,
       and_26_out, and_27_out, and_28_out, and_29_out, and_30_out, and_31_out, and_32_out, and_33_out,
       and_34_out, and_35_out, not_1_out, not_2_out, not_3_out, not_4_out, not_5_out, not_6_out, not_7_out,
       not_8_out, not_9_out, not_10_out, not_11_out, not_12_out, not_13_out, not_14_out, not_15_out,
       not_16_out, not_17_out, not_18_out, not_19_out, not_20_out, not_21_out, not_22_out, not_23_out,
       not_24_out, not_25_out, not_26_out, not_27_out, not_28_out, not_29_out, not_30_out, not_31_out,
       not_32_out, not_33_out, not_34_out, not_35_out, not_36_out, not_37_out, not_38_out, not_39_out,
       not_40_out, not_41_out, not_42_out, not_43_out;

  not not_1 (not_1_out, B2);
  and and_1 (and_1_out, not_1_out, not_2_out);
  not not_2 (not_2_out, B0);
  not not_3 (not_3_out, B3);
  and and_2 (and_2_out, not_3_out, B1);
  not not_4 (not_4_out, B3);
  and and_3 (and_3_out, not_4_out, B2, B0);
  and and_4 (and_4_out, B2, B1);
  not not_5 (not_5_out, B2);
  and and_5 (and_5_out, B3, not_5_out, not_6_out);
  not not_6 (not_6_out, B1);
  and and_6 (and_6_out, B3, not_7_out);
  not not_7 (not_7_out, B0);
  not not_8 (not_8_out, B3);
  and and_7 (and_7_out, not_8_out, not_9_out);
  not not_9 (not_9_out, B2);
  not not_10 (not_10_out, B3);
  not not_11 (not_11_out, B1);
  and and_8 (and_8_out, not_10_out, not_11_out, not_12_out);
  not not_12 (not_12_out, B0);
  not not_13 (not_13_out, B2);
  and and_9 (and_9_out, not_13_out, not_14_out);
  not not_14 (not_14_out, B0);
  not not_15 (not_15_out, B3);
  and and_10 (and_10_out, not_15_out, B1, B0);
  not not_16 (not_16_out, B1);
  and and_11 (and_11_out, B3, not_16_out, B0);
  not not_17 (not_17_out, B3);
  and and_12 (and_12_out, not_17_out, not_18_out);
  not not_18 (not_18_out, B1);
  not not_19 (not_19_out, B3);
  and and_13 (and_13_out, not_19_out, B0);
  not not_20 (not_20_out, B1);
  and and_14 (and_14_out, not_20_out, B0);
  not not_21 (not_21_out, B3);
  and and_15 (and_15_out, not_21_out, B2);
  and and_16 (and_16_out, B3, not_22_out);
  not not_22 (not_22_out, B2);
  not not_23 (not_23_out, B3);
  not not_24 (not_24_out, B2);
  and and_17 (and_17_out, not_23_out, not_24_out, not_25_out);
  not not_25 (not_25_out, B0);
  not not_26 (not_26_out, B2);
  and and_18 (and_18_out, not_26_out, B1, B0);
  not not_27 (not_27_out, B1);
  and and_19 (and_19_out, B2, not_27_out, B0);
  and and_20 (and_20_out, B2, B1, not_28_out);
  not not_28 (not_28_out, B0);
  and and_21 (and_21_out, B3, not_29_out);
  not not_29 (not_29_out, B1);
  not not_30 (not_30_out, B2);
  and and_22 (and_22_out, not_30_out, not_31_out);
  not not_31 (not_31_out, B0);
  and and_23 (and_23_out, B1, not_32_out);
  not not_32 (not_32_out, B0);
  and and_24 (and_24_out, B3, B1);
  and and_25 (and_25_out, B3, B2);
  not not_33 (not_33_out, B1);
  and and_26 (and_26_out, not_33_out, not_34_out);
  not not_34 (not_34_out, B0);
  not not_35 (not_35_out, B3);
  and and_27 (and_27_out, not_35_out, B2, not_36_out);
  not not_36 (not_36_out, B1);
  and and_28 (and_28_out, B2, not_37_out);
  not not_37 (not_37_out, B0);
  and and_29 (and_29_out, B3, not_38_out);
  not not_38 (not_38_out, B2);
  and and_30 (and_30_out, B3, B1);
  not not_39 (not_39_out, B2);
  and and_31 (and_31_out, not_39_out, B1);
  and and_32 (and_32_out, B1, not_40_out);
  not not_40 (not_40_out, B0);
  not not_41 (not_41_out, B3);
  and and_33 (and_33_out, not_41_out, B2, not_42_out);
  not not_42 (not_42_out, B1);
  and and_34 (and_34_out, B3, not_43_out);
  not not_43 (not_43_out, B2);
  and and_35 (and_35_out, B3, B0);
  or or_1 (b, and_7_out, and_8_out, and_9_out, and_10_out, and_11_out);
  or or_2 (c, and_12_out, and_13_out, and_14_out, and_15_out, and_16_out);
  or or_3 (d, and_17_out, and_18_out, and_19_out, and_20_out, and_21_out);
  or or_4 (e, and_22_out, and_23_out, and_24_out, and_25_out);
  or or_5 (f, and_26_out, and_27_out, and_28_out, and_29_out, and_30_out);
  or or_6 (g, and_31_out, and_32_out, and_33_out, and_34_out, and_35_out);
  or or_7 (a, and_1_out, and_2_out, and_3_out, and_4_out, and_5_out, and_6_out);
endmodule

module \实验1_7段数码管显示译码器带极性控制端  (
  input  P,
  input  B0,
  input  B1,
  input  B2,
  input  B3,
  output a,
  output b,
  output c,
  output d,
  output e,
  output f,
  output g
);

  wire \实验1_7段数码管显示译码器组件_显示0_f_1_a , \实验1_7段数码管显示译码器组件_显示0_f_1_b , \实验1_7段数码管显示译码器组件_显示0_f_1_c ,
       \实验1_7段数码管显示译码器组件_显示0_f_1_d , \实验1_7段数码管显示译码器组件_显示0_f_1_e , \实验1_7段数码管显示译码器组件_显示0_f_1_f ,
       \实验1_7段数码管显示译码器组件_显示0_f_1_g ;

  \实验1_7段数码管显示译码器组件_显示0_F  \u_实验1_7段数码管显示译码器组件_显示0_f_1  (
    .B3(B3), .B2(B2), .B1(B1), .B0(B0), .a(\实验1_7段数码管显示译码器组件_显示0_f_1_a ), .b(\实验1_7段数码管显示译码器组件_显示0_f_1_b ),
    .c(\实验1_7段数码管显示译码器组件_显示0_f_1_c ), .d(\实验1_7段数码管显示译码器组件_显示0_f_1_d ), .e(\实验1_7段数码管显示译码器组件_显示0_f_1_e ),
    .f(\实验1_7段数码管显示译码器组件_显示0_f_1_f ), .g(\实验1_7段数码管显示译码器组件_显示0_f_1_g ));
  xor xor_1 (a, P, \实验1_7段数码管显示译码器组件_显示0_f_1_a );
  xor xor_2 (b, P, \实验1_7段数码管显示译码器组件_显示0_f_1_b );
  xor xor_3 (c, P, \实验1_7段数码管显示译码器组件_显示0_f_1_c );
  xor xor_4 (d, P, \实验1_7段数码管显示译码器组件_显示0_f_1_d );
  xor xor_5 (e, P, \实验1_7段数码管显示译码器组件_显示0_f_1_e );
  xor xor_6 (f, P, \实验1_7段数码管显示译码器组件_显示0_f_1_f );
  xor xor_7 (g, P, \实验1_7段数码管显示译码器组件_显示0_f_1_g );
endmodule

module \实验1_7段数码管显示译码器_带极性控制端且显示A_F  (
  input  in_1
);

  wire clock_1_out, \实验1_7段数码管显示译码器带极性控制端_1_a , \实验1_7段数码管显示译码器带极性控制端_1_b , \实验1_7段数码管显示译码器带极性控制端_1_c ,
       \实验1_7段数码管显示译码器带极性控制端_1_d , \实验1_7段数码管显示译码器带极性控制端_1_e , \实验1_7段数码管显示译码器带极性控制端_1_f ,
       \实验1_7段数码管显示译码器带极性控制端_1_g ;
  wire [3:0] counter_1_q;

  Clock #(.highDuration(8), .lowDuration(8)) clock_1 (.out(clock_1_out));
  Counter #(.width(4), .max('hf), .ongoal("wrap"), .trigger("rising"), .behavior("new")) counter_1 (
    .D(counter_1_q), .Q(counter_1_q), .clk(clock_1_out));  // open: load, count, carry, clr, preset, down
  \实验1_7段数码管显示译码器带极性控制端  \u_实验1_7段数码管显示译码器带极性控制端_1  (
    .P(in_1), .a(\实验1_7段数码管显示译码器带极性控制端_1_a ), .B0(counter_1_q[0]), .b(\实验1_7段数码管显示译码器带极性控制端_1_b ),
    .B1(counter_1_q[1]), .B2(counter_1_q[2]), .c(\实验1_7段数码管显示译码器带极性控制端_1_c ), .B3(counter_1_q[3]),
    .d(\实验1_7段数码管显示译码器带极性控制端_1_d ), .e(\实验1_7段数码管显示译码器带极性控制端_1_e ), .f(\实验1_7段数码管显示译码器带极性控制端_1_f ),
    .g(\实验1_7段数码管显示译码器带极性控制端_1_g ));
  _7_Segment_Display #(.active("true")) u_7_segment_display_1 (
    .g(\实验1_7段数码管显示译码器带极性控制端_1_g ), .f(\实验1_7段数码管显示译码器带极性控制端_1_f ), .a(\实验1_7段数码管显示译码器带极性控制端_1_a ),
    .b(\实验1_7段数码管显示译码器带极性控制端_1_b ), .e(\实验1_7段数码管显示译码器带极性控制端_1_e ), .d(\实验1_7段数码管显示译码器带极性控制端_1_d ),
    .c(\实验1_7段数码管显示译码器带极性控制端_1_c ));  // open: dp
endmodule

module \实验2_乘法器_组合逻辑电路  (
  input  in_1,
  input  in_2,
  input  in_3,
  input  in_4,
  input  in_5,
  input  in_6,
  input  in_7,
  input  in_8,
  input  [7:0] B,
  input  [7:0] A,
  output [15:0] \结果 
);

  wire A0B1_out, A0B2_out, A0B3_out, A0B4_out, A0B5_out, A0B6_2_out, A0B6_out, A1B0_out, A1B1_out, A1B2_out,
       A1B3_out, A1B4_out, A1B5_out, A1B6_2_out, A1B6_out, A2B0_out, A2B1_out, A2B2_out, A2B3_out, A2B4_out,
       A2B5_out, A2B6_2_out, A2B6_out, A3B0_out, A3B1_out, A3B2_out, A3B3_out, A3B4_out, A3B5_out,
       A3B6_2_out, A3B6_out, A4B0_out, A4B1_out, A4B2_out, A4B3_out, A4B4_out, A4B5_out, A4B6_2_out,
       A4B6_out, A5B0_out, A5B1_out, A5B2_out, A5B3_out, A5B4_out, A5B5_out, A5B6_2_out, A5B6_out, A6B0_out,
       A6B1_out, A6B2_out, A6B3_out, A6B4_out, A6B5_out, A6B6_2_out, A6B6_out, A7B0_out, A7B1_out, A7B2_out,
       A7B3_out, A7B4_out, A7B5_out, A7B6_2_out, A7B6_out, \平时作业1_全加器子电路_1_carry , \平时作业1_全加器子电路_1_sum ,
       \平时作业1_全加器子电路_3_carry , \平时作业1_全加器子电路_4_carry , \平时作业1_全加器子电路_4_sum , \平时作业1_全加器子电路_5_carry ,
       \平时作业1_全加器子电路_5_sum , \平时作业1_全加器子电路_6_carry , \平时作业1_全加器子电路_7_carry , \平时作业1_全加器子电路_7_sum ,
       \平时作业1_全加器子电路_8_carry , \平时作业1_全加器子电路_8_sum , \平时作业1_全加器子电路_9_carry , \平时作业1_全加器子电路_9_sum ,
       \平时作业1_全加器子电路_10_carry , \平时作业1_全加器子电路_11_carry , \平时作业1_全加器子电路_11_sum , \平时作业1_全加器子电路_12_carry ,
       \平时作业1_全加器子电路_12_sum , \平时作业1_全加器子电路_13_carry , \平时作业1_全加器子电路_13_sum , \平时作业1_全加器子电路_14_carry ,
       \平时作业1_全加器子电路_15_carry , \平时作业1_全加器子电路_15_sum , \平时作业1_全加器子电路_16_carry , \平时作业1_全加器子电路_16_sum ,
       \平时作业1_全加器子电路_17_carry , \平时作业1_全加器子电路_17_sum , \平时作业1_全加器子电路_18_carry , \平时作业1_全加器子电路_18_sum ,
       \平时作业1_全加器子电路_19_carry , \平时作业1_全加器子电路_19_sum , \平时作业1_全加器子电路_20_carry , \平时作业1_全加器子电路_20_sum ,
       \平时作业1_全加器子电路_21_carry , \平时作业1_全加器子电路_22_carry , \平时作业1_全加器子电路_22_sum , \平时作业1_全加器子电路_23_carry ,
       \平时作业1_全加器子电路_23_sum , \平时作业1_全加器子电路_24_carry , \平时作业1_全加器子电路_24_sum , \平时作业1_全加器子电路_25_carry ,
       \平时作业1_全加器子电路_26_carry , \平时作业1_全加器子电路_26_sum , \平时作业1_全加器子电路_27_carry , \平时作业1_全加器子电路_27_sum ,
       \平时作业1_全加器子电路_28_carry , \平时作业1_全加器子电路_28_sum , \平时作业1_全加器子电路_29_carry , \平时作业1_全加器子电路_29_sum ,
       \平时作业1_全加器子电路_30_carry , \平时作业1_全加器子电路_30_sum , \平时作业1_全加器子电路_31_carry , \平时作业1_全加器子电路_32_carry ,
       \平时作业1_全加器子电路_32_sum , \平时作业1_全加器子电路_33_carry , \平时作业1_全加器子电路_33_sum , \平时作业1_全加器子电路_34_carry ,
       \平时作业1_全加器子电路_34_sum , \平时作业1_全加器子电路_35_carry , \平时作业1_全加器子电路_35_sum , \平时作业1_全加器子电路_36_carry ,
       \平时作业1_全加器子电路_36_sum , \平时作业1_全加器子电路_37_carry , \平时作业1_全加器子电路_38_carry , \平时作业1_全加器子电路_38_sum ,
       \平时作业1_全加器子电路_39_carry , \平时作业1_全加器子电路_39_sum , \平时作业1_全加器子电路_40_carry , \平时作业1_全加器子电路_40_sum ,
       \平时作业1_全加器子电路_41_carry , \平时作业1_全加器子电路_41_sum , \平时作业1_全加器子电路_42_carry , \平时作业1_全加器子电路_43_carry ,
       \平时作业1_全加器子电路_43_sum , \平时作业1_全加器子电路_44_carry , \平时作业1_全加器子电路_44_sum , \平时作业1_全加器子电路_45_carry ,
       \平时作业1_全加器子电路_45_sum , \平时作业1_全加器子电路_46_carry , \平时作业1_全加器子电路_46_sum , \平时作业1_全加器子电路_47_carry ,
       \平时作业1_全加器子电路_47_sum , \平时作业1_全加器子电路_48_carry , \平时作业1_全加器子电路_48_sum , \平时作业1_全加器子电路_49_carry ,
       \平时作业1_全加器子电路_49_sum , \平时作业1_全加器子电路_50_carry , \平时作业1_全加器子电路_51_carry , \平时作业1_全加器子电路_51_sum ,
       \平时作业1_全加器子电路_52_carry , \平时作业1_全加器子电路_52_sum , \平时作业1_全加器子电路_53_carry , \平时作业1_全加器子电路_54_carry ,
       \平时作业1_全加器子电路_55_carry , \平时作业1_全加器子电路_55_sum , \平时作业1_全加器子电路_56_carry ;

  \平时作业1_全加器子电路  \u_平时作业1_全加器子电路_1  (
    .x(A7B6_2_out), .y(\平时作业1_全加器子电路_4_carry ), .Cin(\平时作业1_全加器子电路_5_carry ), .Carry(\平时作业1_全加器子电路_1_carry ),
    .sum(\平时作业1_全加器子电路_1_sum ));
  \平时作业1_全加器子电路  \u_平时作业1_全加器子电路_2  (
    .x(A7B6_out), .y(\平时作业1_全加器子电路_1_carry ), .Cin(\平时作业1_全加器子电路_3_carry ), .Carry(\结果 [15]), .sum(\结果 [14]));
  and A6B6 (A6B6_out, A[6], B[7]);
  and A7B6 (A7B6_out, A[7], B[7]);
  and A7B6_2 (A7B6_2_out, A[7], B[6]);
  \平时作业1_全加器子电路  \u_平时作业1_全加器子电路_3  (
    .x(\平时作业1_全加器子电路_1_sum ), .y(A6B6_out), .Cin(\平时作业1_全加器子电路_6_carry ), .Carry(\平时作业1_全加器子电路_3_carry ),
    .sum(\结果 [13]));
  and A7B5 (A7B5_out, A[7], B[5]);
  \平时作业1_全加器子电路  \u_平时作业1_全加器子电路_4  (
    .x(A7B5_out), .y(\平时作业1_全加器子电路_7_carry ), .Cin(\平时作业1_全加器子电路_8_carry ), .Carry(\平时作业1_全加器子电路_4_carry ),
    .sum(\平时作业1_全加器子电路_4_sum ));
  and A6B6_2 (A6B6_2_out, A[6], B[6]);
  \平时作业1_全加器子电路  \u_平时作业1_全加器子电路_5  (
    .x(\平时作业1_全加器子电路_4_sum ), .y(A6B6_2_out), .Cin(\平时作业1_全加器子电路_9_carry ), .Carry(\平时作业1_全加器子电路_5_carry ),
    .sum(\平时作业1_全加器子电路_5_sum ));
  and A5B6 (A5B6_out, A[5], B[7]);
  \平时作业1_全加器子电路  \u_平时作业1_全加器子电路_6  (
    .x(\平时作业1_全加器子电路_5_sum ), .y(A5B6_out), .Cin(\平时作业1_全加器子电路_10_carry ), .Carry(\平时作业1_全加器子电路_6_carry ),
    .sum(\结果 [12]));
  // Probe on B
  and A7B4 (A7B4_out, A[7], B[4]);
  \平时作业1_全加器子电路  \u_平时作业1_全加器子电路_7  (
    .x(A7B4_out), .y(\平时作业1_全加器子电路_17_carry ), .Cin(\平时作业1_全加器子电路_11_carry ), .Carry(\平时作业1_全加器子电路_7_carry ),
    .sum(\平时作业1_全加器子电路_7_sum ));
  and A6B5 (A6B5_out, A[6], B[5]);
  \平时作业1_全加器子电路  \u_平时作业1_全加器子电路_8  (
    .x(\平时作业1_全加器子电路_7_sum ), .y(A6B5_out), .Cin(\平时作业1_全加器子电路_12_carry ), .Carry(\平时作业1_全加器子电路_8_carry ),
    .sum(\平时作业1_全加器子电路_8_sum ));
  and A5B6_2 (A5B6_2_out, A[5], B[6]);
  \平时作业1_全加器子电路  \u_平时作业1_全加器子电路_9  (
    .x(\平时作业1_全加器子电路_8_sum ), .y(A5B6_2_out), .Cin(\平时作业1_全加器子电路_13_carry ), .Carry(\平时作业1_全加器子电路_9_carry ),
    .sum(\平时作业1_全加器子电路_9_sum ));
  and A4B6 (A4B6_out, A[4], B[7]);
  \平时作业1_全加器子电路  \u_平时作业1_全加器子电路_10  (
    .x(\平时作业1_全加器子电路_9_sum ), .y(A4B6_out), .Cin(\平时作业1_全加器子电路_14_carry ), .Carry(\平时作业1_全加器子电路_10_carry ),
    .sum(\结果 [11]));
  and A6B4 (A6B4_out, A[6], B[4]);
  \平时作业1_全加器子电路  \u_平时作业1_全加器子电路_11  (
    .x(\平时作业1_全加器子电路_17_sum ), .y(A6B4_out), .Cin(\平时作业1_全加器子电路_18_carry ), .Carry(\平时作业1_全加器子电路_11_carry ),
    .sum(\平时作业1_全加器子电路_11_sum ));
  and A5B5 (A5B5_out, A[5], B[5]);
  \平时作业1_全加器子电路  \u_平时作业1_全加器子电路_12  (
    .x(\平时作业1_全加器子电路_11_sum ), .y(A5B5_out), .Cin(\平时作业1_全加器子电路_19_carry ), .Carry(\平时作业1_全加器子电路_12_carry ),
    .sum(\平时作业1_全加器子电路_12_sum ));
  and A4B6_2 (A4B6_2_out, A[4], B[6]);
  \平时作业1_全加器子电路  \u_平时作业1_全加器子电路_13  (
    .x(\平时作业1_全加器子电路_12_sum ), .y(A4B6_2_out), .Cin(\平时作业1_全加器子电路_20_carry ),
    .Carry(\平时作业1_全加器子电路_13_carry ), .sum(\平时作业1_全加器子电路_13_sum ));
  and A3B6 (A3B6_out, A[3], B[7]);
  \平时作业1_全加器子电路  \u_平时作业1_全加器子电路_14  (
    .x(\平时作业1_全加器子电路_13_sum ), .y(A3B6_out), .Cin(\平时作业1_全加器子电路_21_carry ), .Carry(\平时作业1_全加器子电路_14_carry ),
    .sum(\结果 [10]));
  // Probe on A
  \平时作业1_全加器子电路  \u_平时作业1_全加器子电路_15  (
    .x(in_1), .y(A7B1_out), .Cin(\平时作业1_全加器子电路_32_carry ), .Carry(\平时作业1_全加器子电路_15_carry ),
    .sum(\平时作业1_全加器子电路_15_sum ));
  \平时作业1_全加器子电路  \u_平时作业1_全加器子电路_16  (
    .x(\平时作业1_全加器子电路_15_carry ), .y(A7B2_out), .Cin(\平时作业1_全加器子电路_26_carry ),
    .Carry(\平时作业1_全加器子电路_16_carry ), .sum(\平时作业1_全加器子电路_16_sum ));
  and A7B3 (A7B3_out, A[7], B[3]);
  and A6B3 (A6B3_out, A[6], B[3]);
  \平时作业1_全加器子电路  \u_平时作业1_全加器子电路_17  (
    .x(\平时作业1_全加器子电路_16_carry ), .y(A7B3_out), .Cin(\平时作业1_全加器子电路_22_carry ),
    .Carry(\平时作业1_全加器子电路_17_carry ), .sum(\平时作业1_全加器子电路_17_sum ));
  and A5B4 (A5B4_out, A[5], B[4]);
  \平时作业1_全加器子电路  \u_平时作业1_全加器子电路_18  (
    .x(\平时作业1_全加器子电路_22_sum ), .y(A5B4_out), .Cin(\平时作业1_全加器子电路_28_carry ), .Carry(\平时作业1_全加器子电路_18_carry ),
    .sum(\平时作业1_全加器子电路_18_sum ));
  and A4B5 (A4B5_out, A[4], B[5]);
  \平时作业1_全加器子电路  \u_平时作业1_全加器子电路_19  (
    .x(\平时作业1_全加器子电路_18_sum ), .y(A4B5_out), .Cin(\平时作业1_全加器子电路_23_carry ), .Carry(\平时作业1_全加器子电路_19_carry ),
    .sum(\平时作业1_全加器子电路_19_sum ));
  and A3B6_2 (A3B6_2_out, A[3], B[6]);
  \平时作业1_全加器子电路  \u_平时作业1_全加器子电路_20  (
    .x(\平时作业1_全加器子电路_19_sum ), .y(A3B6_2_out), .Cin(\平时作业1_全加器子电路_24_carry ),
    .Carry(\平时作业1_全加器子电路_20_carry ), .sum(\平时作业1_全加器子电路_20_sum ));
  and A2B6 (A2B6_out, A[2], B[7]);
  \平时作业1_全加器子电路  \u_平时作业1_全加器子电路_21  (
    .x(\平时作业1_全加器子电路_20_sum ), .y(A2B6_out), .Cin(\平时作业1_全加器子电路_25_carry ), .Carry(\平时作业1_全加器子电路_21_carry ),
    .sum(\结果 [9]));
  and A7B2 (A7B2_out, A[7], B[2]);
  and A5B3 (A5B3_out, A[5], B[3]);
  \平时作业1_全加器子电路  \u_平时作业1_全加器子电路_22  (
    .x(\平时作业1_全加器子电路_16_sum ), .y(A6B3_out), .Cin(\平时作业1_全加器子电路_27_carry ), .Carry(\平时作业1_全加器子电路_22_carry ),
    .sum(\平时作业1_全加器子电路_22_sum ));
  and A4B4 (A4B4_out, A[4], B[4]);
  and A3B5 (A3B5_out, A[3], B[5]);
  \平时作业1_全加器子电路  \u_平时作业1_全加器子电路_23  (
    .x(\平时作业1_全加器子电路_28_sum ), .y(A3B5_out), .Cin(\平时作业1_全加器子电路_29_carry ), .Carry(\平时作业1_全加器子电路_23_carry ),
    .sum(\平时作业1_全加器子电路_23_sum ));
  and A2B6_2 (A2B6_2_out, A[2], B[6]);
  \平时作业1_全加器子电路  \u_平时作业1_全加器子电路_24  (
    .x(\平时作业1_全加器子电路_23_sum ), .y(A2B6_2_out), .Cin(\平时作业1_全加器子电路_30_carry ),
    .Carry(\平时作业1_全加器子电路_24_carry ), .sum(\平时作业1_全加器子电路_24_sum ));
  and A1B6 (A1B6_out, A[1], B[7]);
  \平时作业1_全加器子电路  \u_平时作业1_全加器子电路_25  (
    .x(\平时作业1_全加器子电路_24_sum ), .y(A1B6_out), .Cin(\平时作业1_全加器子电路_31_carry ), .Carry(\平时作业1_全加器子电路_25_carry ),
    .sum(\结果 [8]));
  // Probe on \结果 
  and A7B1 (A7B1_out, A[7], B[1]);
  and A6B2 (A6B2_out, B[2], A[6]);
  \平时作业1_全加器子电路  \u_平时作业1_全加器子电路_26  (
    .x(\平时作业1_全加器子电路_15_sum ), .y(A6B2_out), .Cin(\平时作业1_全加器子电路_33_carry ), .Carry(\平时作业1_全加器子电路_26_carry ),
    .sum(\平时作业1_全加器子电路_26_sum ));
  \平时作业1_全加器子电路  \u_平时作业1_全加器子电路_27  (
    .x(\平时作业1_全加器子电路_26_sum ), .y(A5B3_out), .Cin(\平时作业1_全加器子电路_34_carry ), .Carry(\平时作业1_全加器子电路_27_carry ),
    .sum(\平时作业1_全加器子电路_27_sum ));
  and A3B4 (A3B4_out, A[3], B[4]);
  \平时作业1_全加器子电路  \u_平时作业1_全加器子电路_28  (
    .x(\平时作业1_全加器子电路_27_sum ), .y(A4B4_out), .Cin(\平时作业1_全加器子电路_35_carry ), .Carry(\平时作业1_全加器子电路_28_carry ),
    .sum(\平时作业1_全加器子电路_28_sum ));
  and A2B5 (A2B5_out, A[2], B[5]);
  \平时作业1_全加器子电路  \u_平时作业1_全加器子电路_29  (
    .x(\平时作业1_全加器子电路_35_sum ), .y(A2B5_out), .Cin(\平时作业1_全加器子电路_36_carry ), .Carry(\平时作业1_全加器子电路_29_carry ),
    .sum(\平时作业1_全加器子电路_29_sum ));
  and A1B6_2 (A1B6_2_out, A[1], B[6]);
  \平时作业1_全加器子电路  \u_平时作业1_全加器子电路_30  (
    .x(\平时作业1_全加器子电路_29_sum ), .y(A1B6_2_out), .Cin(\平时作业1_全加器子电路_37_carry ),
    .Carry(\平时作业1_全加器子电路_30_carry ), .sum(\平时作业1_全加器子电路_30_sum ));
  and A0B6 (A0B6_out, A[0], B[7]);
  \平时作业1_全加器子电路  \u_平时作业1_全加器子电路_31  (
    .x(\平时作业1_全加器子电路_30_sum ), .y(A0B6_out), .Cin(in_8), .Carry(\平时作业1_全加器子电路_31_carry ), .sum(\结果 [7]));
  and A6B1 (A6B1_out, A[6], B[1]);
  \平时作业1_全加器子电路  \u_平时作业1_全加器子电路_32  (
    .x(A7B0_out), .y(A6B1_out), .Cin(\平时作业1_全加器子电路_38_carry ), .Carry(\平时作业1_全加器子电路_32_carry ),
    .sum(\平时作业1_全加器子电路_32_sum ));
  and A5B2 (A5B2_out, B[2], A[5]);
  \平时作业1_全加器子电路  \u_平时作业1_全加器子电路_33  (
    .x(\平时作业1_全加器子电路_32_sum ), .y(A5B2_out), .Cin(\平时作业1_全加器子电路_39_carry ), .Carry(\平时作业1_全加器子电路_33_carry ),
    .sum(\平时作业1_全加器子电路_33_sum ));
  and A3B3 (A3B3_out, A[3], B[3]);
  and A4B3 (A4B3_out, A[4], B[3]);
  \平时作业1_全加器子电路  \u_平时作业1_全加器子电路_34  (
    .x(\平时作业1_全加器子电路_33_sum ), .y(A4B3_out), .Cin(\平时作业1_全加器子电路_40_carry ), .Carry(\平时作业1_全加器子电路_34_carry ),
    .sum(\平时作业1_全加器子电路_34_sum ));
  and A2B4 (A2B4_out, A[2], B[4]);
  \平时作业1_全加器子电路  \u_平时作业1_全加器子电路_35  (
    .x(\平时作业1_全加器子电路_34_sum ), .y(A3B4_out), .Cin(\平时作业1_全加器子电路_41_carry ), .Carry(\平时作业1_全加器子电路_35_carry ),
    .sum(\平时作业1_全加器子电路_35_sum ));
  and A1B5 (A1B5_out, A[1], B[5]);
  \平时作业1_全加器子电路  \u_平时作业1_全加器子电路_36  (
    .x(\平时作业1_全加器子电路_41_sum ), .y(A1B5_out), .Cin(\平时作业1_全加器子电路_42_carry ), .Carry(\平时作业1_全加器子电路_36_carry ),
    .sum(\平时作业1_全加器子电路_36_sum ));
  and A0B6_2 (A0B6_2_out, A[0], B[6]);
  \平时作业1_全加器子电路  \u_平时作业1_全加器子电路_37  (
    .x(\平时作业1_全加器子电路_36_sum ), .y(A0B6_2_out), .Cin(in_7), .Carry(\平时作业1_全加器子电路_37_carry ), .sum(\结果 [6]));
  and A7B0 (A7B0_out, A[7], B[0]);
  and A6B0 (A6B0_out, A[6], B[0]);
  and A5B1 (A5B1_out, B[1], A[5]);
  \平时作业1_全加器子电路  \u_平时作业1_全加器子电路_38  (
    .x(A6B0_out), .y(A5B1_out), .Cin(\平时作业1_全加器子电路_43_carry ), .Carry(\平时作业1_全加器子电路_38_carry ),
    .sum(\平时作业1_全加器子电路_38_sum ));
  and A4B2 (A4B2_out, B[2], A[4]);
  \平时作业1_全加器子电路  \u_平时作业1_全加器子电路_39  (
    .x(\平时作业1_全加器子电路_38_sum ), .y(A4B2_out), .Cin(\平时作业1_全加器子电路_44_carry ), .Carry(\平时作业1_全加器子电路_39_carry ),
    .sum(\平时作业1_全加器子电路_39_sum ));
  and A2B3 (A2B3_out, A[2], B[3]);
  \平时作业1_全加器子电路  \u_平时作业1_全加器子电路_40  (
    .x(\平时作业1_全加器子电路_39_sum ), .y(A3B3_out), .Cin(\平时作业1_全加器子电路_45_carry ), .Carry(\平时作业1_全加器子电路_40_carry ),
    .sum(\平时作业1_全加器子电路_40_sum ));
  and A1B4 (A1B4_out, A[1], B[4]);
  \平时作业1_全加器子电路  \u_平时作业1_全加器子电路_41  (
    .x(\平时作业1_全加器子电路_40_sum ), .y(A2B4_out), .Cin(\平时作业1_全加器子电路_46_carry ), .Carry(\平时作业1_全加器子电路_41_carry ),
    .sum(\平时作业1_全加器子电路_41_sum ));
  and A0B5 (A0B5_out, A[0], B[5]);
  \平时作业1_全加器子电路  \u_平时作业1_全加器子电路_42  (
    .x(\平时作业1_全加器子电路_46_sum ), .y(A0B5_out), .Cin(in_6), .Carry(\平时作业1_全加器子电路_42_carry ), .sum(\结果 [5]));
  and A5B0 (A5B0_out, A[5], B[0]);
  and A4B1 (A4B1_out, B[1], A[4]);
  \平时作业1_全加器子电路  \u_平时作业1_全加器子电路_43  (
    .x(A5B0_out), .y(A4B1_out), .Cin(\平时作业1_全加器子电路_47_carry ), .Carry(\平时作业1_全加器子电路_43_carry ),
    .sum(\平时作业1_全加器子电路_43_sum ));
  and A3B2 (A3B2_out, A[3], B[2]);
  \平时作业1_全加器子电路  \u_平时作业1_全加器子电路_44  (
    .x(\平时作业1_全加器子电路_43_sum ), .y(A3B2_out), .Cin(\平时作业1_全加器子电路_48_carry ), .Carry(\平时作业1_全加器子电路_44_carry ),
    .sum(\平时作业1_全加器子电路_44_sum ));
  \平时作业1_全加器子电路  \u_平时作业1_全加器子电路_45  (
    .x(\平时作业1_全加器子电路_44_sum ), .y(A2B3_out), .Cin(\平时作业1_全加器子电路_49_carry ), .Carry(\平时作业1_全加器子电路_45_carry ),
    .sum(\平时作业1_全加器子电路_45_sum ));
  \平时作业1_全加器子电路  \u_平时作业1_全加器子电路_46  (
    .x(\平时作业1_全加器子电路_45_sum ), .y(A1B4_out), .Cin(\平时作业1_全加器子电路_50_carry ), .Carry(\平时作业1_全加器子电路_46_carry ),
    .sum(\平时作业1_全加器子电路_46_sum ));
  and A3B1 (A3B1_out, B[1], A[3]);
  \平时作业1_全加器子电路  \u_平时作业1_全加器子电路_47  (
    .x(A4B0_out), .y(A3B1_out), .Cin(\平时作业1_全加器子电路_51_carry ), .Carry(\平时作业1_全加器子电路_47_carry ),
    .sum(\平时作业1_全加器子电路_47_sum ));
  and A2B2 (A2B2_out, A[2], B[2]);
  \平时作业1_全加器子电路  \u_平时作业1_全加器子电路_48  (
    .x(\平时作业1_全加器子电路_47_sum ), .y(A2B2_out), .Cin(\平时作业1_全加器子电路_52_carry ), .Carry(\平时作业1_全加器子电路_48_carry ),
    .sum(\平时作业1_全加器子电路_48_sum ));
  and A1B3 (A1B3_out, A[1], B[3]);
  \平时作业1_全加器子电路  \u_平时作业1_全加器子电路_49  (
    .x(\平时作业1_全加器子电路_48_sum ), .y(A1B3_out), .Cin(\平时作业1_全加器子电路_53_carry ), .Carry(\平时作业1_全加器子电路_49_carry ),
    .sum(\平时作业1_全加器子电路_49_sum ));
  and A0B4 (A0B4_out, A[0], B[4]);
  \平时作业1_全加器子电路  \u_平时作业1_全加器子电路_50  (
    .x(\平时作业1_全加器子电路_49_sum ), .y(A0B4_out), .Cin(in_5), .Carry(\平时作业1_全加器子电路_50_carry ), .sum(\结果 [4]));
  and A2B1 (A2B1_out, B[1], A[2]);
  and A4B0 (A4B0_out, A[4], B[0]);
  \平时作业1_全加器子电路  \u_平时作业1_全加器子电路_51  (
    .x(A3B0_out), .y(A2B1_out), .Cin(\平时作业1_全加器子电路_55_carry ), .Carry(\平时作业1_全加器子电路_51_carry ),
    .sum(\平时作业1_全加器子电路_51_sum ));
  and A1B2 (A1B2_out, A[1], B[2]);
  \平时作业1_全加器子电路  \u_平时作业1_全加器子电路_52  (
    .x(\平时作业1_全加器子电路_51_sum ), .y(A1B2_out), .Cin(\平时作业1_全加器子电路_54_carry ), .Carry(\平时作业1_全加器子电路_52_carry ),
    .sum(\平时作业1_全加器子电路_52_sum ));
  and A0B3 (A0B3_out, A[0], B[3]);
  \平时作业1_全加器子电路  \u_平时作业1_全加器子电路_53  (
    .x(\平时作业1_全加器子电路_52_sum ), .y(A0B3_out), .Cin(in_4), .Carry(\平时作业1_全加器子电路_53_carry ), .sum(\结果 [3]));
  and A1B1 (A1B1_out, B[1], A[1]);
  and A3B0 (A3B0_out, A[3], B[0]);
  and A0B2 (A0B2_out, B[2], A[0]);
  \平时作业1_全加器子电路  \u_平时作业1_全加器子电路_54  (
    .x(\平时作业1_全加器子电路_55_sum ), .y(A0B2_out), .Cin(in_3), .Carry(\平时作业1_全加器子电路_54_carry ), .sum(\结果 [2]));
  and A2B0 (A2B0_out, B[0], A[2]);
  \平时作业1_全加器子电路  \u_平时作业1_全加器子电路_55  (
    .x(A2B0_out), .y(A1B1_out), .Cin(\平时作业1_全加器子电路_56_carry ), .Carry(\平时作业1_全加器子电路_55_carry ),
    .sum(\平时作业1_全加器子电路_55_sum ));
  and A0B1 (A0B1_out, B[1], A[0]);
  and A1B0 (A1B0_out, B[0], A[1]);
  \平时作业1_全加器子电路  \u_平时作业1_全加器子电路_56  (
    .x(A1B0_out), .y(A0B1_out), .Cin(in_2), .Carry(\平时作业1_全加器子电路_56_carry ), .sum(\结果 [1]));
  and A0B0 (\结果 [0], B[0], A[0]);

  // Notes on the sheet:
  //   X
  //   =
endmodule

module \实验2_乘法控制器_Moore型状态机  (
  input  Start,
  input  B,
  input  B0,
  input  CLK,
  input  Reset,
  output Enable,
  output LoadA,
  output LoadB,
  output Done,
  output ShiftA,
  output ShiftB
);

  wire and_1_out, and_2_out, and_3_out, and_5_out, and_6_out, and_10_out, and_11_out, and_12_out, and_13_out;
  wire [2:0] or_1_out, register_1_q;

  and and_1 (and_1_out, ~register_1_q[2], ~register_1_q[1], register_1_q[0], Start, B, B0);  // AND_Gate
  and and_2 (and_2_out, ~register_1_q[2], register_1_q[1]);  // AND_Gate
  and and_3 (and_3_out, ~register_1_q[2], ~register_1_q[1], ~register_1_q[0], Start);  // AND_Gate
  and and_4 (or_1_out[1], ~register_1_q[2], ~register_1_q[1], register_1_q[0], Start, B);  // AND_Gate
  and and_5 (and_5_out, ~register_1_q[2], ~register_1_q[1], register_1_q[0], Start, ~B);  // AND_Gate
  and and_6 (and_6_out, register_1_q[2], ~register_1_q[1], ~register_1_q[0]);  // AND_Gate
  or or_1 (or_1_out[0], and_1_out, and_2_out, and_3_out);
  or or_2 (or_1_out[2], and_5_out, and_6_out);
  Register #(.width(3), .trigger("rising"), .Select("low")) register_1 (
    .D(or_1_out), .Q(register_1_q), .clk(CLK), .clr(Reset));  // open: en
  and and_7 (ShiftA, ~register_1_q[2], register_1_q[1]);  // AND_Gate
  and and_8 (ShiftB, ~register_1_q[2], register_1_q[1]);  // AND_Gate
  and and_9 (Enable, ~register_1_q[2], register_1_q[1], register_1_q[0]);  // AND_Gate
  and and_10 (and_10_out, ~register_1_q[2], ~register_1_q[1], ~register_1_q[0]);  // AND_Gate
  and and_11 (and_11_out, register_1_q[1], ~register_1_q[2]);  // AND_Gate
  and and_12 (and_12_out, ~register_1_q[2], ~register_1_q[1], ~register_1_q[0]);  // AND_Gate
  and and_13 (and_13_out, register_1_q[1], ~register_1_q[2]);  // AND_Gate
  and and_14 (Done, register_1_q[2], ~register_1_q[1], ~register_1_q[0]);  // AND_Gate
  or or_3 (LoadA, and_10_out, and_11_out);
  or or_4 (LoadB, and_12_out, and_13_out);
endmodule

module \实验2_单精度定点乘法器  (
  input  [7:0] A,
  input  [7:0] B,
  input  in_3,
  output [15:0] C
);

  wire bitselector_1_out, bitselector_2_out, bitselector_3_out, CLK, clock_1_out, comparator_1_eq, Done,
       not_1_out, Reset, xor_1_out, \实验2_乘法控制器_moore型状态机_1_enable , \实验2_乘法控制器_moore型状态机_1_loada ,
       \实验2_乘法控制器_moore型状态机_1_loadb , \实验2_乘法控制器_moore型状态机_1_shifta , \实验2_乘法控制器_moore型状态机_1_shiftb ;
  wire [7:0] multiplexer_1_out, multiplexer_4_out, multiplexer_5_out, negator_1_out, negator_2_out,
       register_3_q, shifter_2_out;
  wire [15:0] adder_1_out, bit_extender_1_out, multiplexer_2_out, multiplexer_3_out, negator_3_out,
       register_1_q, register_2_q, shifter_1_out;

  Negator #(.width(8)) negator_1 (.in(A), .out(negator_1_out));
  BitSelector #(.width(8), .group(1)) bitselector_1 (.in(A), .out(bitselector_1_out), .sel(3'b111));
  Multiplexer #(.select(1), .width(8), .disabled("Z"), .enable("false")) multiplexer_1 (
    .in0(A), .in1(negator_1_out), .out(multiplexer_1_out), .sel(bitselector_1_out));
  LED #(.active("true")) led_1 (.in(Done));
  assign bit_extender_1_out = {{8{1'b0}}, multiplexer_1_out};  // Bit_Extender bit_extender_1
  Multiplexer #(.select(1), .width(16), .disabled("Z"), .enable("false")) multiplexer_2 (
    .in0(bit_extender_1_out), .in1(shifter_1_out), .out(multiplexer_2_out),
    .sel(\实验2_乘法控制器_moore型状态机_1_shifta ));
  xor xor_1 (xor_1_out, bitselector_2_out, bitselector_1_out);
  // Probe on A
  Negator #(.width(8)) negator_2 (.in(B), .out(negator_2_out));
  BitSelector #(.width(8), .group(1)) bitselector_2 (.in(B), .out(bitselector_2_out), .sel(3'b111));
  Register #(.width(16), .trigger("rising"), .Select("low")) register_1 (
    .D(multiplexer_2_out), .en(\实验2_乘法控制器_moore型状态机_1_loada ), .Q(register_1_q), .clk(CLK), .clr(Reset));
  Multiplexer #(.select(1), .width(16), .disabled("Z"), .enable("false")) multiplexer_3 (
    .in1(register_2_q), .out(multiplexer_3_out), .sel(Done));  // open: in0
  // Probe on B
  Multiplexer #(.select(1), .width(8), .disabled("Z"), .enable("false")) multiplexer_4 (
    .in0(B), .in1(negator_2_out), .out(multiplexer_4_out), .sel(bitselector_2_out));
  Shifter #(.width(16), .shift("ll")) shifter_1 (.in(register_1_q), .\dist (4'b0001), .out(shifter_1_out));
  Adder #(.width(16)) adder_1 (.a(register_2_q), .b(register_1_q), .out(adder_1_out));  // open: cin, cout
  Register #(.width(16), .trigger("rising"), .Select("low")) register_2 (
    .D(adder_1_out), .en(\实验2_乘法控制器_moore型状态机_1_enable ), .Q(register_2_q), .clk(CLK), .clr(Reset));
  // Probe on C
  Multiplexer #(.select(1), .width(8), .disabled("Z"), .enable("false")) multiplexer_5 (
    .in0(multiplexer_4_out), .in1(shifter_2_out), .out(multiplexer_5_out),
    .sel(\实验2_乘法控制器_moore型状态机_1_shiftb ));
  Register #(.width(8), .trigger("rising"), .Select("low")) register_3 (
    .D(multiplexer_5_out), .en(\实验2_乘法控制器_moore型状态机_1_loadb ), .Q(register_3_q), .clk(CLK), .clr(Reset));
  Negator #(.width(16)) negator_3 (.in(multiplexer_3_out), .out(negator_3_out));
  Shifter #(.width(8), .shift("lr")) shifter_2 (.in(register_3_q), .\dist (3'b001), .out(shifter_2_out));
  Comparator #(.width(8), .mode("twosComplement")) comparator_1 (
    .a(register_3_q), .b({8{1'b0}}), .eq(comparator_1_eq));  // open: gt, lt
  Multiplexer #(.select(1), .width(16), .disabled("Z"), .enable("false")) multiplexer_6 (
    .in0(multiplexer_3_out), .in1(negator_3_out), .out(C), .sel(xor_1_out));
  BitSelector #(.width(8), .group(1)) bitselector_3 (.in(register_3_q), .out(bitselector_3_out), .sel(3'b000));
  not not_1 (not_1_out, comparator_1_eq);
  \实验2_乘法控制器_Moore型状态机  \u_实验2_乘法控制器_moore型状态机_1  (
    .Start(in_3), .B(not_1_out), .B0(bitselector_3_out), .CLK(CLK), .Reset(Reset),
    .Enable(\实验2_乘法控制器_moore型状态机_1_enable ), .LoadA(\实验2_乘法控制器_moore型状态机_1_loada ),
    .LoadB(\实验2_乘法控制器_moore型状态机_1_loadb ), .Done(Done), .ShiftA(\实验2_乘法控制器_moore型状态机_1_shifta ),
    .ShiftB(\实验2_乘法控制器_moore型状态机_1_shiftb ));
  Clock #(.highDuration(1), .lowDuration(1)) clock_1 (.out(clock_1_out));
  and and_1 (CLK, clock_1_out, in_3);
  Button button_1 (.out(Reset));

  // Other names for the same wires on the sheet: Start = in_3

  // Notes on the sheet:
  //   显示区
  //   X
  //   =
endmodule

module \实验2_快速乘法器  (
  input  [7:0] in_1,
  input  [7:0] in_2,
  output [15:0] out_3
);

  wire bitselector_1_out, bitselector_2_out, CLK, Restart, Start, xor_1_out;
  wire [1:0] bitselector_3_out;
  wire [7:0] counter_1_q, multiplexer_1_out, multiplexer_2_out, negator_1_out, negator_2_out;
  wire [15:0] adder_1_out, adder_2_out, bit_extender_1_out, bit_extender_2_out, multiplexer_3_out,
       multiplexer_4_out, multiplexer_5_out, negator_3_out, register_1_q, register_2_q, register_3_q,
       shifter_1_out, shifter_2_out, shifter_3_out;

  Negator #(.width(8)) negator_1 (.in(in_1), .out(negator_1_out));
  BitSelector #(.width(8), .group(1)) bitselector_1 (.in(in_1), .out(bitselector_1_out), .sel(3'b111));
  Negator #(.width(8)) negator_2 (.in(in_2), .out(negator_2_out));
  Multiplexer #(.select(1), .width(8), .disabled("Z"), .enable("false")) multiplexer_1 (
    .in0(in_1), .in1(negator_1_out), .out(multiplexer_1_out), .sel(bitselector_1_out));
  Multiplexer #(.select(1), .width(8), .disabled("Z"), .enable("false")) multiplexer_2 (
    .in0(in_2), .in1(negator_2_out), .out(multiplexer_2_out), .sel(bitselector_2_out));
  BitSelector #(.width(8), .group(1)) bitselector_2 (.in(in_2), .out(bitselector_2_out), .sel(3'b111));
  assign bit_extender_1_out = {{8{1'b0}}, multiplexer_1_out};  // Bit_Extender bit_extender_1
  Multiplexer #(.select(1), .width(16), .disabled("Z"), .enable("false")) multiplexer_3 (
    .in0(bit_extender_1_out), .in1(shifter_1_out), .out(multiplexer_3_out), .sel(Start));
  Register #(.width(16), .trigger("rising"), .Select("low")) register_1 (
    .D(multiplexer_3_out), .Q(register_1_q), .clk(CLK), .clr(Restart));  // open: en
  assign bit_extender_2_out = {{8{1'b0}}, multiplexer_2_out};  // Bit_Extender bit_extender_2
  Multiplexer #(.select(1), .width(16), .disabled("Z"), .enable("false")) multiplexer_4 (
    .in0(bit_extender_2_out), .in1(shifter_3_out), .out(multiplexer_4_out), .sel(Start));
  Shifter #(.width(16), .shift("ll")) shifter_1 (.in(register_1_q), .\dist (4'b0010), .out(shifter_1_out));
  Register #(.width(16), .trigger("rising"), .Select("low")) register_2 (
    .D(multiplexer_4_out), .Q(register_2_q), .clk(CLK), .clr(Restart));  // open: en
  // Probe on in_2
  // Probe on in_1
  Shifter #(.width(16), .shift("ll")) shifter_2 (.in(register_1_q), .\dist (4'b0001), .out(shifter_2_out));
  Adder #(.width(16)) adder_1 (.a(shifter_2_out), .b(register_1_q), .out(adder_1_out));  // open: cin, cout
  BitSelector #(.width(16), .group(2)) bitselector_3 (.in(register_2_q), .out(bitselector_3_out), .sel(3'b000));
  Shifter #(.width(16), .shift("lr")) shifter_3 (.in(register_2_q), .\dist (4'b0010), .out(shifter_3_out));
  // Probe on out_3
  Multiplexer #(.select(2), .width(16), .disabled("Z"), .enable("false")) multiplexer_5 (
    .in0({16{1'b0}}), .in1(register_1_q), .in2(shifter_2_out), .in3(adder_1_out), .out(multiplexer_5_out),
    .sel(bitselector_3_out));
  xor xor_1 (xor_1_out, bitselector_1_out, bitselector_2_out);
  Clock #(.highDuration(1), .lowDuration(1)) clock_1 (.out(CLK));
  Button button_1 (.out(Restart));
  Counter #(.width(8), .max('hff), .ongoal("wrap"), .trigger("rising"), .behavior("new")) counter_1 (
    .Q(counter_1_q), .clk(CLK), .clr(Restart));  // open: load, D, count, carry, preset, down
  Adder #(.width(16)) adder_2 (.a(multiplexer_5_out), .b(register_3_q), .out(adder_2_out));  // open: cin, cout
  Comparator #(.width(8), .mode("twosComplement")) comparator_1 (
    .a(counter_1_q), .b({8{1'b0}}), .gt(Start));  // open: eq, lt
  Register #(.width(16), .trigger("rising"), .Select("low")) register_3 (
    .D(adder_2_out), .Q(register_3_q), .clk(CLK), .clr(Restart));  // open: en
  Multiplexer #(.select(1), .width(16), .disabled("Z"), .enable("false")) multiplexer_6 (
    .in0(register_3_q), .in1(negator_3_out), .out(out_3), .sel(xor_1_out));
  Negator #(.width(16)) negator_3 (.in(register_3_q), .out(negator_3_out));

  // Notes on the sheet:
  //   被乘数B
  //   乘数C
  //   显示区
  //   x
  //   2B
  //   =
  //   至多5次时钟上升沿就可以计算出结果
endmodule

// ALU
module \实验3_算术逻辑运算单元ALU  (
  input  [31:0] X,
  input  [31:0] Y,
  input  [2:0] AluOP,
  output \结果是否为0 ,
  output [31:0] Result
);

  wire comparator_1_lt;
  wire [24:0] \运算指示 ;
  wire [31:0] adder_3_out, AND, AND_prime, not_1_out, not_2_out, OR, OR_prime, SLT, tunnel, tunnel_t;

  // Probe on X
  // Probe on X
  // Probe on Y
  // Probe on Y
  assign AND = X & Y;  // AND_Gate and_1, 32 bits wide
  assign OR = X | Y;  // OR_Gate or_1, 32 bits wide
  Adder #(.width(32)) adder_1 (.a(X), .b(Y), .out(tunnel));  // open: cin, cout
  assign AND_prime = X & ~Y;  // AND_Gate and_2, 32 bits wide
  assign not_1_out = ~Y;  // NOT_Gate not_1, 32 bits wide
  assign not_2_out = ~Y;  // NOT_Gate not_2, 32 bits wide
  // Probe on AluOP
  assign OR_prime = X | ~Y;  // OR_Gate or_2, 32 bits wide
  Adder #(.width(32)) adder_2 (.a(X), .b(not_1_out), .out(tunnel_t), .cin(1'b1));  // open: cout
  Adder #(.width(32)) adder_3 (.a(X), .b(not_2_out), .out(adder_3_out), .cin(1'b1));  // open: cout
  // Probe on Result
  // Probe on Result
  Comparator #(.width(32), .mode("twosComplement")) comparator_1 (
    .a(adder_3_out), .b({32{1'b0}}), .lt(comparator_1_lt));  // open: gt, eq
  DotMatrix #(.inputtype("column"), .matrixcols(5), .matrixrows(5), .persist(0), .dotshape("square")) dotmatrix_1 (
    .col0(\运算指示 [24:20]), .col1(\运算指示 [19:15]), .col2(\运算指示 [14:10]), .col3(\运算指示 [9:5]), .col4(\运算指示 [4:0]));
  assign SLT = {{31{1'b0}}, comparator_1_lt};  // Bit_Extender bit_extender_1
  Multiplexer #(.select(3), .width(32), .disabled("Z"), .enable("false")) multiplexer_1 (
    .in0(AND), .in1(OR), .in2(tunnel), .in3(32'h1), .in4(AND_prime), .in5(OR_prime), .in6(tunnel_t),
    .in7(SLT), .out(Result), .sel(AluOP));
  Comparator #(.width(32), .mode("twosComplement")) comparator_2 (
    .a(Result), .b({32{1'b0}}), .eq(\结果是否为0 ));  // open: gt, lt
  Multiplexer #(.select(3), .width(25), .disabled("Z"), .enable("false")) multiplexer_2 (
    .in0(25'h124081), .in1(25'h1020490), .in2(25'h427c84), .in3({25{1'b0}}), .in4(25'h124091),
    .in5(25'h1020490), .in6(25'h421084), .in7(25'h402811), .out(\运算指示 ), .sel(AluOP));

  // Other names for the same wires on the sheet: S[2:0] = AluOP; Zero = \结果是否为0 

  // Notes on the sheet:
  //   AluOP: pull=down
  //   Y: pull=down
  //   X: pull=down
  //   不要改变此引脚区域内容，也不要改变ALU封装形式
  //   请在下方利用上方输入输出引脚的隧道信号构建ALU电路，ctrl+d复制选择部件
  //   输入引脚
  //   探测区域
  //   输出引脚
  //   功能说明：
  //   000：X AND Y      100：X AND Y'
  //   001：X OR Y        101：X OR Y'  
  //   010：X + Y           110：X - Y  
  //   011：未使用         111：SLT  
endmodule

module \实验3_32位地址总线32位数据总线RAM存储器  (
  input  CS,
  input  Store,
  input  CLK,
  input  [31:0] Address_Bus,
  input  [31:0] Data_Bus_In,
  input  Load,
  input  Clear,
  output [31:0] Data_Bus_Out
);

  wire decoder_1_out0, decoder_1_out1, decoder_1_out2, decoder_1_out3, decoder_1_out4, decoder_1_out5,
       decoder_1_out6, decoder_1_out7, decoder_2_out0, decoder_2_out1, decoder_2_out2, decoder_2_out3,
       decoder_2_out4, decoder_2_out5, decoder_2_out6, decoder_2_out7, nand_1_out, nand_2_out, nand_3_out,
       nand_4_out, nand_5_out, nand_6_out, nand_7_out, nand_8_out, nand_9_out, nand_10_out, nand_11_out,
       nand_12_out, nand_13_out, nand_14_out, nand_15_out, nand_16_out, nand_17_out, nand_18_out,
       nand_19_out, nand_20_out, nand_21_out, nand_22_out, nand_23_out, nand_24_out, nand_25_out,
       nand_26_out, nand_27_out, nand_28_out, nand_29_out, nand_30_out, nand_31_out, nand_32_out,
       nand_33_out, nand_34_out, nand_35_out, nand_36_out, nand_37_out, nand_38_out, nand_39_out,
       nand_40_out, nand_41_out, nand_42_out, nand_43_out, nand_44_out, nand_45_out, nand_46_out,
       nand_47_out, nand_48_out, nand_49_out, nand_50_out, nand_51_out, nand_52_out, nand_53_out,
       nand_54_out, nand_55_out, nand_56_out, nand_57_out, nand_58_out, nand_59_out, nand_60_out,
       nand_61_out, nand_62_out, nand_63_out, nand_64_out;

  Decoder #(.select(3), .tristate("false"), .disabled("Z"), .enable("true")) decoder_1 (
    .out0(decoder_1_out0), .out1(decoder_1_out1), .out2(decoder_1_out2), .out3(decoder_1_out3),
    .out4(decoder_1_out4), .out5(decoder_1_out5), .out6(decoder_1_out6), .out7(decoder_1_out7),
    .sel(Address_Bus[31:29]), .en(CS));
  Decoder #(.select(3), .tristate("false"), .disabled("Z"), .enable("true")) decoder_2 (
    .out0(decoder_2_out0), .out1(decoder_2_out1), .out2(decoder_2_out2), .out3(decoder_2_out3),
    .out4(decoder_2_out4), .out5(decoder_2_out5), .out6(decoder_2_out6), .out7(decoder_2_out7),
    .sel(Address_Bus[28:26]), .en(CS));
  nand nand_1 (nand_1_out, decoder_2_out0, decoder_1_out0);
  nand nand_2 (nand_2_out, decoder_2_out0, decoder_1_out1);
  nand nand_3 (nand_3_out, decoder_2_out0, decoder_1_out2);
  nand nand_4 (nand_4_out, decoder_2_out0, decoder_1_out3);
  nand nand_5 (nand_5_out, decoder_2_out0, decoder_1_out4);
  nand nand_6 (nand_6_out, decoder_2_out0, decoder_1_out5);
  nand nand_7 (nand_7_out, decoder_2_out0, decoder_1_out6);
  nand nand_8 (nand_8_out, decoder_2_out0, decoder_1_out7);
  RAM #(.addrWidth(24), .dataWidth(32), .bus("separate"), .Select("low")) ram_1 (
    .addr(Address_Bus[25:2]), .din(Data_Bus_In), .data(Data_Bus_Out), .str(Store), .sel(nand_1_out),
    .clk(CLK), .ld(Load), .clr(Clear));
  RAM #(.addrWidth(24), .dataWidth(32), .bus("separate"), .Select("low")) ram_2 (
    .addr(Address_Bus[25:2]), .din(Data_Bus_In), .data(Data_Bus_Out), .str(Store), .sel(nand_2_out),
    .clk(CLK), .ld(Load), .clr(Clear));
  RAM #(.addrWidth(24), .dataWidth(32), .bus("separate"), .Select("low")) ram_3 (
    .addr(Address_Bus[25:2]), .din(Data_Bus_In), .data(Data_Bus_Out), .str(Store), .sel(nand_3_out),
    .clk(CLK), .ld(Load), .clr(Clear));
  RAM #(.addrWidth(24), .dataWidth(32), .bus("separate"), .Select("low")) ram_4 (
    .addr(Address_Bus[25:2]), .din(Data_Bus_In), .data(Data_Bus_Out), .str(Store), .sel(nand_4_out),
    .clk(CLK), .ld(Load), .clr(Clear));
  RAM #(.addrWidth(24), .dataWidth(32), .bus("separate"), .Select("low")) ram_5 (
    .addr(Address_Bus[25:2]), .din(Data_Bus_In), .data(Data_Bus_Out), .str(Store), .sel(nand_5_out),
    .clk(CLK), .ld(Load), .clr(Clear));
  RAM #(.addrWidth(24), .dataWidth(32), .bus("separate"), .Select("low")) ram_6 (
    .addr(Address_Bus[25:2]), .din(Data_Bus_In), .data(Data_Bus_Out), .str(Store), .sel(nand_6_out),
    .clk(CLK), .ld(Load), .clr(Clear));
  RAM #(.addrWidth(24), .dataWidth(32), .bus("separate"), .Select("low")) ram_7 (
    .addr(Address_Bus[25:2]), .din(Data_Bus_In), .data(Data_Bus_Out), .str(Store), .sel(nand_7_out),
    .clk(CLK), .ld(Load), .clr(Clear));
  RAM #(.addrWidth(24), .dataWidth(32), .bus("separate"), .Select("low")) ram_8 (
    .addr(Address_Bus[25:2]), .din(Data_Bus_In), .data(Data_Bus_Out), .str(Store), .sel(nand_8_out),
    .clk(CLK), .ld(Load), .clr(Clear));
  nand nand_9 (nand_9_out, decoder_2_out1, decoder_1_out0);
  nand nand_10 (nand_10_out, decoder_2_out1, decoder_1_out1);
  nand nand_11 (nand_11_out, decoder_2_out1, decoder_1_out2);
  nand nand_12 (nand_12_out, decoder_2_out1, decoder_1_out3);
  nand nand_13 (nand_13_out, decoder_2_out1, decoder_1_out4);
  nand nand_14 (nand_14_out, decoder_2_out1, decoder_1_out5);
  nand nand_15 (nand_15_out, decoder_2_out1, decoder_1_out6);
  nand nand_16 (nand_16_out, decoder_2_out1, decoder_1_out7);
  RAM #(.addrWidth(24), .dataWidth(32), .bus("separate"), .Select("low")) ram_9 (
    .addr(Address_Bus[25:2]), .din(Data_Bus_In), .data(Data_Bus_Out), .str(Store), .sel(nand_9_out),
    .clk(CLK), .ld(Load), .clr(Clear));
  RAM #(.addrWidth(24), .dataWidth(32), .bus("separate"), .Select("low")) ram_10 (
    .addr(Address_Bus[25:2]), .din(Data_Bus_In), .data(Data_Bus_Out), .str(Store), .sel(nand_10_out),
    .clk(CLK), .ld(Load), .clr(Clear));
  RAM #(.addrWidth(24), .dataWidth(32), .bus("separate"), .Select("low")) ram_11 (
    .addr(Address_Bus[25:2]), .din(Data_Bus_In), .data(Data_Bus_Out), .str(Store), .sel(nand_11_out),
    .clk(CLK), .ld(Load), .clr(Clear));
  RAM #(.addrWidth(24), .dataWidth(32), .bus("separate"), .Select("low")) ram_12 (
    .addr(Address_Bus[25:2]), .din(Data_Bus_In), .data(Data_Bus_Out), .str(Store), .sel(nand_12_out),
    .clk(CLK), .ld(Load), .clr(Clear));
  RAM #(.addrWidth(24), .dataWidth(32), .bus("separate"), .Select("low")) ram_13 (
    .addr(Address_Bus[25:2]), .din(Data_Bus_In), .data(Data_Bus_Out), .str(Store), .sel(nand_13_out),
    .clk(CLK), .ld(Load), .clr(Clear));
  RAM #(.addrWidth(24), .dataWidth(32), .bus("separate"), .Select("low")) ram_14 (
    .addr(Address_Bus[25:2]), .din(Data_Bus_In), .data(Data_Bus_Out), .str(Store), .sel(nand_14_out),
    .clk(CLK), .ld(Load), .clr(Clear));
  RAM #(.addrWidth(24), .dataWidth(32), .bus("separate"), .Select("low")) ram_15 (
    .addr(Address_Bus[25:2]), .din(Data_Bus_In), .data(Data_Bus_Out), .str(Store), .sel(nand_15_out),
    .clk(CLK), .ld(Load), .clr(Clear));
  RAM #(.addrWidth(24), .dataWidth(32), .bus("separate"), .Select("low")) ram_16 (
    .addr(Address_Bus[25:2]), .din(Data_Bus_In), .data(Data_Bus_Out), .str(Store), .sel(nand_16_out),
    .clk(CLK), .ld(Load), .clr(Clear));
  nand nand_17 (nand_17_out, decoder_2_out2, decoder_1_out0);
  nand nand_18 (nand_18_out, decoder_2_out2, decoder_1_out1);
  nand nand_19 (nand_19_out, decoder_2_out2, decoder_1_out2);
  nand nand_20 (nand_20_out, decoder_2_out2, decoder_1_out3);
  nand nand_21 (nand_21_out, decoder_2_out2, decoder_1_out4);
  nand nand_22 (nand_22_out, decoder_2_out2, decoder_1_out5);
  nand nand_23 (nand_23_out, decoder_2_out2, decoder_1_out6);
  nand nand_24 (nand_24_out, decoder_2_out2, decoder_1_out7);
  RAM #(.addrWidth(24), .dataWidth(32), .bus("separate"), .Select("low")) ram_17 (
    .addr(Address_Bus[25:2]), .din(Data_Bus_In), .data(Data_Bus_Out), .str(Store), .sel(nand_17_out),
    .clk(CLK), .ld(Load), .clr(Clear));
  RAM #(.addrWidth(24), .dataWidth(32), .bus("separate"), .Select("low")) ram_18 (
    .addr(Address_Bus[25:2]), .din(Data_Bus_In), .data(Data_Bus_Out), .str(Store), .sel(nand_18_out),
    .clk(CLK), .ld(Load), .clr(Clear));
  RAM #(.addrWidth(24), .dataWidth(32), .bus("separate"), .Select("low")) ram_19 (
    .addr(Address_Bus[25:2]), .din(Data_Bus_In), .data(Data_Bus_Out), .str(Store), .sel(nand_19_out),
    .clk(CLK), .ld(Load), .clr(Clear));
  RAM #(.addrWidth(24), .dataWidth(32), .bus("separate"), .Select("low")) ram_20 (
    .addr(Address_Bus[25:2]), .din(Data_Bus_In), .data(Data_Bus_Out), .str(Store), .sel(nand_20_out),
    .clk(CLK), .ld(Load), .clr(Clear));
  RAM #(.addrWidth(24), .dataWidth(32), .bus("separate"), .Select("low")) ram_21 (
    .addr(Address_Bus[25:2]), .din(Data_Bus_In), .data(Data_Bus_Out), .str(Store), .sel(nand_21_out),
    .clk(CLK), .ld(Load), .clr(Clear));
  RAM #(.addrWidth(24), .dataWidth(32), .bus("separate"), .Select("low")) ram_22 (
    .addr(Address_Bus[25:2]), .din(Data_Bus_In), .data(Data_Bus_Out), .str(Store), .sel(nand_22_out),
    .clk(CLK), .ld(Load), .clr(Clear));
  RAM #(.addrWidth(24), .dataWidth(32), .bus("separate"), .Select("low")) ram_23 (
    .addr(Address_Bus[25:2]), .din(Data_Bus_In), .data(Data_Bus_Out), .str(Store), .sel(nand_23_out),
    .clk(CLK), .ld(Load), .clr(Clear));
  RAM #(.addrWidth(24), .dataWidth(32), .bus("separate"), .Select("low")) ram_24 (
    .addr(Address_Bus[25:2]), .din(Data_Bus_In), .data(Data_Bus_Out), .str(Store), .sel(nand_24_out),
    .clk(CLK), .ld(Load), .clr(Clear));
  nand nand_25 (nand_25_out, decoder_2_out3, decoder_1_out0);
  nand nand_26 (nand_26_out, decoder_2_out3, decoder_1_out1);
  nand nand_27 (nand_27_out, decoder_2_out3, decoder_1_out2);
  nand nand_28 (nand_28_out, decoder_2_out3, decoder_1_out3);
  nand nand_29 (nand_29_out, decoder_2_out3, decoder_1_out4);
  nand nand_30 (nand_30_out, decoder_2_out3, decoder_1_out5);
  nand nand_31 (nand_31_out, decoder_2_out3, decoder_1_out6);
  nand nand_32 (nand_32_out, decoder_2_out3, decoder_1_out7);
  RAM #(.addrWidth(24), .dataWidth(32), .bus("separate"), .Select("low")) ram_25 (
    .addr(Address_Bus[25:2]), .din(Data_Bus_In), .data(Data_Bus_Out), .str(Store), .sel(nand_25_out),
    .clk(CLK), .ld(Load), .clr(Clear));
  RAM #(.addrWidth(24), .dataWidth(32), .bus("separate"), .Select("low")) ram_26 (
    .addr(Address_Bus[25:2]), .din(Data_Bus_In), .data(Data_Bus_Out), .str(Store), .sel(nand_26_out),
    .clk(CLK), .ld(Load), .clr(Clear));
  RAM #(.addrWidth(24), .dataWidth(32), .bus("separate"), .Select("low")) ram_27 (
    .addr(Address_Bus[25:2]), .din(Data_Bus_In), .data(Data_Bus_Out), .str(Store), .sel(nand_27_out),
    .clk(CLK), .ld(Load), .clr(Clear));
  RAM #(.addrWidth(24), .dataWidth(32), .bus("separate"), .Select("low")) ram_28 (
    .addr(Address_Bus[25:2]), .din(Data_Bus_In), .data(Data_Bus_Out), .str(Store), .sel(nand_28_out),
    .clk(CLK), .ld(Load), .clr(Clear));
  RAM #(.addrWidth(24), .dataWidth(32), .bus("separate"), .Select("low")) ram_29 (
    .addr(Address_Bus[25:2]), .din(Data_Bus_In), .data(Data_Bus_Out), .str(Store), .sel(nand_29_out),
    .clk(CLK), .ld(Load), .clr(Clear));
  RAM #(.addrWidth(24), .dataWidth(32), .bus("separate"), .Select("low")) ram_30 (
    .addr(Address_Bus[25:2]), .din(Data_Bus_In), .data(Data_Bus_Out), .str(Store), .sel(nand_30_out),
    .clk(CLK), .ld(Load), .clr(Clear));
  RAM #(.addrWidth(24), .dataWidth(32), .bus("separate"), .Select("low")) ram_31 (
    .addr(Address_Bus[25:2]), .din(Data_Bus_In), .data(Data_Bus_Out), .str(Store), .sel(nand_31_out),
    .clk(CLK), .ld(Load), .clr(Clear));
  RAM #(.addrWidth(24), .dataWidth(32), .bus("separate"), .Select("low")) ram_32 (
    .addr(Address_Bus[25:2]), .din(Data_Bus_In), .data(Data_Bus_Out), .str(Store), .sel(nand_32_out),
    .clk(CLK), .ld(Load), .clr(Clear));
  // Probe on Data_Bus_In
  nand nand_33 (nand_33_out, decoder_2_out4, decoder_1_out0);
  nand nand_34 (nand_34_out, decoder_2_out4, decoder_1_out1);
  nand nand_35 (nand_35_out, decoder_2_out4, decoder_1_out2);
  nand nand_36 (nand_36_out, decoder_2_out4, decoder_1_out3);
  nand nand_37 (nand_37_out, decoder_2_out4, decoder_1_out4);
  nand nand_38 (nand_38_out, decoder_2_out4, decoder_1_out5);
  nand nand_39 (nand_39_out, decoder_2_out4, decoder_1_out6);
  nand nand_40 (nand_40_out, decoder_2_out4, decoder_1_out7);
  RAM #(.addrWidth(24), .dataWidth(32), .bus("separate"), .Select("low")) ram_33 (
    .addr(Address_Bus[25:2]), .din(Data_Bus_In), .data(Data_Bus_Out), .str(Store), .sel(nand_33_out),
    .clk(CLK), .ld(Load), .clr(Clear));
  RAM #(.addrWidth(24), .dataWidth(32), .bus("separate"), .Select("low")) ram_34 (
    .addr(Address_Bus[25:2]), .din(Data_Bus_In), .data(Data_Bus_Out), .str(Store), .sel(nand_34_out),
    .clk(CLK), .ld(Load), .clr(Clear));
  RAM #(.addrWidth(24), .dataWidth(32), .bus("separate"), .Select("low")) ram_35 (
    .addr(Address_Bus[25:2]), .din(Data_Bus_In), .data(Data_Bus_Out), .str(Store), .sel(nand_35_out),
    .clk(CLK), .ld(Load), .clr(Clear));
  RAM #(.addrWidth(24), .dataWidth(32), .bus("separate"), .Select("low")) ram_36 (
    .addr(Address_Bus[25:2]), .din(Data_Bus_In), .data(Data_Bus_Out), .str(Store), .sel(nand_36_out),
    .clk(CLK), .ld(Load), .clr(Clear));
  RAM #(.addrWidth(24), .dataWidth(32), .bus("separate"), .Select("low")) ram_37 (
    .addr(Address_Bus[25:2]), .din(Data_Bus_In), .data(Data_Bus_Out), .str(Store), .sel(nand_37_out),
    .clk(CLK), .ld(Load), .clr(Clear));
  RAM #(.addrWidth(24), .dataWidth(32), .bus("separate"), .Select("low")) ram_38 (
    .addr(Address_Bus[25:2]), .din(Data_Bus_In), .data(Data_Bus_Out), .str(Store), .sel(nand_38_out),
    .clk(CLK), .ld(Load), .clr(Clear));
  RAM #(.addrWidth(24), .dataWidth(32), .bus("separate"), .Select("low")) ram_39 (
    .addr(Address_Bus[25:2]), .din(Data_Bus_In), .data(Data_Bus_Out), .str(Store), .sel(nand_39_out),
    .clk(CLK), .ld(Load), .clr(Clear));
  RAM #(.addrWidth(24), .dataWidth(32), .bus("separate"), .Select("low")) ram_40 (
    .addr(Address_Bus[25:2]), .din(Data_Bus_In), .data(Data_Bus_Out), .str(Store), .sel(nand_40_out),
    .clk(CLK), .ld(Load), .clr(Clear));
  nand nand_41 (nand_41_out, decoder_2_out5, decoder_1_out0);
  nand nand_42 (nand_42_out, decoder_2_out5, decoder_1_out1);
  nand nand_43 (nand_43_out, decoder_2_out5, decoder_1_out2);
  nand nand_44 (nand_44_out, decoder_2_out5, decoder_1_out3);
  nand nand_45 (nand_45_out, decoder_2_out5, decoder_1_out4);
  nand nand_46 (nand_46_out, decoder_2_out5, decoder_1_out5);
  nand nand_47 (nand_47_out, decoder_2_out5, decoder_1_out6);
  nand nand_48 (nand_48_out, decoder_2_out5, decoder_1_out7);
  RAM #(.addrWidth(24), .dataWidth(32), .bus("separate"), .Select("low")) ram_41 (
    .addr(Address_Bus[25:2]), .din(Data_Bus_In), .data(Data_Bus_Out), .str(Store), .sel(nand_41_out),
    .clk(CLK), .ld(Load), .clr(Clear));
  RAM #(.addrWidth(24), .dataWidth(32), .bus("separate"), .Select("low")) ram_42 (
    .addr(Address_Bus[25:2]), .din(Data_Bus_In), .data(Data_Bus_Out), .str(Store), .sel(nand_42_out),
    .clk(CLK), .ld(Load), .clr(Clear));
  RAM #(.addrWidth(24), .dataWidth(32), .bus("separate"), .Select("low")) ram_43 (
    .addr(Address_Bus[25:2]), .din(Data_Bus_In), .data(Data_Bus_Out), .str(Store), .sel(nand_43_out),
    .clk(CLK), .ld(Load), .clr(Clear));
  RAM #(.addrWidth(24), .dataWidth(32), .bus("separate"), .Select("low")) ram_44 (
    .addr(Address_Bus[25:2]), .din(Data_Bus_In), .data(Data_Bus_Out), .str(Store), .sel(nand_44_out),
    .clk(CLK), .ld(Load), .clr(Clear));
  RAM #(.addrWidth(24), .dataWidth(32), .bus("separate"), .Select("low")) ram_45 (
    .addr(Address_Bus[25:2]), .din(Data_Bus_In), .data(Data_Bus_Out), .str(Store), .sel(nand_45_out),
    .clk(CLK), .ld(Load), .clr(Clear));
  RAM #(.addrWidth(24), .dataWidth(32), .bus("separate"), .Select("low")) ram_46 (
    .addr(Address_Bus[25:2]), .din(Data_Bus_In), .data(Data_Bus_Out), .str(Store), .sel(nand_46_out),
    .clk(CLK), .ld(Load), .clr(Clear));
  RAM #(.addrWidth(24), .dataWidth(32), .bus("separate"), .Select("low")) ram_47 (
    .addr(Address_Bus[25:2]), .din(Data_Bus_In), .data(Data_Bus_Out), .str(Store), .sel(nand_47_out),
    .clk(CLK), .ld(Load), .clr(Clear));
  RAM #(.addrWidth(24), .dataWidth(32), .bus("separate"), .Select("low")) ram_48 (
    .addr(Address_Bus[25:2]), .din(Data_Bus_In), .data(Data_Bus_Out), .str(Store), .sel(nand_48_out),
    .clk(CLK), .ld(Load), .clr(Clear));
  nand nand_49 (nand_49_out, decoder_2_out6, decoder_1_out0);
  nand nand_50 (nand_50_out, decoder_2_out6, decoder_1_out1);
  nand nand_51 (nand_51_out, decoder_2_out6, decoder_1_out2);
  nand nand_52 (nand_52_out, decoder_2_out6, decoder_1_out3);
  nand nand_53 (nand_53_out, decoder_2_out6, decoder_1_out4);
  nand nand_54 (nand_54_out, decoder_2_out6, decoder_1_out5);
  nand nand_55 (nand_55_out, decoder_2_out6, decoder_1_out6);
  nand nand_56 (nand_56_out, decoder_2_out6, decoder_1_out7);
  RAM #(.addrWidth(24), .dataWidth(32), .bus("separate"), .Select("low")) ram_49 (
    .addr(Address_Bus[25:2]), .din(Data_Bus_In), .data(Data_Bus_Out), .str(Store), .sel(nand_49_out),
    .clk(CLK), .ld(Load), .clr(Clear));
  RAM #(.addrWidth(24), .dataWidth(32), .bus("separate"), .Select("low")) ram_50 (
    .addr(Address_Bus[25:2]), .din(Data_Bus_In), .data(Data_Bus_Out), .str(Store), .sel(nand_50_out),
    .clk(CLK), .ld(Load), .clr(Clear));
  RAM #(.addrWidth(24), .dataWidth(32), .bus("separate"), .Select("low")) ram_51 (
    .addr(Address_Bus[25:2]), .din(Data_Bus_In), .data(Data_Bus_Out), .str(Store), .sel(nand_51_out),
    .clk(CLK), .ld(Load), .clr(Clear));
  RAM #(.addrWidth(24), .dataWidth(32), .bus("separate"), .Select("low")) ram_52 (
    .addr(Address_Bus[25:2]), .din(Data_Bus_In), .data(Data_Bus_Out), .str(Store), .sel(nand_52_out),
    .clk(CLK), .ld(Load), .clr(Clear));
  RAM #(.addrWidth(24), .dataWidth(32), .bus("separate"), .Select("low")) ram_53 (
    .addr(Address_Bus[25:2]), .din(Data_Bus_In), .data(Data_Bus_Out), .str(Store), .sel(nand_53_out),
    .clk(CLK), .ld(Load), .clr(Clear));
  RAM #(.addrWidth(24), .dataWidth(32), .bus("separate"), .Select("low")) ram_54 (
    .addr(Address_Bus[25:2]), .din(Data_Bus_In), .data(Data_Bus_Out), .str(Store), .sel(nand_54_out),
    .clk(CLK), .ld(Load), .clr(Clear));
  RAM #(.addrWidth(24), .dataWidth(32), .bus("separate"), .Select("low")) ram_55 (
    .addr(Address_Bus[25:2]), .din(Data_Bus_In), .data(Data_Bus_Out), .str(Store), .sel(nand_55_out),
    .clk(CLK), .ld(Load), .clr(Clear));
  RAM #(.addrWidth(24), .dataWidth(32), .bus("separate"), .Select("low")) ram_56 (
    .addr(Address_Bus[25:2]), .din(Data_Bus_In), .data(Data_Bus_Out), .str(Store), .sel(nand_56_out),
    .clk(CLK), .ld(Load), .clr(Clear));
  nand nand_57 (nand_57_out, decoder_2_out7, decoder_1_out0);
  nand nand_58 (nand_58_out, decoder_2_out7, decoder_1_out1);
  nand nand_59 (nand_59_out, decoder_2_out7, decoder_1_out2);
  nand nand_60 (nand_60_out, decoder_2_out7, decoder_1_out3);
  nand nand_61 (nand_61_out, decoder_2_out7, decoder_1_out4);
  nand nand_62 (nand_62_out, decoder_2_out7, decoder_1_out5);
  nand nand_63 (nand_63_out, decoder_2_out7, decoder_1_out6);
  nand nand_64 (nand_64_out, decoder_2_out7, decoder_1_out7);
  RAM #(.addrWidth(24), .dataWidth(32), .bus("separate"), .Select("low")) ram_57 (
    .addr(Address_Bus[25:2]), .din(Data_Bus_In), .data(Data_Bus_Out), .str(Store), .sel(nand_57_out),
    .clk(CLK), .ld(Load), .clr(Clear));
  RAM #(.addrWidth(24), .dataWidth(32), .bus("separate"), .Select("low")) ram_58 (
    .addr(Address_Bus[25:2]), .din(Data_Bus_In), .data(Data_Bus_Out), .str(Store), .sel(nand_58_out),
    .clk(CLK), .ld(Load), .clr(Clear));
  RAM #(.addrWidth(24), .dataWidth(32), .bus("separate"), .Select("low")) ram_59 (
    .addr(Address_Bus[25:2]), .din(Data_Bus_In), .data(Data_Bus_Out), .str(Store), .sel(nand_59_out),
    .clk(CLK), .ld(Load), .clr(Clear));
  RAM #(.addrWidth(24), .dataWidth(32), .bus("separate"), .Select("low")) ram_60 (
    .addr(Address_Bus[25:2]), .din(Data_Bus_In), .data(Data_Bus_Out), .str(Store), .sel(nand_60_out),
    .clk(CLK), .ld(Load), .clr(Clear));
  RAM #(.addrWidth(24), .dataWidth(32), .bus("separate"), .Select("low")) ram_61 (
    .addr(Address_Bus[25:2]), .din(Data_Bus_In), .data(Data_Bus_Out), .str(Store), .sel(nand_61_out),
    .clk(CLK), .ld(Load), .clr(Clear));
  RAM #(.addrWidth(24), .dataWidth(32), .bus("separate"), .Select("low")) ram_62 (
    .addr(Address_Bus[25:2]), .din(Data_Bus_In), .data(Data_Bus_Out), .str(Store), .sel(nand_62_out),
    .clk(CLK), .ld(Load), .clr(Clear));
  RAM #(.addrWidth(24), .dataWidth(32), .bus("separate"), .Select("low")) ram_63 (
    .addr(Address_Bus[25:2]), .din(Data_Bus_In), .data(Data_Bus_Out), .str(Store), .sel(nand_63_out),
    .clk(CLK), .ld(Load), .clr(Clear));
  RAM #(.addrWidth(24), .dataWidth(32), .bus("separate"), .Select("low")) ram_64 (
    .addr(Address_Bus[25:2]), .din(Data_Bus_In), .data(Data_Bus_Out), .str(Store), .sel(nand_64_out),
    .clk(CLK), .ld(Load), .clr(Clear));

  // Other names for the same wires on the sheet: Ad_TP[31:0] = Address_Bus; _24位[23:0] = Address_Bus[25:2];
  //   Data_Bus_In_TP[31:0] = Data_Bus_In; DataOut[31:0] = Data_Bus_Out

  // Notes on the sheet:
  //   外部各接口定义与原RAM相同
  //   按照字节编址，但按照字对齐访问
endmodule

module \实验3_32位地址总线32位数据总线ROM存储器  (
  input  CS,
  input  [31:0] Address_Bus,
  output [31:0] Data_Bus_Out
);

  wire decoder_1_out0, decoder_1_out1, decoder_1_out2, decoder_1_out3, decoder_1_out4, decoder_1_out5,
       decoder_1_out7, decoder_2_out0, decoder_2_out1, decoder_2_out2, decoder_2_out3, decoder_2_out4,
       decoder_2_out5, decoder_2_out6, decoder_2_out7, nand_1_out, nand_2_out, nand_3_out, nand_4_out,
       nand_5_out, nand_6_out, nand_7_out, nand_8_out, nand_9_out, nand_10_out, nand_11_out, nand_12_out,
       nand_13_out, nand_14_out, nand_15_out, nand_16_out, nand_17_out, nand_18_out, nand_19_out,
       nand_20_out, nand_21_out, nand_22_out, nand_23_out, nand_24_out, nand_25_out, nand_26_out,
       nand_27_out, nand_28_out, nand_29_out, nand_30_out, nand_31_out, nand_32_out, nand_33_out,
       nand_34_out, nand_35_out, nand_36_out, nand_37_out, nand_38_out, nand_39_out, nand_40_out,
       nand_41_out, nand_42_out, nand_43_out, nand_44_out, nand_45_out, nand_46_out, nand_47_out,
       nand_48_out, nand_49_out, nand_50_out, nand_51_out, nand_52_out, nand_53_out, nand_54_out,
       nand_55_out, nand_56_out, nand_57_out, nand_58_out, nand_59_out, nand_60_out, nand_61_out,
       nand_62_out, nand_63_out, nand_64_out;

  Decoder #(.select(3), .tristate("false"), .disabled("Z"), .enable("true")) decoder_1 (
    .out0(decoder_1_out0), .out1(decoder_1_out1), .out2(decoder_1_out2), .out3(decoder_1_out3),
    .out4(decoder_1_out4), .out5(decoder_1_out5), .out6(decoder_1_out5), .out7(decoder_1_out7),
    .sel(Address_Bus[31:29]), .en(CS));
  Decoder #(.select(3), .tristate("false"), .disabled("Z"), .enable("true")) decoder_2 (
    .out0(decoder_2_out0), .out1(decoder_2_out1), .out2(decoder_2_out2), .out3(decoder_2_out3),
    .out4(decoder_2_out4), .out5(decoder_2_out5), .out6(decoder_2_out6), .out7(decoder_2_out7),
    .sel(Address_Bus[28:26]), .en(CS));
  nand nand_1 (nand_1_out, decoder_2_out0, decoder_1_out0);
  nand nand_2 (nand_2_out, decoder_2_out0, decoder_1_out1);
  nand nand_3 (nand_3_out, decoder_2_out0, decoder_1_out2);
  nand nand_4 (nand_4_out, decoder_2_out0, decoder_1_out3);
  nand nand_5 (nand_5_out, decoder_2_out0, decoder_1_out4);
  nand nand_6 (nand_6_out, decoder_2_out0, decoder_1_out5);
  nand nand_7 (nand_7_out, decoder_2_out0, decoder_1_out5);
  nand nand_8 (nand_8_out, decoder_2_out0, decoder_1_out7);
  ROM #(.addrWidth(24), .dataWidth(32), .Select("low")) rom_1 (
    .addr(Address_Bus[25:2]), .data(Data_Bus_Out), .sel(nand_1_out));
  ROM #(.addrWidth(24), .dataWidth(32), .Select("low")) rom_2 (
    .addr(Address_Bus[25:2]), .data(Data_Bus_Out), .sel(nand_2_out));
  ROM #(.addrWidth(24), .dataWidth(32), .Select("low")) rom_3 (
    .addr(Address_Bus[25:2]), .data(Data_Bus_Out), .sel(nand_3_out));
  ROM #(.addrWidth(24), .dataWidth(32), .Select("low")) rom_4 (
    .addr(Address_Bus[25:2]), .data(Data_Bus_Out), .sel(nand_4_out));
  ROM #(.addrWidth(24), .dataWidth(32), .Select("low")) rom_5 (
    .addr(Address_Bus[25:2]), .data(Data_Bus_Out), .sel(nand_5_out));
  ROM #(.addrWidth(24), .dataWidth(32), .Select("low")) rom_6 (
    .addr(Address_Bus[25:2]), .data(Data_Bus_Out), .sel(nand_6_out));
  ROM #(.addrWidth(24), .dataWidth(32), .Select("low")) rom_7 (
    .addr(Address_Bus[25:2]), .data(Data_Bus_Out), .sel(nand_7_out));
  ROM #(.addrWidth(24), .dataWidth(32), .Select("low")) rom_8 (
    .addr(Address_Bus[25:2]), .data(Data_Bus_Out), .sel(nand_8_out));
  nand nand_9 (nand_9_out, decoder_2_out1, decoder_1_out0);
  nand nand_10 (nand_10_out, decoder_2_out1, decoder_1_out1);
  nand nand_11 (nand_11_out, decoder_2_out1, decoder_1_out2);
  nand nand_12 (nand_12_out, decoder_2_out1, decoder_1_out3);
  nand nand_13 (nand_13_out, decoder_2_out1, decoder_1_out4);
  nand nand_14 (nand_14_out, decoder_2_out1, decoder_1_out5);
  nand nand_15 (nand_15_out, decoder_2_out1, decoder_1_out5);
  nand nand_16 (nand_16_out, decoder_2_out1, decoder_1_out7);
  ROM #(.addrWidth(24), .dataWidth(32), .Select("low")) rom_9 (
    .addr(Address_Bus[25:2]), .data(Data_Bus_Out), .sel(nand_9_out));
  ROM #(.addrWidth(24), .dataWidth(32), .Select("low")) rom_10 (
    .addr(Address_Bus[25:2]), .data(Data_Bus_Out), .sel(nand_10_out));
  ROM #(.addrWidth(24), .dataWidth(32), .Select("low")) rom_11 (
    .addr(Address_Bus[25:2]), .data(Data_Bus_Out), .sel(nand_11_out));
  ROM #(.addrWidth(24), .dataWidth(32), .Select("low")) rom_12 (
    .addr(Address_Bus[25:2]), .data(Data_Bus_Out), .sel(nand_12_out));
  ROM #(.addrWidth(24), .dataWidth(32), .Select("low")) rom_13 (
    .addr(Address_Bus[25:2]), .data(Data_Bus_Out), .sel(nand_13_out));
  ROM #(.addrWidth(24), .dataWidth(32), .Select("low")) rom_14 (
    .addr(Address_Bus[25:2]), .data(Data_Bus_Out), .sel(nand_14_out));
  ROM #(.addrWidth(24), .dataWidth(32), .Select("low")) rom_15 (
    .addr(Address_Bus[25:2]), .data(Data_Bus_Out), .sel(nand_15_out));
  ROM #(.addrWidth(24), .dataWidth(32), .Select("low")) rom_16 (
    .addr(Address_Bus[25:2]), .data(Data_Bus_Out), .sel(nand_16_out));
  nand nand_17 (nand_17_out, decoder_2_out2, decoder_1_out0);
  nand nand_18 (nand_18_out, decoder_2_out2, decoder_1_out1);
  nand nand_19 (nand_19_out, decoder_2_out2, decoder_1_out2);
  nand nand_20 (nand_20_out, decoder_2_out2, decoder_1_out3);
  nand nand_21 (nand_21_out, decoder_2_out2, decoder_1_out4);
  nand nand_22 (nand_22_out, decoder_2_out2, decoder_1_out5);
  nand nand_23 (nand_23_out, decoder_2_out2, decoder_1_out5);
  nand nand_24 (nand_24_out, decoder_2_out2, decoder_1_out7);
  ROM #(.addrWidth(24), .dataWidth(32), .Select("low")) rom_17 (
    .addr(Address_Bus[25:2]), .data(Data_Bus_Out), .sel(nand_17_out));
  ROM #(.addrWidth(24), .dataWidth(32), .Select("low")) rom_18 (
    .addr(Address_Bus[25:2]), .data(Data_Bus_Out), .sel(nand_18_out));
  ROM #(.addrWidth(24), .dataWidth(32), .Select("low")) rom_19 (
    .addr(Address_Bus[25:2]), .data(Data_Bus_Out), .sel(nand_19_out));
  ROM #(.addrWidth(24), .dataWidth(32), .Select("low")) rom_20 (
    .addr(Address_Bus[25:2]), .data(Data_Bus_Out), .sel(nand_20_out));
  ROM #(.addrWidth(24), .dataWidth(32), .Select("low")) rom_21 (
    .addr(Address_Bus[25:2]), .data(Data_Bus_Out), .sel(nand_21_out));
  ROM #(.addrWidth(24), .dataWidth(32), .Select("low")) rom_22 (
    .addr(Address_Bus[25:2]), .data(Data_Bus_Out), .sel(nand_22_out));
  ROM #(.addrWidth(24), .dataWidth(32), .Select("low")) rom_23 (
    .addr(Address_Bus[25:2]), .data(Data_Bus_Out), .sel(nand_23_out));
  ROM #(.addrWidth(24), .dataWidth(32), .Select("low")) rom_24 (
    .addr(Address_Bus[25:2]), .data(Data_Bus_Out), .sel(nand_24_out));
  nand nand_25 (nand_25_out, decoder_2_out3, decoder_1_out0);
  nand nand_26 (nand_26_out, decoder_2_out3, decoder_1_out1);
  nand nand_27 (nand_27_out, decoder_2_out3, decoder_1_out2);
  nand nand_28 (nand_28_out, decoder_2_out3, decoder_1_out3);
  nand nand_29 (nand_29_out, decoder_2_out3, decoder_1_out4);
  nand nand_30 (nand_30_out, decoder_2_out3, decoder_1_out5);
  nand nand_31 (nand_31_out, decoder_2_out3, decoder_1_out5);
  nand nand_32 (nand_32_out, decoder_2_out3, decoder_1_out7);
  ROM #(.addrWidth(24), .dataWidth(32), .Select("low")) rom_25 (
    .addr(Address_Bus[25:2]), .data(Data_Bus_Out), .sel(nand_25_out));
  ROM #(.addrWidth(24), .dataWidth(32), .Select("low")) rom_26 (
    .addr(Address_Bus[25:2]), .data(Data_Bus_Out), .sel(nand_26_out));
  ROM #(.addrWidth(24), .dataWidth(32), .Select("low")) rom_27 (
    .addr(Address_Bus[25:2]), .data(Data_Bus_Out), .sel(nand_27_out));
  ROM #(.addrWidth(24), .dataWidth(32), .Select("low")) rom_28 (
    .addr(Address_Bus[25:2]), .data(Data_Bus_Out), .sel(nand_28_out));
  ROM #(.addrWidth(24), .dataWidth(32), .Select("low")) rom_29 (
    .addr(Address_Bus[25:2]), .data(Data_Bus_Out), .sel(nand_29_out));
  ROM #(.addrWidth(24), .dataWidth(32), .Select("low")) rom_30 (
    .addr(Address_Bus[25:2]), .data(Data_Bus_Out), .sel(nand_30_out));
  ROM #(.addrWidth(24), .dataWidth(32), .Select("low")) rom_31 (
    .addr(Address_Bus[25:2]), .data(Data_Bus_Out), .sel(nand_31_out));
  ROM #(.addrWidth(24), .dataWidth(32), .Select("low")) rom_32 (
    .addr(Address_Bus[25:2]), .data(Data_Bus_Out), .sel(nand_32_out));
  nand nand_33 (nand_33_out, decoder_2_out4, decoder_1_out0);
  nand nand_34 (nand_34_out, decoder_2_out4, decoder_1_out1);
  nand nand_35 (nand_35_out, decoder_2_out4, decoder_1_out2);
  nand nand_36 (nand_36_out, decoder_2_out4, decoder_1_out3);
  nand nand_37 (nand_37_out, decoder_2_out4, decoder_1_out4);
  nand nand_38 (nand_38_out, decoder_2_out4, decoder_1_out5);
  nand nand_39 (nand_39_out, decoder_2_out4, decoder_1_out5);
  nand nand_40 (nand_40_out, decoder_2_out4, decoder_1_out7);
  ROM #(.addrWidth(24), .dataWidth(32), .Select("low")) rom_33 (
    .addr(Address_Bus[25:2]), .data(Data_Bus_Out), .sel(nand_33_out));
  ROM #(.addrWidth(24), .dataWidth(32), .Select("low")) rom_34 (
    .addr(Address_Bus[25:2]), .data(Data_Bus_Out), .sel(nand_34_out));
  ROM #(.addrWidth(24), .dataWidth(32), .Select("low")) rom_35 (
    .addr(Address_Bus[25:2]), .data(Data_Bus_Out), .sel(nand_35_out));
  ROM #(.addrWidth(24), .dataWidth(32), .Select("low")) rom_36 (
    .addr(Address_Bus[25:2]), .data(Data_Bus_Out), .sel(nand_36_out));
  ROM #(.addrWidth(24), .dataWidth(32), .Select("low")) rom_37 (
    .addr(Address_Bus[25:2]), .data(Data_Bus_Out), .sel(nand_37_out));
  ROM #(.addrWidth(24), .dataWidth(32), .Select("low")) rom_38 (
    .addr(Address_Bus[25:2]), .data(Data_Bus_Out), .sel(nand_38_out));
  ROM #(.addrWidth(24), .dataWidth(32), .Select("low")) rom_39 (
    .addr(Address_Bus[25:2]), .data(Data_Bus_Out), .sel(nand_39_out));
  ROM #(.addrWidth(24), .dataWidth(32), .Select("low")) rom_40 (
    .addr(Address_Bus[25:2]), .data(Data_Bus_Out), .sel(nand_40_out));
  nand nand_41 (nand_41_out, decoder_2_out5, decoder_1_out0);
  nand nand_42 (nand_42_out, decoder_2_out5, decoder_1_out1);
  nand nand_43 (nand_43_out, decoder_2_out5, decoder_1_out2);
  nand nand_44 (nand_44_out, decoder_2_out5, decoder_1_out3);
  nand nand_45 (nand_45_out, decoder_2_out5, decoder_1_out4);
  nand nand_46 (nand_46_out, decoder_2_out5, decoder_1_out5);
  nand nand_47 (nand_47_out, decoder_2_out5, decoder_1_out5);
  nand nand_48 (nand_48_out, decoder_2_out5, decoder_1_out7);
  ROM #(.addrWidth(24), .dataWidth(32), .Select("low")) rom_41 (
    .addr(Address_Bus[25:2]), .data(Data_Bus_Out), .sel(nand_41_out));
  ROM #(.addrWidth(24), .dataWidth(32), .Select("low")) rom_42 (
    .addr(Address_Bus[25:2]), .data(Data_Bus_Out), .sel(nand_42_out));
  ROM #(.addrWidth(24), .dataWidth(32), .Select("low")) rom_43 (
    .addr(Address_Bus[25:2]), .data(Data_Bus_Out), .sel(nand_43_out));
  ROM #(.addrWidth(24), .dataWidth(32), .Select("low")) rom_44 (
    .addr(Address_Bus[25:2]), .data(Data_Bus_Out), .sel(nand_44_out));
  ROM #(.addrWidth(24), .dataWidth(32), .Select("low")) rom_45 (
    .addr(Address_Bus[25:2]), .data(Data_Bus_Out), .sel(nand_45_out));
  ROM #(.addrWidth(24), .dataWidth(32), .Select("low")) rom_46 (
    .addr(Address_Bus[25:2]), .data(Data_Bus_Out), .sel(nand_46_out));
  ROM #(.addrWidth(24), .dataWidth(32), .Select("low")) rom_47 (
    .addr(Address_Bus[25:2]), .data(Data_Bus_Out), .sel(nand_47_out));
  ROM #(.addrWidth(24), .dataWidth(32), .Select("low")) rom_48 (
    .addr(Address_Bus[25:2]), .data(Data_Bus_Out), .sel(nand_48_out));
  nand nand_49 (nand_49_out, decoder_2_out6, decoder_1_out0);
  nand nand_50 (nand_50_out, decoder_2_out6, decoder_1_out1);
  nand nand_51 (nand_51_out, decoder_2_out6, decoder_1_out2);
  nand nand_52 (nand_52_out, decoder_2_out6, decoder_1_out3);
  nand nand_53 (nand_53_out, decoder_2_out6, decoder_1_out4);
  nand nand_54 (nand_54_out, decoder_2_out6, decoder_1_out5);
  nand nand_55 (nand_55_out, decoder_2_out6, decoder_1_out5);
  nand nand_56 (nand_56_out, decoder_2_out6, decoder_1_out7);
  ROM #(.addrWidth(24), .dataWidth(32), .Select("low")) rom_49 (
    .addr(Address_Bus[25:2]), .data(Data_Bus_Out), .sel(nand_49_out));
  ROM #(.addrWidth(24), .dataWidth(32), .Select("low")) rom_50 (
    .addr(Address_Bus[25:2]), .data(Data_Bus_Out), .sel(nand_50_out));
  ROM #(.addrWidth(24), .dataWidth(32), .Select("low")) rom_51 (
    .addr(Address_Bus[25:2]), .data(Data_Bus_Out), .sel(nand_51_out));
  ROM #(.addrWidth(24), .dataWidth(32), .Select("low")) rom_52 (
    .addr(Address_Bus[25:2]), .data(Data_Bus_Out), .sel(nand_52_out));
  ROM #(.addrWidth(24), .dataWidth(32), .Select("low")) rom_53 (
    .addr(Address_Bus[25:2]), .data(Data_Bus_Out), .sel(nand_53_out));
  ROM #(.addrWidth(24), .dataWidth(32), .Select("low")) rom_54 (
    .addr(Address_Bus[25:2]), .data(Data_Bus_Out), .sel(nand_54_out));
  ROM #(.addrWidth(24), .dataWidth(32), .Select("low")) rom_55 (
    .addr(Address_Bus[25:2]), .data(Data_Bus_Out), .sel(nand_55_out));
  ROM #(.addrWidth(24), .dataWidth(32), .Select("low")) rom_56 (
    .addr(Address_Bus[25:2]), .data(Data_Bus_Out), .sel(nand_56_out));
  nand nand_57 (nand_57_out, decoder_2_out7, decoder_1_out0);
  nand nand_58 (nand_58_out, decoder_2_out7, decoder_1_out1);
  nand nand_59 (nand_59_out, decoder_2_out7, decoder_1_out2);
  nand nand_60 (nand_60_out, decoder_2_out7, decoder_1_out3);
  nand nand_61 (nand_61_out, decoder_2_out7, decoder_1_out4);
  nand nand_62 (nand_62_out, decoder_2_out7, decoder_1_out5);
  nand nand_63 (nand_63_out, decoder_2_out7, decoder_1_out5);
  nand nand_64 (nand_64_out, decoder_2_out7, decoder_1_out7);
  ROM #(.addrWidth(24), .dataWidth(32), .Select("low")) rom_57 (
    .addr(Address_Bus[25:2]), .data(Data_Bus_Out), .sel(nand_57_out));
  ROM #(.addrWidth(24), .dataWidth(32), .Select("low")) rom_58 (
    .addr(Address_Bus[25:2]), .data(Data_Bus_Out), .sel(nand_58_out));
  ROM #(.addrWidth(24), .dataWidth(32), .Select("low")) rom_59 (
    .addr(Address_Bus[25:2]), .data(Data_Bus_Out), .sel(nand_59_out));
  ROM #(.addrWidth(24), .dataWidth(32), .Select("low")) rom_60 (
    .addr(Address_Bus[25:2]), .data(Data_Bus_Out), .sel(nand_60_out));
  ROM #(.addrWidth(24), .dataWidth(32), .Select("low")) rom_61 (
    .addr(Address_Bus[25:2]), .data(Data_Bus_Out), .sel(nand_61_out));
  ROM #(.addrWidth(24), .dataWidth(32), .Select("low")) rom_62 (
    .addr(Address_Bus[25:2]), .data(Data_Bus_Out), .sel(nand_62_out));
  ROM #(.addrWidth(24), .dataWidth(32), .Select("low")) rom_63 (
    .addr(Address_Bus[25:2]), .data(Data_Bus_Out), .sel(nand_63_out));
  ROM #(.addrWidth(24), .dataWidth(32), .Select("low")) rom_64 (
    .addr(Address_Bus[25:2]), .data(Data_Bus_Out), .sel(nand_64_out));

  // Other names for the same wires on the sheet: Ad_TP[31:0] = Address_Bus; _24位[23:0] = Address_Bus[25:2];
  //   DataOut[31:0] = Data_Bus_Out

  // Notes on the sheet:
  //   contents of rom_1 (hex, n*v repeats v):
  //   2010ffff 20110000 ae300000 22100001 22310004 ae300000 22100001 22310004 ae300000 22100001 22310004
  //   ae300000 22100001 22310004 ae300000 22100001 22310004 ae300000 22100001 22310004 ae300000 22100001
  //   22310004 ae300000 8020 2011001c 8e130000 8e340200 274402a 11000002 ae330000 ae140000 2231fffc
  //   1611fff8 22100004 2011001c 1611fff5 c
  //   外部各接口定义与原ROM相同
  //   按照字节编址，但按照字对齐访问
  //   contents of rom_9 (hex, n*v repeats v):
  //   2010000a 20110005 2114020 2114822 20120055 201300aa 2535024 2535825 324c00aa 366d0055 c
  //   contents of rom_17 (hex, n*v repeats v):
  //   20100001 20110000 ae300000 22100001 22310004 ae300000 22100001 22310004 ae300000 22100001 22310004
  //   ae300000 22100001 22310004 ae300000 22100001 22310004 ae300000 22100001 22310004 ae300000 22100001
  //   22310004 ae300000 8020 2011001c 8e130000 8e340000 274402a 11000002 ae330000 ae140000 2231fffc
  //   1611fff8 22100004 2011001c 1611fff5 c
endmodule

module \实验3_MIPS寄存器文件  (
  input  [4:0] A1_address,
  input  [31:0] W_data,
  input  [4:0] A2_address,
  input  [4:0] W_address,
  input  W_Enable,
  input  CLK,
  output [31:0] R_data1,
  output [31:0] R_data2
);

  // RegisterFile registerfile_1: pin names not known; wires that end beside it: W_data, CLK, W_Enable, W_address, A1_address, A2_address, R_data1, R_data2

  // Other names for the same wires on the sheet: A1[4:0] = A1_address; A2[4:0] = A2_address; A3[4:0] = W_address;
  //   RD1[31:0] = R_data1; RD2[31:0] = R_data2; WD3[31:0] = W_data; WE3 = W_Enable
endmodule

module \实验3_单周期处理器控制器  (
  input  [5:0] Op5_0,
  input  [5:0] Funct,
  output RegWrite,
  output RegDst,
  output AluSrc,
  output Bne,
  output Beq,
  output MemtoReg,
  output MemWrite,
  output [2:0] ALUControl2_0,
  output SYSCALL
);

  wire and_3_out, and_5_out, and_6_out, and_7_out, and_8_out, and_11_out, and_12_out, and_14_out, and_16_out,
       comparator_1_eq, comparator_2_eq, or_1_out, or_2_out;
  wire [0:0] ALUOp;

  and and_1 (RegDst, ~Op5_0[5], ~Op5_0[4], ~Op5_0[3], ~Op5_0[2], ~Op5_0[1], ~Op5_0[0]);  // AND_Gate
  and and_2 (MemtoReg, Op5_0[5], ~Op5_0[4], ~Op5_0[3], ~Op5_0[2], Op5_0[1], Op5_0[0]);  // AND_Gate
  and and_3 (and_3_out, Funct[5], ~Funct[4], ~Funct[3], ~Funct[2], ~Funct[0]);  // AND_Gate
  Comparator #(.width(6), .mode("twosComplement")) comparator_1 (
    .a(Funct), .b(6'b001100), .eq(comparator_1_eq));  // open: gt, lt
  Comparator #(.width(2), .mode("twosComplement")) comparator_2 (
    .a({RegDst, ALUOp[0]}), .b(2'b10), .eq(comparator_2_eq));  // open: gt, lt
  and and_4 (MemWrite, Op5_0[5], ~Op5_0[4], Op5_0[3], ~Op5_0[2], Op5_0[1], Op5_0[0]);  // AND_Gate
  and and_5 (and_5_out, Funct[5], ~Funct[4], Funct[3], ~Funct[2], Funct[1], ~Funct[0]);  // AND_Gate
  and and_6 (and_6_out, Funct[3], ~Funct[2], Funct[1], ~Funct[0]);  // AND_Gate
  and and_7 (and_7_out, ~Funct[4], Funct[5], RegDst);  // AND_Gate
  or or_1 (or_1_out, and_5_out, and_3_out);
  and and_8 (and_8_out, ALUOp[0], ~RegDst);  // AND_Gate
  and and_9 (SYSCALL, comparator_1_eq, comparator_2_eq);
  and and_10 (Beq, ~Op5_0[5], ~Op5_0[4], ~Op5_0[3], Op5_0[2], ~Op5_0[1], ~Op5_0[0]);  // AND_Gate
  and and_11 (and_11_out, ~Funct[3], Funct[2], ~Funct[1], Funct[0]);  // AND_Gate
  or or_2 (or_2_out, and_6_out, and_11_out);
  and and_12 (and_12_out, or_1_out, RegDst);
  and and_13 (Bne, ~Op5_0[5], ~Op5_0[4], ~Op5_0[3], Op5_0[2], ~Op5_0[1], Op5_0[0]);  // AND_Gate
  and and_14 (and_14_out, RegDst, Funct[5], ~Funct[4], ~Funct[2], Funct[1], ~Funct[0]);  // AND_Gate
  and and_15 (ALUControl2_0[0], or_2_out, and_7_out);
  or or_3 (ALUControl2_0[1], and_12_out, ~RegDst);  // OR_Gate
  or or_4 (ALUControl2_0[2], and_14_out, and_8_out);
  and and_16 (and_16_out, ~Op5_0[5], ~Op5_0[4], Op5_0[3], ~Op5_0[2], ~Op5_0[1], ~Op5_0[0]);  // AND_Gate
  or or_5 (RegWrite, MemtoReg, and_16_out, RegDst);
  or or_6 (AluSrc, MemtoReg, and_16_out, MemWrite);
  or or_7 (ALUOp[0], Bne, Beq);

  // Other names for the same wires on the sheet: ALUOp[1] = RegDst
endmodule

module \实验3_单周期CPU  (
);

  wire AluSrc, and_2_out, and_3_out, Beq, Bne, Branch, CLK, clock_1_out, MemtoReg, MemWrite, RegDst,
       RegWrite, Reset, SYSCALL, Zero;
  wire [2:0] ALUControl;
  wire [4:0] multiplexer_2_out;
  wire [31:0] adder_1_out, adder_2_out, bit_extender_1_out, multiplexer_1_out, multiplexer_3_out,
       multiplexer_4_out, register_1_q, shifter_1_out, \实验3_32位地址总线32位数据总线ram存储器_1_data_bus_out ,
       \实验3_32位地址总线32位数据总线rom存储器_1_data_bus_out , \实验3_mips寄存器文件_1_r_data1 , \实验3_mips寄存器文件_1_r_data2 ,
       \实验3_算术逻辑运算单元alu_1_result ;

  Button u_Reset (.out(Reset));
  and and_1 (CLK, clock_1_out, ~SYSCALL);  // AND_Gate
  Multiplexer #(.select(1), .width(32), .disabled("Z"), .enable("false")) multiplexer_1 (
    .in0(adder_1_out), .in1(adder_2_out), .out(multiplexer_1_out), .sel(Branch));
  Register #(.width(32), .trigger("rising"), .Select("low")) register_1 (
    .D(multiplexer_1_out), .Q(register_1_q), .clk(CLK), .clr(Reset));  // open: en
  Clock #(.highDuration(1), .lowDuration(1)) clock_1 (.out(clock_1_out));
  // Probe on register_1_q
  Adder #(.width(32)) adder_1 (.a(register_1_q), .b(32'h4), .out(adder_1_out));  // open: cin, cout
  // Probe on \实验3_32位地址总线32位数据总线rom存储器_1_data_bus_out 
  \实验3_32位地址总线32位数据总线ROM存储器  \u_实验3_32位地址总线32位数据总线rom存储器_1  (
    .CS(1'b1), .Address_Bus(register_1_q), .Data_Bus_Out(\实验3_32位地址总线32位数据总线rom存储器_1_data_bus_out ));
  \实验3_单周期处理器控制器  \u_实验3_单周期处理器控制器_1  (
    .Op5_0(\实验3_32位地址总线32位数据总线rom存储器_1_data_bus_out [31:26]),
    .Funct(\实验3_32位地址总线32位数据总线rom存储器_1_data_bus_out [5:0]), .RegWrite(RegWrite), .RegDst(RegDst),
    .AluSrc(AluSrc), .Beq(Beq), .MemWrite(MemWrite), .ALUControl2_0(ALUControl), .MemtoReg(MemtoReg),
    .Bne(Bne), .SYSCALL(SYSCALL));
  \实验3_MIPS寄存器文件  \u_实验3_mips寄存器文件_1  (
    .A1_address(\实验3_32位地址总线32位数据总线rom存储器_1_data_bus_out [25:21]), .W_data(multiplexer_4_out),
    .R_data1(\实验3_mips寄存器文件_1_r_data1 ), .R_data2(\实验3_mips寄存器文件_1_r_data2 ),
    .A2_address(\实验3_32位地址总线32位数据总线rom存储器_1_data_bus_out [20:16]), .W_address(multiplexer_2_out),
    .W_Enable(RegWrite), .CLK(CLK));
  assign bit_extender_1_out = {{16{\实验3_32位地址总线32位数据总线rom存储器_1_data_bus_out [15]}}, \实验3_32位地址总线32位数据总线rom存储器_1_data_bus_out [15:0]};  // Bit_Extender bit_extender_1
  Multiplexer #(.select(1), .width(5), .disabled("Z"), .enable("false")) multiplexer_2 (
    .in0(\实验3_32位地址总线32位数据总线rom存储器_1_data_bus_out [20:16]),
    .in1(\实验3_32位地址总线32位数据总线rom存储器_1_data_bus_out [15:11]), .out(multiplexer_2_out), .sel(RegDst));
  Shifter #(.width(32), .shift("ll")) shifter_1 (.in(bit_extender_1_out), .\dist (5'b00010), .out(shifter_1_out));
  \实验3_算术逻辑运算单元ALU  \u_实验3_算术逻辑运算单元alu_1  (
    .AluOP(ALUControl), .X(\实验3_mips寄存器文件_1_r_data1 ), .Result(\实验3_算术逻辑运算单元alu_1_result ),
    .Y(multiplexer_3_out), .\结果是否为0 (Zero));
  Multiplexer #(.select(1), .width(32), .disabled("Z"), .enable("false")) multiplexer_3 (
    .in0(\实验3_mips寄存器文件_1_r_data2 ), .in1(bit_extender_1_out), .out(multiplexer_3_out), .sel(AluSrc));
  Adder #(.width(32)) adder_2 (.a(shifter_1_out), .b(adder_1_out), .out(adder_2_out));  // open: cin, cout
  or or_1 (Branch, and_3_out, and_2_out);
  and and_2 (and_2_out, Zero, Beq);
  and and_3 (and_3_out, Bne, ~Zero);  // AND_Gate
  \实验3_32位地址总线32位数据总线RAM存储器  \u_实验3_32位地址总线32位数据总线ram存储器_1  (
    .CS(1'b1), .Store(MemWrite), .CLK(CLK), .Address_Bus(\实验3_算术逻辑运算单元alu_1_result ),
    .Data_Bus_In(\实验3_mips寄存器文件_1_r_data2 ), .Load(1'b1), .Clear(1'b0),
    .Data_Bus_Out(\实验3_32位地址总线32位数据总线ram存储器_1_data_bus_out ));
  Multiplexer #(.select(1), .width(32), .disabled("Z"), .enable("false")) multiplexer_4 (
    .in0(\实验3_算术逻辑运算单元alu_1_result ), .in1(\实验3_32位地址总线32位数据总线ram存储器_1_data_bus_out ),
    .out(multiplexer_4_out), .sel(MemtoReg));
endmodule

module \ALU自动测试  (
  output [7:0] TEST_num
);

  wire ADD, AND, and_1_out, AND_prime, CLK, comparator_2_eq, HALT, Halt_t, multiplexer_1_out, nHalt, NotEQ,
       OR, OR_prime, priority_encoder_1_gs, Rok, SLT, SUB, X___Y, X___Y_t, X_AND_Y, X_AND_Y_prime, X_OR_Y,
       X_OR_Y_prime, X_Y, xnor_1_out, Zero, Zero_Standard, \悬空检测 ;
  wire [2:0] ALUOP;
  wire [3:0] \个位 , \十位 , \百位 ;
  wire [7:0] adder_1_out, \单项评分_1_总条数 , \单项评分_1_扣分 , \单项评分_1_正确条数 , \单项评分_2_总条数 , \单项评分_2_扣分 , \单项评分_2_正确条数 ,
       \单项评分_3_总条数 , \单项评分_3_扣分 , \单项评分_3_正确条数 , \单项评分_4_总条数 , \单项评分_4_扣分 , \单项评分_4_正确条数 , \单项评分_5_总条数 ,
       \单项评分_5_扣分 , \单项评分_5_正确条数 , \单项评分_6_总条数 , \单项评分_6_扣分 , \单项评分_6_正确条数 , \单项评分_7_总条数 , \单项评分_7_扣分 ,
       \单项评分_7_正确条数 , \单项评分_8_扣分 , \总项评分_1_总分 ;
  wire [9:0] counter_1_q;
  wire [31:0] bit_extender_1_out, R, R_Standard, X, Y;

  Register #(.width(8), .trigger("rising"), .Select("low")) register_1 (
    .D(adder_1_out), .en(nHalt), .Q(TEST_num), .clk(CLK));  // open: clr
  Clock #(.highDuration(1), .lowDuration(1)) clock_1 (.out(CLK));
  \单项评分  \u_单项评分_1  (
    .ALUOP(AND), .\扣分 (\单项评分_1_扣分 ), .\正确条数 (\单项评分_1_正确条数 ), .Rok(Rok), .nHalt(nHalt), .Right(X_AND_Y),
    .CLK(CLK), .\总条数 (\单项评分_1_总条数 ), .NotEQ(NotEQ));
  // Probe on \单项评分_1_总条数 
  // Probe on \单项评分_1_正确条数 
  // Probe on \单项评分_1_扣分 
  Adder #(.width(8)) adder_1 (.a(8'h1), .b(TEST_num), .out(adder_1_out));  // open: cin, cout
  not not_1 (nHalt, Halt_t);
  Comparator #(.width(3), .mode("twosComplement")) comparator_1 (.a(ALUOP), .b(3'b011), .eq(Halt_t));  // open: gt, lt
  Counter #(.width(10), .max('h3ff), .ongoal("wrap"), .trigger("rising"), .behavior("old")) counter_1 (
    .count(NotEQ), .Q(counter_1_q), .clk(CLK), .clr(Halt_t));  // open: load, D, carry, preset
  and and_1 (and_1_out, ~Halt_t, NotEQ);  // AND_Gate
  \单项评分  \u_单项评分_2  (
    .ALUOP(OR), .\扣分 (\单项评分_2_扣分 ), .\正确条数 (\单项评分_2_正确条数 ), .Rok(Rok), .nHalt(nHalt), .Right(X_OR_Y),
    .CLK(CLK), .\总条数 (\单项评分_2_总条数 ), .NotEQ(NotEQ));
  // Probe on \单项评分_2_总条数 
  // Probe on \单项评分_2_正确条数 
  // Probe on \单项评分_2_扣分 
  \总项评分  \u_总项评分_1  (
    .in_1(\单项评分_1_扣分 ), .in_2(\单项评分_2_扣分 ), .in_3(\单项评分_3_扣分 ), .in_4(\单项评分_4_扣分 ), .in_5(\单项评分_5_扣分 ),
    .in_6(\单项评分_6_扣分 ), .in_8(\单项评分_7_扣分 ), .in_9(\单项评分_8_扣分 ), .\总分 (\总项评分_1_总分 ), .\百位 (\百位 ), .\十位 (\十位 ),
    .\个位 (\个位 ), .\Zero悬空扣分 (\悬空检测 ));
  trace trace_1 (.in_1(TEST_num), .X(X), .Y(Y), .AluOP(ALUOP), .R(R_Standard), .Zero(Zero_Standard));
  \单项评分  \u_单项评分_3  (
    .ALUOP(ADD), .\扣分 (\单项评分_3_扣分 ), .\正确条数 (\单项评分_3_正确条数 ), .Rok(Rok), .nHalt(nHalt), .Right(X___Y),
    .CLK(CLK), .\总条数 (\单项评分_3_总条数 ), .NotEQ(NotEQ));
  // Probe on \单项评分_3_总条数 
  // Probe on \单项评分_3_正确条数 
  // Probe on \单项评分_3_扣分 
  RAM #(.addrWidth(10), .dataWidth(32), .bus("separate"), .Select("low")) ram_1 (
    .addr(counter_1_q), .din(X), .str(and_1_out), .clk(CLK));  // open: data, sel, ld, clr
  \单项评分  \u_单项评分_4  (
    .ALUOP(AND_prime), .\扣分 (\单项评分_4_扣分 ), .\正确条数 (\单项评分_4_正确条数 ), .Rok(Rok), .nHalt(nHalt),
    .Right(X_AND_Y_prime), .CLK(CLK), .\总条数 (\单项评分_4_总条数 ), .NotEQ(NotEQ));
  // Probe on \单项评分_4_总条数 
  // Probe on \单项评分_4_正确条数 
  // Probe on \单项评分_4_扣分 
  \单项评分  \u_单项评分_5  (
    .ALUOP(OR_prime), .\扣分 (\单项评分_5_扣分 ), .\正确条数 (\单项评分_5_正确条数 ), .Rok(Rok), .nHalt(nHalt),
    .Right(X_OR_Y_prime), .CLK(CLK), .\总条数 (\单项评分_5_总条数 ), .NotEQ(NotEQ));
  // Probe on \单项评分_5_总条数 
  // Probe on \单项评分_5_正确条数 
  // Probe on \单项评分_5_扣分 
  // Probe on \总项评分_1_总分 
  \实验3_算术逻辑运算单元ALU  \u_实验3_算术逻辑运算单元alu_1  (.AluOP(ALUOP), .X(X), .Result(R), .Y(Y), .\结果是否为0 (Zero));
  RAM #(.addrWidth(10), .dataWidth(32), .bus("separate"), .Select("low")) ram_2 (
    .addr(counter_1_q), .din(Y), .str(and_1_out), .clk(CLK));  // open: data, sel, ld, clr
  assign bit_extender_1_out = {{29{1'b0}}, ALUOP};  // Bit_Extender bit_extender_1
  \单项评分  \u_单项评分_6  (
    .ALUOP(SUB), .\扣分 (\单项评分_6_扣分 ), .\正确条数 (\单项评分_6_正确条数 ), .Rok(Rok), .nHalt(nHalt), .Right(X___Y_t),
    .CLK(CLK), .\总条数 (\单项评分_6_总条数 ), .NotEQ(NotEQ));
  // Probe on \单项评分_6_总条数 
  // Probe on \单项评分_7_总条数 
  // Probe on \单项评分_6_正确条数 
  // Probe on \单项评分_6_扣分 
  \单项评分  \u_单项评分_7  (
    .ALUOP(SLT), .\扣分 (\单项评分_7_扣分 ), .\正确条数 (\单项评分_7_正确条数 ), .Rok(Rok), .nHalt(nHalt), .Right(X_Y),
    .CLK(CLK), .\总条数 (\单项评分_7_总条数 ), .NotEQ(NotEQ));
  // Probe on \单项评分_7_正确条数 
  // Probe on \单项评分_7_扣分 
  // Probe on ALUOP
  \单项评分  \u_单项评分_8  (
    .ALUOP(1'b0), .\扣分 (\单项评分_8_扣分 ), .Rok(Rok), .nHalt(nHalt), .CLK(CLK), .NotEQ(NotEQ));  // open: 正确条数, Right, 总条数
  RAM #(.addrWidth(10), .dataWidth(32), .bus("separate"), .Select("low")) ram_3 (
    .addr(counter_1_q), .din(bit_extender_1_out), .str(and_1_out), .clk(CLK));  // open: data, sel, ld, clr
  Decoder #(.select(3), .tristate("false"), .disabled("Z"), .enable("false")) decoder_1 (
    .out0(AND), .out1(OR), .out2(ADD), .out3(HALT), .out4(AND_prime), .out5(OR_prime), .out6(SUB),
    .out7(SLT), .sel(ALUOP));
  Multiplexer #(.select(1), .width(1), .disabled("Z"), .enable("false")) multiplexer_1 (
    .in0(1'b1), .in1(1'b1), .out(multiplexer_1_out), .sel(Zero));
  xnor xnor_1 (xnor_1_out, Zero_Standard, Zero);
  Comparator #(.width(32), .mode("twosComplement")) comparator_2 (
    .a(R_Standard), .b(R), .eq(comparator_2_eq));  // open: gt, lt
  LED #(.active("false")) led_1 (.in(X_AND_Y));
  LED #(.active("false")) led_2 (.in(X_OR_Y));
  LED #(.active("false")) led_3 (.in(X___Y));
  LED #(.active("false")) led_4 (.in(X_AND_Y_prime));
  LED #(.active("false")) led_5 (.in(X_OR_Y_prime));
  LED #(.active("false")) led_6 (.in(X___Y_t));
  LED #(.active("false")) led_7 (.in(X_Y));
  LED #(.active("true")) led_8 (.in(NotEQ));
  Priority_Encoder #(.select(1), .disabled("Z")) priority_encoder_1 (
    .in0(multiplexer_1_out), .in1(multiplexer_1_out), .gs(priority_encoder_1_gs));  // open: out, en_out, en_in
  not not_2 (\悬空检测 , priority_encoder_1_gs);
  nand nand_1 (NotEQ, xnor_1_out, Rok);
  Priority_Encoder #(.select(1), .disabled("Z")) priority_encoder_2 (
    .in0(comparator_2_eq), .in1(comparator_2_eq), .gs(Rok));  // open: out, en_out, en_in
  Hex_Digit_Display hex_digit_display_1 (.value(\百位 ));  // open: dp
  Hex_Digit_Display hex_digit_display_2 (.value(\十位 ));  // open: dp
  Hex_Digit_Display hex_digit_display_3 (.value(\个位 ));  // open: dp

  // Notes on the sheet:
  //   X 错误记录
  //   Y 错误记录
  //   ALUOP 错误记录
  //   运算故障指示
  //   红色异常
  //   成绩
endmodule

module trace (
  input  [7:0] in_1,
  output [31:0] X,
  output [31:0] Y,
  output [2:0] AluOP,
  output [31:0] R,
  output Zero
);

  ROM #(.addrWidth(8), .dataWidth(32), .Select("high")) rom_1 (.addr(in_1), .data(X));
  ROM #(.addrWidth(8), .dataWidth(32), .Select("high")) rom_2 (.addr(in_1), .data(Y));
  ROM #(.addrWidth(8), .dataWidth(3), .Select("high")) rom_3 (.addr(in_1), .data(AluOP));
  ROM #(.addrWidth(8), .dataWidth(32), .Select("high")) rom_4 (.addr(in_1), .data(R));
  ROM #(.addrWidth(8), .dataWidth(1), .Select("high")) rom_5 (.addr(in_1), .data(Zero));

  // Notes on the sheet:
  //   X trace
  //   contents of rom_1 (hex, n*v repeats v):
  //   1 1 1 0 11111111 0 0 0 10b67f2
  //   Y trace
  //   contents of rom_2 (hex, n*v repeats v):
  //   1 0 1 4*0 1 2f5a0df4
  //   ALU OP Trace
  //   contents of rom_3 (hex, n*v repeats v):
  //   0 1 2 0 4 5 6 7 2
  //   Result
  //   contents of rom_4 (hex, n*v repeats v):
  //   1 1 2 0 11111111 ffffffff 0 1 306575e6
  //   Zero Flag
  //   contents of rom_5 (hex, n*v repeats v):
  //   0 0 0 1 0 0 1 0 0 247*1
endmodule

module \单项评分  (
  input  ALUOP,
  input  NotEQ,
  input  Rok,
  input  nHalt,
  input  CLK,
  output [7:0] \扣分 ,
  output [7:0] \正确条数 ,
  output Right,
  output [7:0] \总条数 
);

  wire and_1_out, and_2_out, and_3_out, and_4_out, comparator_1_eq, not_1_out, not_2_out, not_3_out,
       undriven, undriven_2, undriven_3, undriven_4;
  wire [7:0] counter_1_q, counter_2_q, multiplexer_1_out;

  not not_1 (not_1_out, NotEQ);
  and and_1 (and_1_out, undriven, undriven_2, undriven_3);
  and and_2 (and_2_out, undriven, undriven_3);
  and and_3 (and_3_out, ALUOP, not_1_out, Rok, nHalt);
  and and_4 (and_4_out, ALUOP, nHalt);
  Counter #(.width(8), .max('hff), .ongoal("wrap"), .trigger("rising"), .behavior("new")) counter_1 (
    .Q(counter_1_q), .clk(undriven_4), .down(and_1_out));  // open: load, D, count, carry, clr, preset
  Counter #(.width(8), .max('hff), .ongoal("wrap"), .trigger("rising"), .behavior("new")) counter_2 (
    .Q(counter_2_q), .down(and_2_out));  // open: load, D, count, carry, clk, clr, preset
  Counter #(.width(8), .max('hff), .ongoal("wrap"), .trigger("rising"), .behavior("old")) counter_3 (
    .count(and_3_out), .Q(\正确条数 ), .clk(CLK));  // open: load, D, carry, clr, preset
  Counter #(.width(8), .max('hff), .ongoal("wrap"), .trigger("rising"), .behavior("old")) counter_4 (
    .count(and_4_out), .Q(\总条数 ), .clk(CLK));  // open: load, D, carry, clr, preset
  Comparator #(.width(8), .mode("twosComplement")) comparator_1 (
    .a(counter_1_q), .b(counter_2_q), .eq(comparator_1_eq));  // open: gt, lt
  Comparator #(.width(8), .mode("twosComplement")) comparator_2 (.a(\正确条数 ), .b(\总条数 ), .eq(Right));  // open: gt, lt
  Multiplexer #(.select(1), .width(8), .disabled("Z"), .enable("false")) multiplexer_1 (
    .in0({8{1'b0}}), .in1(8'h5), .out(multiplexer_1_out), .sel(not_2_out));
  not not_2 (not_2_out, comparator_1_eq);
  not not_3 (not_3_out, Right);
  Multiplexer #(.select(1), .width(8), .disabled("Z"), .enable("false")) multiplexer_2 (
    .in0({8{1'b0}}), .in1(8'h5), .out(\扣分 ), .sel(not_3_out));

  // Notes on the sheet:
  //   ALUOP
  //   Rok
  //   ~Halt
  //   CLK
  //   Duplicated
  //   总条数
  //   正确条数
  //   扣分
  //   Right？
endmodule

module \总项评分  (
  input  [7:0] in_1,
  input  [7:0] in_2,
  input  [7:0] in_3,
  input  [7:0] in_4,
  input  [7:0] in_5,
  input  [7:0] in_6,
  input  \Zero悬空扣分 ,
  input  [7:0] in_8,
  input  [7:0] in_9,
  output [7:0] \总分 ,
  output [3:0] \百位 ,
  output [3:0] \十位 ,
  output [3:0] \个位 
);

  wire [7:0] adder_1_out, adder_2_out, adder_3_out, adder_4_out, adder_5_out, adder_6_out, adder_7_out,
       divider_1_out, subtractor_1_out, subtractor_2_out;
  wire [7:4] divider_1_rem, divider_2_out, divider_2_rem;

  Adder #(.width(8)) adder_1 (.a(in_1), .b(in_2), .out(adder_1_out));  // open: cin, cout
  Adder #(.width(8)) adder_2 (.a(in_3), .b(in_4), .out(adder_2_out));  // open: cin, cout
  Adder #(.width(8)) adder_3 (.a(in_5), .b(in_6), .out(adder_3_out));  // open: cin, cout
  Adder #(.width(8)) adder_4 (.a(in_8), .b(in_9), .out(adder_4_out));  // open: cin, cout
  Adder #(.width(8)) adder_5 (.a(adder_1_out), .b(adder_2_out), .out(adder_5_out));  // open: cin, cout
  Adder #(.width(8)) adder_6 (.a(adder_3_out), .b(adder_4_out), .out(adder_6_out));  // open: cin, cout
  Adder #(.width(8)) adder_7 (.a(adder_5_out), .b(adder_6_out), .out(adder_7_out));  // open: cin, cout
  Subtractor #(.width(8)) subtractor_1 (.a(8'h64), .b(adder_7_out), .out(subtractor_1_out));  // open: bin, bout
  Subtractor #(.width(8)) subtractor_2 (.a(subtractor_1_out), .b(8'h5), .out(subtractor_2_out));  // open: bin, bout
  Multiplexer #(.select(1), .width(8), .disabled("Z"), .enable("false")) multiplexer_1 (
    .in0(subtractor_1_out), .in1(subtractor_2_out), .out(\总分 ), .sel(\Zero悬空扣分 ));
  Divider #(.width(8)) divider_1 (.a(\总分 ), .b(8'ha), .out(divider_1_out), .rem({divider_1_rem, \个位 }));  // open: upper
  Divider #(.width(8)) divider_2 (
    .a(divider_1_out), .b(8'ha), .out({divider_2_out, \百位 }), .rem({divider_2_rem, \十位 }));  // open: upper
endmodule

module \平时作业1_全加器子电路  (
  input  x,
  input  y,
  input  Cin,
  output Carry,
  output sum
);

  wire and_1_out, and_2_out, and_3_out, and_4_out, and_5_out, and_6_out, and_7_out, not_1_out, not_2_out,
       not_3_out, not_4_out, not_5_out, not_6_out;

  and and_1 (and_1_out, y, Cin);
  and and_2 (and_2_out, x, Cin);
  and and_3 (and_3_out, x, y);
  not not_1 (not_1_out, x);
  not not_2 (not_2_out, y);
  not not_3 (not_3_out, x);
  not not_4 (not_4_out, Cin);
  not not_5 (not_5_out, y);
  not not_6 (not_6_out, Cin);
  or or_1 (Carry, and_1_out, and_2_out, and_3_out);
  and and_4 (and_4_out, not_1_out, not_2_out, Cin);
  and and_5 (and_5_out, not_3_out, y, not_4_out);
  and and_6 (and_6_out, x, not_5_out, not_6_out);
  and and_7 (and_7_out, x, y, Cin);
  or or_2 (sum, and_4_out, and_5_out, and_6_out, and_7_out);
endmodule

module \平时作业1_溢出判断  (
  input  Sa,
  input  Sb,
  input  Sf,
  output Overflow
);

  wire and_1_out, and_2_out, not_1_out, not_2_out, not_3_out;

  not not_1 (not_1_out, Sa);
  not not_2 (not_2_out, Sb);
  not not_3 (not_3_out, Sf);
  and and_1 (and_1_out, not_1_out, not_2_out, Sf);
  and and_2 (and_2_out, Sa, Sb, not_3_out);
  or or_1 (Overflow, and_1_out, and_2_out);
endmodule

module \平时作业1_带有溢出判断和进位输出的4_bit加法器  (
  input  [3:0] in_1,
  input  [3:0] in_2,
  output Overflow,
  output [3:0] out_4
);

  wire \平时作业1_全加器子电路_2_carry , \平时作业1_全加器子电路_3_carry , \平时作业1_全加器子电路_4_carry ;

  // Probe on in_1
  // Probe on in_2
  \平时作业1_全加器子电路  \u_平时作业1_全加器子电路_1  (
    .x(in_1[3]), .y(in_2[3]), .Cin(\平时作业1_全加器子电路_2_carry ), .Carry(Overflow), .sum(out_4[3]));
  // Probe on out_4
  \平时作业1_全加器子电路  \u_平时作业1_全加器子电路_2  (
    .x(in_1[2]), .y(in_2[2]), .Cin(\平时作业1_全加器子电路_3_carry ), .Carry(\平时作业1_全加器子电路_2_carry ), .sum(out_4[2]));
  \平时作业1_全加器子电路  \u_平时作业1_全加器子电路_3  (
    .x(in_1[1]), .y(in_2[1]), .Cin(\平时作业1_全加器子电路_4_carry ), .Carry(\平时作业1_全加器子电路_3_carry ), .sum(out_4[1]));
  \平时作业1_全加器子电路  \u_平时作业1_全加器子电路_4  (
    .x(in_1[0]), .y(in_2[0]), .Cin(1'b0), .Carry(\平时作业1_全加器子电路_4_carry ), .sum(out_4[0]));

  // Notes on the sheet:
  //   带有溢出判断和进位输出的4-bit加法器
endmodule

module \平时作业1_带有溢出判断和进位输出的4_bit有符号数的补码加法器1  (
  input  [3:0] in_1,
  input  [3:0] in_2,
  output Overflow,
  output [3:0] out_4
);

  wire \平时作业1_全加器子电路_2_carry , \平时作业1_全加器子电路_3_carry , \平时作业1_全加器子电路_4_carry ;

  \平时作业1_溢出判断  \u_平时作业1_溢出判断_1  (.Sa(in_1[3]), .Sb(in_2[3]), .Sf(\平时作业1_全加器子电路_2_carry ), .Overflow(Overflow));
  // Probe on in_1
  // Probe on in_2
  // Probe on out_4
  \平时作业1_全加器子电路  \u_平时作业1_全加器子电路_1  (
    .x(in_1[3]), .y(in_2[3]), .Cin(\平时作业1_全加器子电路_2_carry ), .sum(out_4[3]));  // open: Carry
  \平时作业1_全加器子电路  \u_平时作业1_全加器子电路_2  (
    .x(in_1[2]), .y(in_2[2]), .Cin(\平时作业1_全加器子电路_3_carry ), .Carry(\平时作业1_全加器子电路_2_carry ), .sum(out_4[2]));
  \平时作业1_全加器子电路  \u_平时作业1_全加器子电路_3  (
    .x(in_1[1]), .y(in_2[1]), .Cin(\平时作业1_全加器子电路_4_carry ), .Carry(\平时作业1_全加器子电路_3_carry ), .sum(out_4[1]));
  \平时作业1_全加器子电路  \u_平时作业1_全加器子电路_4  (
    .x(in_1[0]), .y(in_2[0]), .Cin(1'b0), .Carry(\平时作业1_全加器子电路_4_carry ), .sum(out_4[0]));

  // Notes on the sheet:
  //   带有溢出判断和进位输出的4-bit有符号数的补码加法器
  //   第一种
endmodule
module \平时作业1_带有溢出判断和进位输出的4_bit有符号数的补码加法器2  (
  input  [3:0] in_1,
  input  [3:0] in_2,
  output Overflow,
  output [3:0] out_4
);

  wire \平时作业1_全加器子电路_1_carry , \平时作业1_全加器子电路_2_carry , \平时作业1_全加器子电路_3_carry , \平时作业1_全加器子电路_4_carry ;

  xor xor_1 (Overflow, \平时作业1_全加器子电路_1_carry , \平时作业1_全加器子电路_2_carry );
  // Probe on out_4
  // Probe on in_1
  // Probe on in_2
  \平时作业1_全加器子电路  \u_平时作业1_全加器子电路_1  (
    .x(in_1[3]), .y(in_2[3]), .Cin(\平时作业1_全加器子电路_2_carry ), .Carry(\平时作业1_全加器子电路_1_carry ), .sum(out_4[3]));
  \平时作业1_全加器子电路  \u_平时作业1_全加器子电路_2  (
    .x(in_1[2]), .y(in_2[2]), .Cin(\平时作业1_全加器子电路_3_carry ), .Carry(\平时作业1_全加器子电路_2_carry ), .sum(out_4[2]));
  \平时作业1_全加器子电路  \u_平时作业1_全加器子电路_3  (
    .x(in_1[1]), .y(in_2[1]), .Cin(\平时作业1_全加器子电路_4_carry ), .Carry(\平时作业1_全加器子电路_3_carry ), .sum(out_4[1]));
  \平时作业1_全加器子电路  \u_平时作业1_全加器子电路_4  (
    .x(in_1[0]), .y(in_2[0]), .Cin(1'b0), .Carry(\平时作业1_全加器子电路_4_carry ), .sum(out_4[0]));

  // Notes on the sheet:
  //   第二种：异或
endmodule

module \平时作业1_带有溢出判断和进位输出的4_bit有符号数的补码加法器3  (
  input  [3:0] in_1,
  input  [3:0] in_2,
  output Overflow,
  output [3:0] out_4
);

  wire \平时作业1_全加器子电路_1_sum , \平时作业1_全加器子电路_2_carry , \平时作业1_全加器子电路_3_carry , \平时作业1_全加器子电路_4_carry ,
       \平时作业1_全加器子电路_5_carry ;

  xor xor_1 (Overflow, \平时作业1_全加器子电路_1_sum , \平时作业1_全加器子电路_3_carry );
  \平时作业1_全加器子电路  \u_平时作业1_全加器子电路_1  (
    .x(in_2[3]), .y(in_1[3]), .Cin(\平时作业1_全加器子电路_2_carry ), .sum(\平时作业1_全加器子电路_1_sum ));  // open: Carry
  // Probe on in_1
  // Probe on in_2
  // Probe on out_4
  \平时作业1_全加器子电路  \u_平时作业1_全加器子电路_2  (
    .x(in_1[3]), .y(in_2[3]), .Cin(\平时作业1_全加器子电路_3_carry ), .Carry(\平时作业1_全加器子电路_2_carry ), .sum(out_4[3]));
  \平时作业1_全加器子电路  \u_平时作业1_全加器子电路_3  (
    .x(in_1[2]), .y(in_2[2]), .Cin(\平时作业1_全加器子电路_4_carry ), .Carry(\平时作业1_全加器子电路_3_carry ), .sum(out_4[2]));
  \平时作业1_全加器子电路  \u_平时作业1_全加器子电路_4  (
    .x(in_1[1]), .y(in_2[1]), .Cin(\平时作业1_全加器子电路_5_carry ), .Carry(\平时作业1_全加器子电路_4_carry ), .sum(out_4[1]));
  \平时作业1_全加器子电路  \u_平时作业1_全加器子电路_5  (
    .x(in_1[0]), .y(in_2[0]), .Cin(1'b0), .Carry(\平时作业1_全加器子电路_5_carry ), .sum(out_4[0]));

  // Notes on the sheet:
  //   第三种：双符号位
endmodule

module \平时作业2_红绿灯1  (
  input  First,
  input  Second,
  input  Third,
  output Red,
  output Yellow,
  output Green,
  output Second_Out,
  output Third_Out
);

  wire not_1_out, not_2_out, not_3_out;

  not not_1 (not_1_out, Second);
  not not_2 (not_2_out, Second);
  not not_3 (not_3_out, Third);
  and and_1 (Yellow, not_1_out, Third);
  and and_2 (Green, not_2_out, not_3_out);

  assign Red = Second;
  assign Second_Out = First;
  assign Third_Out = Second;

  // Notes on the sheet:
  //   不管第一段有没有车通过，都有灯亮起
endmodule

module \平时作业2_红绿灯2  (
  input  First,
  input  Second,
  input  Third
);

  wire and_1_out, and_2_out, and_3_out, not_1_out, not_2_out, not_3_out;

  and and_1 (and_1_out, First, Second);
  not not_1 (not_1_out, Second);
  not not_2 (not_2_out, Second);
  not not_3 (not_3_out, Third);
  LED #(.active("true")) led_1 (.in(and_1_out));
  LED #(.active("true")) led_2 (.in(and_2_out));
  and and_2 (and_2_out, First, not_1_out, Third);
  and and_3 (and_3_out, First, not_2_out, not_3_out);
  LED #(.active("true")) led_3 (.in(and_3_out));

  // Notes on the sheet:
  //   只有第一段有车通过，才会亮灯
endmodule

module \平时作业2_多段铁路红绿灯连接  (
  input  in_1,
  input  in_2,
  input  in_3,
  output out_4,
  output out_5
);

  wire \平时作业2_红绿灯1_1_green , \平时作业2_红绿灯1_1_red , \平时作业2_红绿灯1_1_second_out , \平时作业2_红绿灯1_1_third_out ,
       \平时作业2_红绿灯1_1_yellow , \平时作业2_红绿灯1_2_green , \平时作业2_红绿灯1_2_red , \平时作业2_红绿灯1_2_second_out ,
       \平时作业2_红绿灯1_2_third_out , \平时作业2_红绿灯1_2_yellow , \平时作业2_红绿灯1_3_green , \平时作业2_红绿灯1_3_red ,
       \平时作业2_红绿灯1_3_yellow ;

  \平时作业2_红绿灯1  \u_平时作业2_红绿灯1_1  (
    .First(in_1), .Second(1'b0), .Third(1'b0), .Red(\平时作业2_红绿灯1_1_red ), .Yellow(\平时作业2_红绿灯1_1_yellow ),
    .Green(\平时作业2_红绿灯1_1_green ), .Second_Out(\平时作业2_红绿灯1_1_second_out ), .Third_Out(\平时作业2_红绿灯1_1_third_out ));
  \平时作业2_红绿灯1  \u_平时作业2_红绿灯1_2  (
    .First(in_2), .Second(\平时作业2_红绿灯1_1_second_out ), .Third(\平时作业2_红绿灯1_1_third_out ),
    .Red(\平时作业2_红绿灯1_2_red ), .Yellow(\平时作业2_红绿灯1_2_yellow ), .Green(\平时作业2_红绿灯1_2_green ),
    .Second_Out(\平时作业2_红绿灯1_2_second_out ), .Third_Out(\平时作业2_红绿灯1_2_third_out ));
  \平时作业2_红绿灯1  \u_平时作业2_红绿灯1_3  (
    .First(in_3), .Second(\平时作业2_红绿灯1_2_second_out ), .Third(\平时作业2_红绿灯1_2_third_out ),
    .Red(\平时作业2_红绿灯1_3_red ), .Yellow(\平时作业2_红绿灯1_3_yellow ), .Green(\平时作业2_红绿灯1_3_green ),
    .Second_Out(out_4), .Third_Out(out_5));
  LED #(.active("true")) led_1 (.in(\平时作业2_红绿灯1_1_red ));
  LED #(.active("true")) led_2 (.in(\平时作业2_红绿灯1_1_yellow ));
  LED #(.active("true")) led_3 (.in(\平时作业2_红绿灯1_1_green ));
  LED #(.active("true")) led_4 (.in(\平时作业2_红绿灯1_2_red ));
  LED #(.active("true")) led_5 (.in(\平时作业2_红绿灯1_2_yellow ));
  LED #(.active("true")) led_6 (.in(\平时作业2_红绿灯1_2_green ));
  LED #(.active("true")) led_7 (.in(\平时作业2_红绿灯1_3_red ));
  LED #(.active("true")) led_8 (.in(\平时作业2_红绿灯1_3_yellow ));
  LED #(.active("true")) led_9 (.in(\平时作业2_红绿灯1_3_green ));

  // Notes on the sheet:
  //   第 i+1 段
  //   第 i 段
  //   第 i-1 段
endmodule

module \平时作业2_28段轨道的红绿灯  (
  input  in_1,
  input  in_2,
  input  in_3,
  input  in_4,
  input  in_5,
  input  in_6,
  input  in_7,
  input  in_8,
  input  in_9,
  input  in_10,
  input  in_11,
  input  in_12,
  input  in_13,
  input  in_14,
  input  in_15,
  input  in_16,
  input  in_17,
  input  in_18,
  input  in_19,
  input  in_20,
  input  in_21,
  input  in_22,
  input  in_23,
  input  in_24,
  input  in_25,
  input  in_26,
  input  in_27,
  input  in_28,
  output out_29,
  output out_30
);

  wire \平时作业2_红绿灯1_1_green , \平时作业2_红绿灯1_1_red , \平时作业2_红绿灯1_1_second_out , \平时作业2_红绿灯1_1_third_out ,
       \平时作业2_红绿灯1_1_yellow , \平时作业2_红绿灯1_2_green , \平时作业2_红绿灯1_2_red , \平时作业2_红绿灯1_2_second_out ,
       \平时作业2_红绿灯1_2_third_out , \平时作业2_红绿灯1_2_yellow , \平时作业2_红绿灯1_3_green , \平时作业2_红绿灯1_3_red ,
       \平时作业2_红绿灯1_3_second_out , \平时作业2_红绿灯1_3_third_out , \平时作业2_红绿灯1_3_yellow , \平时作业2_红绿灯1_4_green ,
       \平时作业2_红绿灯1_4_red , \平时作业2_红绿灯1_4_second_out , \平时作业2_红绿灯1_4_third_out , \平时作业2_红绿灯1_4_yellow ,
       \平时作业2_红绿灯1_5_green , \平时作业2_红绿灯1_5_red , \平时作业2_红绿灯1_5_second_out , \平时作业2_红绿灯1_5_third_out ,
       \平时作业2_红绿灯1_5_yellow , \平时作业2_红绿灯1_6_green , \平时作业2_红绿灯1_6_red , \平时作业2_红绿灯1_6_second_out ,
       \平时作业2_红绿灯1_6_third_out , \平时作业2_红绿灯1_6_yellow , \平时作业2_红绿灯1_7_green , \平时作业2_红绿灯1_7_red ,
       \平时作业2_红绿灯1_7_second_out , \平时作业2_红绿灯1_7_third_out , \平时作业2_红绿灯1_7_yellow , \平时作业2_红绿灯1_8_green ,
       \平时作业2_红绿灯1_8_red , \平时作业2_红绿灯1_8_second_out , \平时作业2_红绿灯1_8_third_out , \平时作业2_红绿灯1_8_yellow ,
       \平时作业2_红绿灯1_9_green , \平时作业2_红绿灯1_9_red , \平时作业2_红绿灯1_9_second_out , \平时作业2_红绿灯1_9_third_out ,
       \平时作业2_红绿灯1_9_yellow , \平时作业2_红绿灯1_10_green , \平时作业2_红绿灯1_10_red , \平时作业2_红绿灯1_10_second_out ,
       \平时作业2_红绿灯1_10_third_out , \平时作业2_红绿灯1_10_yellow , \平时作业2_红绿灯1_11_green , \平时作业2_红绿灯1_11_red ,
       \平时作业2_红绿灯1_11_second_out , \平时作业2_红绿灯1_11_third_out , \平时作业2_红绿灯1_11_yellow , \平时作业2_红绿灯1_12_green ,
       \平时作业2_红绿灯1_12_red , \平时作业2_红绿灯1_12_second_out , \平时作业2_红绿灯1_12_third_out , \平时作业2_红绿灯1_12_yellow ,
       \平时作业2_红绿灯1_13_green , \平时作业2_红绿灯1_13_red , \平时作业2_红绿灯1_13_second_out , \平时作业2_红绿灯1_13_third_out ,
       \平时作业2_红绿灯1_13_yellow , \平时作业2_红绿灯1_14_green , \平时作业2_红绿灯1_14_red , \平时作业2_红绿灯1_14_second_out ,
       \平时作业2_红绿灯1_14_third_out , \平时作业2_红绿灯1_14_yellow , \平时作业2_红绿灯1_15_green , \平时作业2_红绿灯1_15_red ,
       \平时作业2_红绿灯1_15_second_out , \平时作业2_红绿灯1_15_third_out , \平时作业2_红绿灯1_15_yellow , \平时作业2_红绿灯1_16_green ,
       \平时作业2_红绿灯1_16_red , \平时作业2_红绿灯1_16_second_out , \平时作业2_红绿灯1_16_third_out , \平时作业2_红绿灯1_16_yellow ,
       \平时作业2_红绿灯1_17_green , \平时作业2_红绿灯1_17_red , \平时作业2_红绿灯1_17_second_out , \平时作业2_红绿灯1_17_third_out ,
       \平时作业2_红绿灯1_17_yellow , \平时作业2_红绿灯1_18_green , \平时作业2_红绿灯1_18_red , \平时作业2_红绿灯1_18_second_out ,
       \平时作业2_红绿灯1_18_third_out , \平时作业2_红绿灯1_18_yellow , \平时作业2_红绿灯1_19_green , \平时作业2_红绿灯1_19_red ,
       \平时作业2_红绿灯1_19_second_out , \平时作业2_红绿灯1_19_third_out , \平时作业2_红绿灯1_19_yellow , \平时作业2_红绿灯1_20_green ,
       \平时作业2_红绿灯1_20_red , \平时作业2_红绿灯1_20_second_out , \平时作业2_红绿灯1_20_third_out , \平时作业2_红绿灯1_20_yellow ,
       \平时作业2_红绿灯1_21_green , \平时作业2_红绿灯1_21_red , \平时作业2_红绿灯1_21_second_out , \平时作业2_红绿灯1_21_third_out ,
       \平时作业2_红绿灯1_21_yellow , \平时作业2_红绿灯1_22_green , \平时作业2_红绿灯1_22_red , \平时作业2_红绿灯1_22_second_out ,
       \平时作业2_红绿灯1_22_third_out , \平时作业2_红绿灯1_22_yellow , \平时作业2_红绿灯1_23_green , \平时作业2_红绿灯1_23_red ,
       \平时作业2_红绿灯1_23_second_out , \平时作业2_红绿灯1_23_third_out , \平时作业2_红绿灯1_23_yellow , \平时作业2_红绿灯1_24_green ,
       \平时作业2_红绿灯1_24_red , \平时作业2_红绿灯1_24_second_out , \平时作业2_红绿灯1_24_third_out , \平时作业2_红绿灯1_24_yellow ,
       \平时作业2_红绿灯1_25_green , \平时作业2_红绿灯1_25_red , \平时作业2_红绿灯1_25_second_out , \平时作业2_红绿灯1_25_third_out ,
       \平时作业2_红绿灯1_25_yellow , \平时作业2_红绿灯1_26_green , \平时作业2_红绿灯1_26_red , \平时作业2_红绿灯1_26_second_out ,
       \平时作业2_红绿灯1_26_third_out , \平时作业2_红绿灯1_26_yellow , \平时作业2_红绿灯1_27_green , \平时作业2_红绿灯1_27_red ,
       \平时作业2_红绿灯1_27_second_out , \平时作业2_红绿灯1_27_third_out , \平时作业2_红绿灯1_27_yellow , \平时作业2_红绿灯1_28_green ,
       \平时作业2_红绿灯1_28_red , \平时作业2_红绿灯1_28_yellow ;

  \平时作业2_红绿灯1  \u_平时作业2_红绿灯1_1  (
    .First(in_1), .Second(1'b0), .Third(1'b0), .Red(\平时作业2_红绿灯1_1_red ), .Yellow(\平时作业2_红绿灯1_1_yellow ),
    .Green(\平时作业2_红绿灯1_1_green ), .Second_Out(\平时作业2_红绿灯1_1_second_out ), .Third_Out(\平时作业2_红绿灯1_1_third_out ));
  \平时作业2_红绿灯1  \u_平时作业2_红绿灯1_2  (
    .First(in_2), .Second(\平时作业2_红绿灯1_1_second_out ), .Third(\平时作业2_红绿灯1_1_third_out ),
    .Red(\平时作业2_红绿灯1_2_red ), .Yellow(\平时作业2_红绿灯1_2_yellow ), .Green(\平时作业2_红绿灯1_2_green ),
    .Second_Out(\平时作业2_红绿灯1_2_second_out ), .Third_Out(\平时作业2_红绿灯1_2_third_out ));
  \平时作业2_红绿灯1  \u_平时作业2_红绿灯1_3  (
    .First(in_3), .Second(\平时作业2_红绿灯1_2_second_out ), .Third(\平时作业2_红绿灯1_2_third_out ),
    .Red(\平时作业2_红绿灯1_3_red ), .Yellow(\平时作业2_红绿灯1_3_yellow ), .Green(\平时作业2_红绿灯1_3_green ),
    .Second_Out(\平时作业2_红绿灯1_3_second_out ), .Third_Out(\平时作业2_红绿灯1_3_third_out ));
  \平时作业2_红绿灯1  \u_平时作业2_红绿灯1_4  (
    .First(in_4), .Second(\平时作业2_红绿灯1_3_second_out ), .Third(\平时作业2_红绿灯1_3_third_out ),
    .Red(\平时作业2_红绿灯1_4_red ), .Yellow(\平时作业2_红绿灯1_4_yellow ), .Green(\平时作业2_红绿灯1_4_green ),
    .Second_Out(\平时作业2_红绿灯1_4_second_out ), .Third_Out(\平时作业2_红绿灯1_4_third_out ));
  \平时作业2_红绿灯1  \u_平时作业2_红绿灯1_5  (
    .First(in_5), .Second(\平时作业2_红绿灯1_4_second_out ), .Third(\平时作业2_红绿灯1_4_third_out ),
    .Red(\平时作业2_红绿灯1_5_red ), .Yellow(\平时作业2_红绿灯1_5_yellow ), .Green(\平时作业2_红绿灯1_5_green ),
    .Second_Out(\平时作业2_红绿灯1_5_second_out ), .Third_Out(\平时作业2_红绿灯1_5_third_out ));
  \平时作业2_红绿灯1  \u_平时作业2_红绿灯1_6  (
    .First(in_6), .Second(\平时作业2_红绿灯1_5_second_out ), .Third(\平时作业2_红绿灯1_5_third_out ),
    .Red(\平时作业2_红绿灯1_6_red ), .Yellow(\平时作业2_红绿灯1_6_yellow ), .Green(\平时作业2_红绿灯1_6_green ),
    .Second_Out(\平时作业2_红绿灯1_6_second_out ), .Third_Out(\平时作业2_红绿灯1_6_third_out ));
  \平时作业2_红绿灯1  \u_平时作业2_红绿灯1_7  (
    .First(in_7), .Second(\平时作业2_红绿灯1_6_second_out ), .Third(\平时作业2_红绿灯1_6_third_out ),
    .Red(\平时作业2_红绿灯1_7_red ), .Yellow(\平时作业2_红绿灯1_7_yellow ), .Green(\平时作业2_红绿灯1_7_green ),
    .Second_Out(\平时作业2_红绿灯1_7_second_out ), .Third_Out(\平时作业2_红绿灯1_7_third_out ));
  \平时作业2_红绿灯1  \u_平时作业2_红绿灯1_8  (
    .First(in_8), .Second(\平时作业2_红绿灯1_7_second_out ), .Third(\平时作业2_红绿灯1_7_third_out ),
    .Red(\平时作业2_红绿灯1_8_red ), .Yellow(\平时作业2_红绿灯1_8_yellow ), .Green(\平时作业2_红绿灯1_8_green ),
    .Second_Out(\平时作业2_红绿灯1_8_second_out ), .Third_Out(\平时作业2_红绿灯1_8_third_out ));
  \平时作业2_红绿灯1  \u_平时作业2_红绿灯1_9  (
    .First(in_9), .Second(\平时作业2_红绿灯1_8_second_out ), .Third(\平时作业2_红绿灯1_8_third_out ),
    .Red(\平时作业2_红绿灯1_9_red ), .Yellow(\平时作业2_红绿灯1_9_yellow ), .Green(\平时作业2_红绿灯1_9_green ),
    .Second_Out(\平时作业2_红绿灯1_9_second_out ), .Third_Out(\平时作业2_红绿灯1_9_third_out ));
  \平时作业2_红绿灯1  \u_平时作业2_红绿灯1_10  (
    .First(in_10), .Second(\平时作业2_红绿灯1_9_second_out ), .Third(\平时作业2_红绿灯1_9_third_out ),
    .Red(\平时作业2_红绿灯1_10_red ), .Yellow(\平时作业2_红绿灯1_10_yellow ), .Green(\平时作业2_红绿灯1_10_green ),
    .Second_Out(\平时作业2_红绿灯1_10_second_out ), .Third_Out(\平时作业2_红绿灯1_10_third_out ));
  \平时作业2_红绿灯1  \u_平时作业2_红绿灯1_11  (
    .First(in_11), .Second(\平时作业2_红绿灯1_10_second_out ), .Third(\平时作业2_红绿灯1_10_third_out ),
    .Red(\平时作业2_红绿灯1_11_red ), .Yellow(\平时作业2_红绿灯1_11_yellow ), .Green(\平时作业2_红绿灯1_11_green ),
    .Second_Out(\平时作业2_红绿灯1_11_second_out ), .Third_Out(\平时作业2_红绿灯1_11_third_out ));
  \平时作业2_红绿灯1  \u_平时作业2_红绿灯1_12  (
    .First(in_12), .Second(\平时作业2_红绿灯1_11_second_out ), .Third(\平时作业2_红绿灯1_11_third_out ),
    .Red(\平时作业2_红绿灯1_12_red ), .Yellow(\平时作业2_红绿灯1_12_yellow ), .Green(\平时作业2_红绿灯1_12_green ),
    .Second_Out(\平时作业2_红绿灯1_12_second_out ), .Third_Out(\平时作业2_红绿灯1_12_third_out ));
  \平时作业2_红绿灯1  \u_平时作业2_红绿灯1_13  (
    .First(in_13), .Second(\平时作业2_红绿灯1_12_second_out ), .Third(\平时作业2_红绿灯1_12_third_out ),
    .Red(\平时作业2_红绿灯1_13_red ), .Yellow(\平时作业2_红绿灯1_13_yellow ), .Green(\平时作业2_红绿灯1_13_green ),
    .Second_Out(\平时作业2_红绿灯1_13_second_out ), .Third_Out(\平时作业2_红绿灯1_13_third_out ));
  \平时作业2_红绿灯1  \u_平时作业2_红绿灯1_14  (
    .First(in_14), .Second(\平时作业2_红绿灯1_13_second_out ), .Third(\平时作业2_红绿灯1_13_third_out ),
    .Red(\平时作业2_红绿灯1_14_red ), .Yellow(\平时作业2_红绿灯1_14_yellow ), .Green(\平时作业2_红绿灯1_14_green ),
    .Second_Out(\平时作业2_红绿灯1_14_second_out ), .Third_Out(\平时作业2_红绿灯1_14_third_out ));
  \平时作业2_红绿灯1  \u_平时作业2_红绿灯1_15  (
    .First(in_15), .Second(\平时作业2_红绿灯1_14_second_out ), .Third(\平时作业2_红绿灯1_14_third_out ),
    .Red(\平时作业2_红绿灯1_15_red ), .Yellow(\平时作业2_红绿灯1_15_yellow ), .Green(\平时作业2_红绿灯1_15_green ),
    .Second_Out(\平时作业2_红绿灯1_15_second_out ), .Third_Out(\平时作业2_红绿灯1_15_third_out ));
  \平时作业2_红绿灯1  \u_平时作业2_红绿灯1_16  (
    .First(in_16), .Second(\平时作业2_红绿灯1_15_second_out ), .Third(\平时作业2_红绿灯1_15_third_out ),
    .Red(\平时作业2_红绿灯1_16_red ), .Yellow(\平时作业2_红绿灯1_16_yellow ), .Green(\平时作业2_红绿灯1_16_green ),
    .Second_Out(\平时作业2_红绿灯1_16_second_out ), .Third_Out(\平时作业2_红绿灯1_16_third_out ));
  \平时作业2_红绿灯1  \u_平时作业2_红绿灯1_17  (
    .First(in_17), .Second(\平时作业2_红绿灯1_16_second_out ), .Third(\平时作业2_红绿灯1_16_third_out ),
    .Red(\平时作业2_红绿灯1_17_red ), .Yellow(\平时作业2_红绿灯1_17_yellow ), .Green(\平时作业2_红绿灯1_17_green ),
    .Second_Out(\平时作业2_红绿灯1_17_second_out ), .Third_Out(\平时作业2_红绿灯1_17_third_out ));
  \平时作业2_红绿灯1  \u_平时作业2_红绿灯1_18  (
    .First(in_18), .Second(\平时作业2_红绿灯1_17_second_out ), .Third(\平时作业2_红绿灯1_17_third_out ),
    .Red(\平时作业2_红绿灯1_18_red ), .Yellow(\平时作业2_红绿灯1_18_yellow ), .Green(\平时作业2_红绿灯1_18_green ),
    .Second_Out(\平时作业2_红绿灯1_18_second_out ), .Third_Out(\平时作业2_红绿灯1_18_third_out ));
  \平时作业2_红绿灯1  \u_平时作业2_红绿灯1_19  (
    .First(in_19), .Second(\平时作业2_红绿灯1_18_second_out ), .Third(\平时作业2_红绿灯1_18_third_out ),
    .Red(\平时作业2_红绿灯1_19_red ), .Yellow(\平时作业2_红绿灯1_19_yellow ), .Green(\平时作业2_红绿灯1_19_green ),
    .Second_Out(\平时作业2_红绿灯1_19_second_out ), .Third_Out(\平时作业2_红绿灯1_19_third_out ));
  \平时作业2_红绿灯1  \u_平时作业2_红绿灯1_20  (
    .First(in_20), .Second(\平时作业2_红绿灯1_19_second_out ), .Third(\平时作业2_红绿灯1_19_third_out ),
    .Red(\平时作业2_红绿灯1_20_red ), .Yellow(\平时作业2_红绿灯1_20_yellow ), .Green(\平时作业2_红绿灯1_20_green ),
    .Second_Out(\平时作业2_红绿灯1_20_second_out ), .Third_Out(\平时作业2_红绿灯1_20_third_out ));
  \平时作业2_红绿灯1  \u_平时作业2_红绿灯1_21  (
    .First(in_21), .Second(\平时作业2_红绿灯1_20_second_out ), .Third(\平时作业2_红绿灯1_20_third_out ),
    .Red(\平时作业2_红绿灯1_21_red ), .Yellow(\平时作业2_红绿灯1_21_yellow ), .Green(\平时作业2_红绿灯1_21_green ),
    .Second_Out(\平时作业2_红绿灯1_21_second_out ), .Third_Out(\平时作业2_红绿灯1_21_third_out ));
  \平时作业2_红绿灯1  \u_平时作业2_红绿灯1_22  (
    .First(in_22), .Second(\平时作业2_红绿灯1_21_second_out ), .Third(\平时作业2_红绿灯1_21_third_out ),
    .Red(\平时作业2_红绿灯1_22_red ), .Yellow(\平时作业2_红绿灯1_22_yellow ), .Green(\平时作业2_红绿灯1_22_green ),
    .Second_Out(\平时作业2_红绿灯1_22_second_out ), .Third_Out(\平时作业2_红绿灯1_22_third_out ));
  \平时作业2_红绿灯1  \u_平时作业2_红绿灯1_23  (
    .First(in_23), .Second(\平时作业2_红绿灯1_22_second_out ), .Third(\平时作业2_红绿灯1_22_third_out ),
    .Red(\平时作业2_红绿灯1_23_red ), .Yellow(\平时作业2_红绿灯1_23_yellow ), .Green(\平时作业2_红绿灯1_23_green ),
    .Second_Out(\平时作业2_红绿灯1_23_second_out ), .Third_Out(\平时作业2_红绿灯1_23_third_out ));
  \平时作业2_红绿灯1  \u_平时作业2_红绿灯1_24  (
    .First(in_24), .Second(\平时作业2_红绿灯1_23_second_out ), .Third(\平时作业2_红绿灯1_23_third_out ),
    .Red(\平时作业2_红绿灯1_24_red ), .Yellow(\平时作业2_红绿灯1_24_yellow ), .Green(\平时作业2_红绿灯1_24_green ),
    .Second_Out(\平时作业2_红绿灯1_24_second_out ), .Third_Out(\平时作业2_红绿灯1_24_third_out ));
  \平时作业2_红绿灯1  \u_平时作业2_红绿灯1_25  (
    .First(in_25), .Second(\平时作业2_红绿灯1_24_second_out ), .Third(\平时作业2_红绿灯1_24_third_out ),
    .Red(\平时作业2_红绿灯1_25_red ), .Yellow(\平时作业2_红绿灯1_25_yellow ), .Green(\平时作业2_红绿灯1_25_green ),
    .Second_Out(\平时作业2_红绿灯1_25_second_out ), .Third_Out(\平时作业2_红绿灯1_25_third_out ));
  \平时作业2_红绿灯1  \u_平时作业2_红绿灯1_26  (
    .First(in_26), .Second(\平时作业2_红绿灯1_25_second_out ), .Third(\平时作业2_红绿灯1_25_third_out ),
    .Red(\平时作业2_红绿灯1_26_red ), .Yellow(\平时作业2_红绿灯1_26_yellow ), .Green(\平时作业2_红绿灯1_26_green ),
    .Second_Out(\平时作业2_红绿灯1_26_second_out ), .Third_Out(\平时作业2_红绿灯1_26_third_out ));
  \平时作业2_红绿灯1  \u_平时作业2_红绿灯1_27  (
    .First(in_27), .Second(\平时作业2_红绿灯1_26_second_out ), .Third(\平时作业2_红绿灯1_26_third_out ),
    .Red(\平时作业2_红绿灯1_27_red ), .Yellow(\平时作业2_红绿灯1_27_yellow ), .Green(\平时作业2_红绿灯1_27_green ),
    .Second_Out(\平时作业2_红绿灯1_27_second_out ), .Third_Out(\平时作业2_红绿灯1_27_third_out ));
  \平时作业2_红绿灯1  \u_平时作业2_红绿灯1_28  (
    .First(in_28), .Second(\平时作业2_红绿灯1_27_second_out ), .Third(\平时作业2_红绿灯1_27_third_out ),
    .Red(\平时作业2_红绿灯1_28_red ), .Yellow(\平时作业2_红绿灯1_28_yellow ), .Green(\平时作业2_红绿灯1_28_green ),
    .Second_Out(out_29), .Third_Out(out_30));
  LED #(.active("true")) led_1 (.in(\平时作业2_红绿灯1_1_red ));
  LED #(.active("true")) led_2 (.in(\平时作业2_红绿灯1_1_yellow ));
  LED #(.active("true")) led_3 (.in(\平时作业2_红绿灯1_1_green ));
  LED #(.active("true")) led_4 (.in(\平时作业2_红绿灯1_2_red ));
  LED #(.active("true")) led_5 (.in(\平时作业2_红绿灯1_2_yellow ));
  LED #(.active("true")) led_6 (.in(\平时作业2_红绿灯1_2_green ));
  LED #(.active("true")) led_7 (.in(\平时作业2_红绿灯1_3_red ));
  LED #(.active("true")) led_8 (.in(\平时作业2_红绿灯1_3_yellow ));
  LED #(.active("true")) led_9 (.in(\平时作业2_红绿灯1_3_green ));
  LED #(.active("true")) led_10 (.in(\平时作业2_红绿灯1_4_red ));
  LED #(.active("true")) led_11 (.in(\平时作业2_红绿灯1_4_yellow ));
  LED #(.active("true")) led_12 (.in(\平时作业2_红绿灯1_4_green ));
  LED #(.active("true")) led_13 (.in(\平时作业2_红绿灯1_5_red ));
  LED #(.active("true")) led_14 (.in(\平时作业2_红绿灯1_5_yellow ));
  LED #(.active("true")) led_15 (.in(\平时作业2_红绿灯1_5_green ));
  LED #(.active("true")) led_16 (.in(\平时作业2_红绿灯1_6_red ));
  LED #(.active("true")) led_17 (.in(\平时作业2_红绿灯1_6_yellow ));
  LED #(.active("true")) led_18 (.in(\平时作业2_红绿灯1_6_green ));
  LED #(.active("true")) led_19 (.in(\平时作业2_红绿灯1_7_red ));
  LED #(.active("true")) led_20 (.in(\平时作业2_红绿灯1_7_yellow ));
  LED #(.active("true")) led_21 (.in(\平时作业2_红绿灯1_7_green ));
  LED #(.active("true")) led_22 (.in(\平时作业2_红绿灯1_8_red ));
  LED #(.active("true")) led_23 (.in(\平时作业2_红绿灯1_8_yellow ));
  LED #(.active("true")) led_24 (.in(\平时作业2_红绿灯1_8_green ));
  LED #(.active("true")) led_25 (.in(\平时作业2_红绿灯1_9_red ));
  LED #(.active("true")) led_26 (.in(\平时作业2_红绿灯1_9_yellow ));
  LED #(.active("true")) led_27 (.in(\平时作业2_红绿灯1_9_green ));
  LED #(.active("true")) led_28 (.in(\平时作业2_红绿灯1_10_red ));
  LED #(.active("true")) led_29 (.in(\平时作业2_红绿灯1_10_yellow ));
  LED #(.active("true")) led_30 (.in(\平时作业2_红绿灯1_10_green ));
  LED #(.active("true")) led_31 (.in(\平时作业2_红绿灯1_11_red ));
  LED #(.active("true")) led_32 (.in(\平时作业2_红绿灯1_11_yellow ));
  LED #(.active("true")) led_33 (.in(\平时作业2_红绿灯1_11_green ));
  LED #(.active("true")) led_34 (.in(\平时作业2_红绿灯1_12_red ));
  LED #(.active("true")) led_35 (.in(\平时作业2_红绿灯1_12_yellow ));
  LED #(.active("true")) led_36 (.in(\平时作业2_红绿灯1_12_green ));
  LED #(.active("true")) led_37 (.in(\平时作业2_红绿灯1_13_red ));
  LED #(.active("true")) led_38 (.in(\平时作业2_红绿灯1_13_yellow ));
  LED #(.active("true")) led_39 (.in(\平时作业2_红绿灯1_13_green ));
  LED #(.active("true")) led_40 (.in(\平时作业2_红绿灯1_14_red ));
  LED #(.active("true")) led_41 (.in(\平时作业2_红绿灯1_14_yellow ));
  LED #(.active("true")) led_42 (.in(\平时作业2_红绿灯1_14_green ));
  LED #(.active("true")) led_43 (.in(\平时作业2_红绿灯1_15_red ));
  LED #(.active("true")) led_44 (.in(\平时作业2_红绿灯1_15_yellow ));
  LED #(.active("true")) led_45 (.in(\平时作业2_红绿灯1_15_green ));
  LED #(.active("true")) led_46 (.in(\平时作业2_红绿灯1_16_red ));
  LED #(.active("true")) led_47 (.in(\平时作业2_红绿灯1_16_yellow ));
  LED #(.active("true")) led_48 (.in(\平时作业2_红绿灯1_16_green ));
  LED #(.active("true")) led_49 (.in(\平时作业2_红绿灯1_17_red ));
  LED #(.active("true")) led_50 (.in(\平时作业2_红绿灯1_17_yellow ));
  LED #(.active("true")) led_51 (.in(\平时作业2_红绿灯1_17_green ));
  LED #(.active("true")) led_52 (.in(\平时作业2_红绿灯1_18_red ));
  LED #(.active("true")) led_53 (.in(\平时作业2_红绿灯1_18_yellow ));
  LED #(.active("true")) led_54 (.in(\平时作业2_红绿灯1_18_green ));
  LED #(.active("true")) led_55 (.in(\平时作业2_红绿灯1_19_red ));
  LED #(.active("true")) led_56 (.in(\平时作业2_红绿灯1_19_yellow ));
  LED #(.active("true")) led_57 (.in(\平时作业2_红绿灯1_19_green ));
  LED #(.active("true")) led_58 (.in(\平时作业2_红绿灯1_20_red ));
  LED #(.active("true")) led_59 (.in(\平时作业2_红绿灯1_20_yellow ));
  LED #(.active("true")) led_60 (.in(\平时作业2_红绿灯1_20_green ));
  LED #(.active("true")) led_61 (.in(\平时作业2_红绿灯1_21_red ));
  LED #(.active("true")) led_62 (.in(\平时作业2_红绿灯1_21_yellow ));
  LED #(.active("true")) led_63 (.in(\平时作业2_红绿灯1_21_green ));
  LED #(.active("true")) led_64 (.in(\平时作业2_红绿灯1_22_red ));
  LED #(.active("true")) led_65 (.in(\平时作业2_红绿灯1_22_yellow ));
  LED #(.active("true")) led_66 (.in(\平时作业2_红绿灯1_22_green ));
  LED #(.active("true")) led_67 (.in(\平时作业2_红绿灯1_23_red ));
  LED #(.active("true")) led_68 (.in(\平时作业2_红绿灯1_23_yellow ));
  LED #(.active("true")) led_69 (.in(\平时作业2_红绿灯1_23_green ));
  LED #(.active("true")) led_70 (.in(\平时作业2_红绿灯1_24_red ));
  LED #(.active("true")) led_71 (.in(\平时作业2_红绿灯1_24_yellow ));
  LED #(.active("true")) led_72 (.in(\平时作业2_红绿灯1_24_green ));
  LED #(.active("true")) led_73 (.in(\平时作业2_红绿灯1_25_red ));
  LED #(.active("true")) led_74 (.in(\平时作业2_红绿灯1_25_yellow ));
  LED #(.active("true")) led_75 (.in(\平时作业2_红绿灯1_25_green ));
  LED #(.active("true")) led_76 (.in(\平时作业2_红绿灯1_26_red ));
  LED #(.active("true")) led_77 (.in(\平时作业2_红绿灯1_26_yellow ));
  LED #(.active("true")) led_78 (.in(\平时作业2_红绿灯1_26_green ));
  LED #(.active("true")) led_79 (.in(\平时作业2_红绿灯1_27_red ));
  LED #(.active("true")) led_80 (.in(\平时作业2_红绿灯1_27_yellow ));
  LED #(.active("true")) led_81 (.in(\平时作业2_红绿灯1_27_green ));
  LED #(.active("true")) led_82 (.in(\平时作业2_红绿灯1_28_red ));
  LED #(.active("true")) led_83 (.in(\平时作业2_红绿灯1_28_yellow ));
  LED #(.active("true")) led_84 (.in(\平时作业2_红绿灯1_28_green ));

  // Notes on the sheet:
  //   红灯
  //   黄灯
  //   绿灯
  //   红灯
  //   黄灯
  //   绿灯
  //   红灯
  //   黄灯
  //   绿灯
  //   红灯
  //   黄灯
  //   绿灯
  //   红灯
  //   红灯
  //   黄灯
  //   绿灯
  //   红灯
  //   黄灯
  //   绿灯
  //   下面都是红灯/黄灯/绿灯
endmodule

module \平时作业3_SR锁存器  (
  input  R,
  input  S,
  output Q,
  output Q_prime
);

  nor nor_1 (Q, R, Q_prime);
  nor nor_2 (Q_prime, Q, S);
endmodule

module \平时作业3_D锁存器  (
  input  Reset,
  input  CLK,
  input  D,
  output Q,
  output Q_prime
);

  wire and_1_out, and_2_out, not_1_out, or_1_out;

  and and_1 (and_1_out, CLK, not_1_out);
  not not_1 (not_1_out, D);
  and and_2 (and_2_out, CLK, D);
  or or_1 (or_1_out, Reset, and_1_out);
  \平时作业3_SR锁存器  \u_平时作业3_sr锁存器_1  (.R(or_1_out), .S(and_2_out), .Q(Q), .Q_prime(Q_prime));
endmodule

module \平时作业3_D触发器_带Reset  (
  input  CLK,
  input  D,
  input  Reset,
  output Q,
  output Q_prime
);

  wire not_1_out, \平时作业3_d锁存器_1_q ;

  \平时作业3_D锁存器  \u_平时作业3_d锁存器_1  (.Reset(Reset), .CLK(not_1_out), .D(D), .Q(\平时作业3_d锁存器_1_q ));  // open: Q_prime
  not not_1 (not_1_out, CLK);
  \平时作业3_D锁存器  \u_平时作业3_d锁存器_2  (.Reset(Reset), .CLK(CLK), .D(\平时作业3_d锁存器_1_q ), .Q(Q), .Q_prime(Q_prime));
endmodule

module \平时作业3_2位状态寄存器  (
  input  CLK,
  input  S1_prime,
  input  S0_prime,
  input  Reset,
  output S1,
  output S0
);

  \平时作业3_D触发器_带Reset  \u_平时作业3_d触发器_带reset_1  (.D(S1_prime), .Reset(Reset), .Q(S1), .CLK(CLK));  // open: Q_prime
  \平时作业3_D触发器_带Reset  \u_平时作业3_d触发器_带reset_2  (.D(S0_prime), .Reset(Reset), .Q(S0), .CLK(CLK));  // open: Q_prime
endmodule

module \平时作业3_交通控制器_有限状态机  (
  input  CLK,
  input  TA,
  input  TB,
  input  Reset,
  output AR,
  output AY,
  output AG,
  output BR,
  output BY,
  output BG
);

  wire and_1_out, and_2_out, and_3_out, and_4_out, not_1_out, or_1_out, xor_1_out, \平时作业3_2位状态寄存器_1_s0 ,
       \平时作业3_2位状态寄存器_1_s1 ;

  and and_1 (and_1_out, ~\平时作业3_2位状态寄存器_1_s1 , ~\平时作业3_2位状态寄存器_1_s0 , ~TA);  // AND_Gate
  and and_2 (and_2_out, \平时作业3_2位状态寄存器_1_s1 , ~\平时作业3_2位状态寄存器_1_s0 , ~TB);  // AND_Gate
  xor xor_1 (xor_1_out, \平时作业3_2位状态寄存器_1_s1 , \平时作业3_2位状态寄存器_1_s0 );
  or or_1 (or_1_out, and_1_out, and_2_out);
  \平时作业3_2位状态寄存器  \u_平时作业3_2位状态寄存器_1  (
    .S1_prime(xor_1_out), .S0_prime(or_1_out), .S1(\平时作业3_2位状态寄存器_1_s1 ), .S0(\平时作业3_2位状态寄存器_1_s0 ),
    .CLK(CLK), .Reset(Reset));
  and and_3 (and_3_out, ~\平时作业3_2位状态寄存器_1_s1 , \平时作业3_2位状态寄存器_1_s0 );  // AND_Gate
  not not_1 (not_1_out, \平时作业3_2位状态寄存器_1_s1 );
  and and_4 (and_4_out, \平时作业3_2位状态寄存器_1_s1 , \平时作业3_2位状态寄存器_1_s0 );
  and and_5 (AR, \平时作业3_2位状态寄存器_1_s1 , ~and_3_out);  // AND_Gate
  and and_6 (AY, ~\平时作业3_2位状态寄存器_1_s1 , and_3_out);  // AND_Gate
  and and_7 (AG, ~\平时作业3_2位状态寄存器_1_s1 , ~and_3_out);  // AND_Gate
  and and_8 (BR, not_1_out, ~and_4_out);  // AND_Gate
  and and_9 (BY, ~not_1_out, and_4_out);  // AND_Gate
  and and_10 (BG, ~not_1_out, ~and_4_out);  // AND_Gate
endmodule

module \平时作业3_交通控制器显示  (
  input  TA,
  input  TB,
  input  Reset
);

  wire AG, AR, AY, BG, BR, BY, clock_1_out;

  Clock #(.highDuration(1), .lowDuration(1)) clock_1 (.out(clock_1_out));
  \平时作业3_交通控制器_有限状态机  \u_平时作业3_交通控制器_有限状态机_1  (
    .CLK(clock_1_out), .TA(TA), .TB(TB), .Reset(Reset), .AR(AR), .AY(AY), .AG(AG), .BR(BR), .BY(BY), .BG(BG));
  LED #(.active("true")) led_1 (.in(AR));
  LED #(.active("true")) led_2 (.in(AY));
  LED #(.active("true")) led_3 (.in(AG));
  LED #(.active("true")) led_4 (.in(BG));
  LED #(.active("true")) led_5 (.in(BR));
  LED #(.active("true")) led_6 (.in(BY));
  LED #(.active("true")) led_7 (.in(BG));
  LED #(.active("true")) led_8 (.in(BR));
  LED #(.active("true")) led_9 (.in(BY));
  LED #(.active("true")) led_10 (.in(AG));
  LED #(.active("true")) led_11 (.in(AY));
  LED #(.active("true")) led_12 (.in(AR));
endmodule

module \平时作业4_存储系统的设计  (
  input  [15:0] Address_Bus,
  input  [7:0] Data_Out,
  input  R_W_prime,
  input  MREQ_prime,
  output [7:0] Data_In
);

  wire and_1_out, clock_1_out, decoder_1_out0, decoder_1_out1, decoder_1_out2, decoder_1_out3,
       decoder_1_out4, decoder_1_out5, decoder_1_out6, decoder_1_out7, MREQ_prime_t, not_3_out, not_4_out,
       not_5_out, not_6_out, not_10_out, not_11_out, not_12_out, Write_prime;

  not not_1 (MREQ_prime_t, MREQ_prime);
  not not_2 (Write_prime, R_W_prime);
  not not_3 (not_3_out, decoder_1_out0);
  Decoder #(.select(3), .tristate("false"), .disabled("Z"), .enable("true")) decoder_1 (
    .out0(decoder_1_out0), .out1(decoder_1_out1), .out2(decoder_1_out2), .out3(decoder_1_out3),
    .out4(decoder_1_out4), .out5(decoder_1_out5), .out6(decoder_1_out6), .out7(decoder_1_out7),
    .sel(Address_Bus[15:13]), .en(MREQ_prime_t));
  not not_4 (not_4_out, decoder_1_out1);
  not not_5 (not_5_out, decoder_1_out2);
  not not_6 (not_6_out, decoder_1_out3);
  // NOT_Gate not_7 has open pins: in=decoder_1_out4, out=open
  // NOT_Gate not_8 has open pins: in=decoder_1_out5, out=open
  // NOT_Gate not_9 has open pins: in=decoder_1_out6, out=open
  not not_10 (not_10_out, decoder_1_out7);
  not not_11 (not_11_out, not_10_out);
  and and_1 (and_1_out, Address_Bus[11], Address_Bus[12], not_11_out);
  not not_12 (not_12_out, and_1_out);
  Clock #(.highDuration(1), .lowDuration(1)) clock_1 (.out(clock_1_out));
  ROM #(.addrWidth(13), .dataWidth(8), .Select("low")) rom_1 (
    .addr(Address_Bus[12:0]), .data(Data_In), .sel(not_3_out));
  RAM #(.addrWidth(13), .dataWidth(8), .bus("separate"), .Select("low")) ram_1 (
    .addr(Address_Bus[12:0]), .din(Data_Out), .data(Data_In), .str(Write_prime), .sel(not_4_out),
    .clk(clock_1_out), .ld(R_W_prime));  // open: clr
  RAM #(.addrWidth(13), .dataWidth(8), .bus("separate"), .Select("low")) ram_2 (
    .addr(Address_Bus[12:0]), .din(Data_Out), .data(Data_In), .str(Write_prime), .sel(not_5_out),
    .clk(clock_1_out), .ld(R_W_prime));  // open: clr
  RAM #(.addrWidth(13), .dataWidth(8), .bus("separate"), .Select("low")) ram_3 (
    .addr(Address_Bus[12:0]), .din(Data_Out), .data(Data_In), .str(Write_prime), .sel(not_6_out),
    .clk(clock_1_out), .ld(R_W_prime));  // open: clr
  RAM #(.addrWidth(11), .dataWidth(8), .bus("separate"), .Select("low")) ram_4 (
    .addr(Address_Bus[10:0]), .din(Data_Out), .data(Data_In), .str(Write_prime), .sel(not_12_out),
    .clk(clock_1_out), .ld(R_W_prime));  // open: clr
  // Probe on Data_In

  // Other names for the same wires on the sheet: Read = R_W_prime

  // Notes on the sheet:
  //   CPU
  //   contents of rom_1 (hex, n*v repeats v):
  //   0 1 2 3 4 5
  //   8K*8bit EPROM
  //   8K*8bit RAM
  //   8K*8bit RAM
  //   8K*8bit RAM
  //   2K*8bit RAM
endmodule
