// Logisim project 实验电路-软件2307-20231601-张子琪aaa.circ as structural Verilog
module \实验一__7段数码管显示译码器带极性控制端且显示A_F的的组件  (
  input  x,
  input  h,
  input  y,
  input  z,
  input  w,
  output a,
  output b,
  output c,
  output d,
  output e,
  output f,
  output g
);

  wire and_1_out, and_2_out, and_3_out, and_4_out, and_5_out, and_6_out, and_7_out, and_8_out, and_9_out,
       and_10_out, and_11_out, and_12_out, and_13_out, and_14_out, and_15_out, and_16_out, and_17_out,
       and_18_out, and_19_out, and_20_out, and_21_out, and_22_out, and_23_out, and_24_out, and_25_out,
       and_26_out, and_27_out, and_28_out, and_29_out, and_30_out, and_31_out, and_32_out, and_33_out,
       and_34_out, and_35_out, and_36_out, and_37_out, and_38_out, and_39_out, and_40_out, and_41_out,
       and_42_out, and_43_out, and_44_out, and_45_out, and_46_out, and_47_out, and_48_out, and_49_out,
       and_50_out, and_51_out, and_52_out, and_53_out, and_54_out, and_55_out, and_56_out, and_57_out,
       and_58_out, and_59_out, and_60_out, not_1_out, not_2_out, not_3_out, not_4_out, not_5_out, not_6_out,
       not_7_out, not_8_out, not_9_out, not_10_out, not_11_out, not_12_out, not_13_out, not_14_out,
       not_15_out, not_16_out, not_17_out, not_18_out, not_19_out, not_20_out, not_21_out, not_22_out,
       not_23_out, not_24_out, not_25_out, not_26_out, not_27_out, not_28_out, not_29_out, not_30_out,
       not_31_out, not_32_out, not_33_out, not_34_out, not_35_out, not_36_out, not_37_out, not_38_out,
       not_39_out, not_40_out, not_41_out, not_42_out, not_43_out, not_44_out, not_45_out, not_46_out,
       not_47_out, not_48_out, not_49_out, not_50_out, not_51_out, not_52_out, not_53_out, not_54_out,
       not_55_out, not_56_out, not_57_out, not_58_out, not_59_out, not_60_out, not_61_out, not_62_out,
       not_63_out, not_64_out, not_65_out, not_66_out, not_67_out, not_68_out, not_69_out, not_70_out,
       not_71_out, not_72_out, not_73_out, not_74_out, not_75_out, not_76_out, not_77_out, not_78_out,
       not_79_out, not_80_out, not_81_out, not_82_out, not_83_out, not_84_out, not_85_out, not_86_out,
       not_87_out, not_88_out, not_89_out, not_90_out, not_91_out, not_92_out, not_93_out, not_94_out,
       not_95_out, not_96_out, not_97_out, not_98_out, not_99_out, not_100_out, not_101_out, not_102_out,
       not_103_out, not_104_out, not_105_out, not_106_out, not_107_out, not_108_out, not_109_out;

  not not_1 (not_1_out, x);
  not not_2 (not_2_out, h);
  not not_3 (not_3_out, y);
  not not_4 (not_4_out, z);
  not not_5 (not_5_out, x);
  not not_6 (not_6_out, h);
  not not_7 (not_7_out, z);
  not not_8 (not_8_out, w);
  not not_9 (not_9_out, y);
  not not_10 (not_10_out, w);
  not not_11 (not_11_out, x);
  not not_12 (not_12_out, x);
  not not_13 (not_13_out, h);
  not not_14 (not_14_out, y);
  not not_15 (not_15_out, h);
  not not_16 (not_16_out, z);
  not not_17 (not_17_out, y);
  not not_18 (not_18_out, z);
  not not_19 (not_19_out, w);
  not not_20 (not_20_out, x);
  not not_21 (not_21_out, h);
  not not_22 (not_22_out, z);
  not not_23 (not_23_out, h);
  not not_24 (not_24_out, w);
  not not_25 (not_25_out, x);
  not not_26 (not_26_out, z);
  not not_27 (not_27_out, w);
  not not_28 (not_28_out, y);
  not not_29 (not_29_out, z);
  not not_30 (not_30_out, y);
  not not_31 (not_31_out, w);
  not not_32 (not_32_out, x);
  not not_33 (not_33_out, h);
  not not_34 (not_34_out, h);
  not not_35 (not_35_out, w);
  not not_36 (not_36_out, z);
  not not_37 (not_37_out, x);
  not not_38 (not_38_out, h);
  not not_39 (not_39_out, y);
  not not_40 (not_40_out, w);
  not not_41 (not_41_out, y);
  not not_42 (not_42_out, z);
  not not_43 (not_43_out, y);
  not not_44 (not_44_out, z);
  not not_45 (not_45_out, x);
  not not_46 (not_46_out, h);
  not not_47 (not_47_out, w);
  not not_48 (not_48_out, h);
  not not_49 (not_49_out, y);
  not not_50 (not_50_out, x);
  not not_51 (not_51_out, h);
  not not_52 (not_52_out, y);
  not not_53 (not_53_out, z);
  not not_54 (not_54_out, x);
  not not_55 (not_55_out, h);
  not not_56 (not_56_out, z);
  not not_57 (not_57_out, w);
  not not_58 (not_58_out, h);
  not not_59 (not_59_out, x);
  not not_60 (not_60_out, y);
  not not_61 (not_61_out, w);
  not not_62 (not_62_out, y);
  not not_63 (not_63_out, z);
  not not_64 (not_64_out, w);
  not not_65 (not_65_out, h);
  not not_66 (not_66_out, y);
  not not_67 (not_67_out, w);
  not not_68 (not_68_out, z);
  not not_69 (not_69_out, x);
  not not_70 (not_70_out, h);
  not not_71 (not_71_out, h);
  not not_72 (not_72_out, y);
  not not_73 (not_73_out, z);
  not not_74 (not_74_out, x);
  not not_75 (not_75_out, h);
  not not_76 (not_76_out, z);
  not not_77 (not_77_out, y);
  not not_78 (not_78_out, w);
  not not_79 (not_79_out, w);
  not not_80 (not_80_out, x);
  not not_81 (not_81_out, h);
  not not_82 (not_82_out, y);
  not not_83 (not_83_out, x);
  not not_84 (not_84_out, h);
  not not_85 (not_85_out, y);
  not not_86 (not_86_out, x);
  not not_87 (not_87_out, h);
  not not_88 (not_88_out, z);
  not not_89 (not_89_out, w);
  not not_90 (not_90_out, x);
  not not_91 (not_91_out, z);
  not not_92 (not_92_out, w);
  not not_93 (not_93_out, h);
  not not_94 (not_94_out, z);
  not not_95 (not_95_out, y);
  not not_96 (not_96_out, x);
  not not_97 (not_97_out, h);
  not not_98 (not_98_out, y);
  not not_99 (not_99_out, z);
  not not_100 (not_100_out, x);
  not not_101 (not_101_out, h);
  not not_102 (not_102_out, y);
  not not_103 (not_103_out, w);
  not not_104 (not_104_out, x);
  not not_105 (not_105_out, z);
  not not_106 (not_106_out, h);
  not not_107 (not_107_out, z);
  not not_108 (not_108_out, w);
  not not_109 (not_109_out, y);
  and and_1 (and_1_out, not_1_out, not_2_out, not_3_out, not_4_out, w);
  and and_2 (and_2_out, not_5_out, not_6_out, y, not_7_out, not_8_out);
  and and_3 (and_3_out, h, not_9_out, not_10_out);
  and and_4 (and_4_out, not_11_out, h, z);
  and and_5 (and_5_out, not_12_out, h, y, w);
  and and_6 (and_6_out, h, y, z);
  and and_7 (and_7_out, x, not_13_out, not_14_out, z, w);
  and and_8 (and_8_out, x, not_15_out, y, not_16_out, w);
  and and_9 (and_9_out, x, h, not_17_out, not_18_out);
  and and_10 (and_10_out, x, h, not_19_out);
  and and_11 (and_11_out, not_20_out, not_21_out, y, not_22_out, w);
  and and_12 (and_12_out, not_23_out, y, z, not_24_out);
  and and_13 (and_13_out, not_25_out, h, not_26_out, not_27_out);
  and and_14 (and_14_out, h, not_28_out, not_29_out);
  and and_15 (and_15_out, h, not_30_out, not_31_out);
  and and_16 (and_16_out, not_32_out, h, z, w);
  and and_17 (and_17_out, x, not_33_out, z, w);
  and and_18 (and_18_out, x, not_34_out, y, not_35_out);
  and and_19 (and_19_out, x, h, not_36_out, w);
  and and_20 (and_20_out, not_37_out, not_38_out, not_39_out, z, not_40_out);
  and and_21 (and_21_out, h, not_41_out, not_42_out);
  and and_22 (and_22_out, h, not_43_out, w);
  and and_23 (and_23_out, h, not_44_out, w);
  and and_24 (and_24_out, not_45_out, h, y);
  and and_25 (and_25_out, x, not_46_out, y, not_47_out);
  and and_26 (and_26_out, x, not_48_out, y, z);
  and and_27 (and_27_out, x, h, not_49_out);
  and and_28 (and_28_out, not_50_out, not_51_out, not_52_out, not_53_out, w);
  and and_29 (and_29_out, not_54_out, not_55_out, y, not_56_out, not_57_out);
  and and_30 (and_30_out, not_58_out, y, z, w);
  and and_31 (and_31_out, not_59_out, h, not_60_out, not_61_out);
  and and_32 (and_32_out, h, not_62_out, z, w);
  and and_33 (and_33_out, h, y, not_63_out, w);
  and and_34 (and_34_out, h, y, z, not_64_out);
  and and_35 (and_35_out, x, not_65_out, not_66_out, z, not_67_out);
  and and_36 (and_36_out, x, h, not_68_out);
  and and_37 (and_37_out, not_69_out, not_70_out, w);
  and and_38 (and_38_out, not_71_out, not_72_out, not_73_out, w);
  and and_39 (and_39_out, not_74_out, not_75_out, y, not_76_out);
  and and_40 (and_40_out, h, not_77_out, not_78_out);
  and and_41 (and_41_out, h, z, not_79_out);
  and and_42 (and_42_out, x, h, z);
  and and_43 (and_43_out, x, h, y);
  and and_44 (and_44_out, not_80_out, not_81_out, not_82_out, w);
  and and_45 (and_45_out, not_83_out, not_84_out, not_85_out, z);
  and and_46 (and_46_out, not_86_out, not_87_out, z, w);
  and and_47 (and_47_out, h, not_88_out, not_89_out);
  and and_48 (and_48_out, not_90_out, h, y, not_91_out);
  and and_49 (and_49_out, h, y, not_92_out);
  and and_50 (and_50_out, x, not_93_out, y, not_94_out, w);
  and and_51 (and_51_out, x, h, not_95_out);
  and and_52 (and_52_out, x, h, z);
  and and_53 (and_53_out, not_96_out, not_97_out, not_98_out, not_99_out);
  and and_54 (and_54_out, not_100_out, not_101_out, y, z, w);
  and and_55 (and_55_out, h, not_102_out, z);
  and and_56 (and_56_out, h, z, not_103_out);
  and and_57 (and_57_out, not_104_out, h, y, not_105_out);
  and and_58 (and_58_out, x, not_106_out, y, not_107_out, not_108_out);
  and and_59 (and_59_out, x, h, not_109_out);
  and and_60 (and_60_out, x, h, w);
  or or_1 (a, and_1_out, and_2_out, and_3_out, and_4_out, and_5_out, and_6_out, and_7_out, and_8_out, and_9_out, and_10_out);
  or or_2 (b, and_11_out, and_12_out, and_13_out, and_14_out, and_15_out, and_16_out, and_17_out, and_18_out, and_19_out);
  or or_3 (c, and_20_out, and_21_out, and_22_out, and_23_out, and_24_out, and_25_out, and_26_out, and_27_out);
  or or_4 (d, and_28_out, and_29_out, and_30_out, and_31_out, and_32_out, and_33_out, and_34_out, and_35_out, and_36_out);
  or or_5 (e, and_37_out, and_38_out, and_39_out, and_40_out, and_41_out, and_42_out, and_43_out);
  or or_6 (f, and_44_out, and_45_out, and_46_out, and_47_out, and_48_out, and_49_out, and_50_out, and_51_out, and_52_out);
  or or_7 (g, and_53_out, and_54_out, and_55_out, and_56_out, and_57_out, and_58_out, and_59_out, and_60_out);
endmodule

module \实验一__7段数码管显示译码器_带极性控制端且显示A_F  (
  input  in_1
);

  wire clock_1_out, \实验一_7段数码管显示译码器带极性控制端且显示a_f的的组件_1_a , \实验一_7段数码管显示译码器带极性控制端且显示a_f的的组件_1_b ,
       \实验一_7段数码管显示译码器带极性控制端且显示a_f的的组件_1_c , \实验一_7段数码管显示译码器带极性控制端且显示a_f的的组件_1_d ,
       \实验一_7段数码管显示译码器带极性控制端且显示a_f的的组件_1_e , \实验一_7段数码管显示译码器带极性控制端且显示a_f的的组件_1_f ,
       \实验一_7段数码管显示译码器带极性控制端且显示a_f的的组件_1_g ;
  wire [3:0] counter_1_q;

  Clock #(.highDuration(8), .lowDuration(8)) clock_1 (.out(clock_1_out));
  Counter #(.width(4), .max('hf), .ongoal("wrap"), .trigger("rising"), .behavior("new")) counter_1 (
    .D(counter_1_q), .Q(counter_1_q), .clk(clock_1_out));  // open: load, count, carry, clr, preset, down
  \实验一__7段数码管显示译码器带极性控制端且显示A_F的的组件  \u_实验一_7段数码管显示译码器带极性控制端且显示a_f的的组件_1  (
    .x(counter_1_q[3]), .h(in_1), .y(counter_1_q[2]), .z(counter_1_q[1]), .w(counter_1_q[0]),
    .a(\实验一_7段数码管显示译码器带极性控制端且显示a_f的的组件_1_a ), .b(\实验一_7段数码管显示译码器带极性控制端且显示a_f的的组件_1_b ),
    .c(\实验一_7段数码管显示译码器带极性控制端且显示a_f的的组件_1_c ), .d(\实验一_7段数码管显示译码器带极性控制端且显示a_f的的组件_1_d ),
    .e(\实验一_7段数码管显示译码器带极性控制端且显示a_f的的组件_1_e ), .f(\实验一_7段数码管显示译码器带极性控制端且显示a_f的的组件_1_f ),
    .g(\实验一_7段数码管显示译码器带极性控制端且显示a_f的的组件_1_g ));
  _7_Segment_Display #(.active("false")) u_7_segment_display_1 (
    .g(\实验一_7段数码管显示译码器带极性控制端且显示a_f的的组件_1_g ), .f(\实验一_7段数码管显示译码器带极性控制端且显示a_f的的组件_1_f ),
    .a(\实验一_7段数码管显示译码器带极性控制端且显示a_f的的组件_1_a ), .b(\实验一_7段数码管显示译码器带极性控制端且显示a_f的的组件_1_b ),
    .e(\实验一_7段数码管显示译码器带极性控制端且显示a_f的的组件_1_e ), .d(\实验一_7段数码管显示译码器带极性控制端且显示a_f的的组件_1_d ),
    .c(\实验一_7段数码管显示译码器带极性控制端且显示a_f的的组件_1_c ));  // open: dp
endmodule

module \实验一__7段数码管显示译码器不显示_9的组件  (
  input  x,
  input  y,
  input  z,
  input  w,
  output a,
  output b,
  output c,
  output d,
  output e,
  output f,
  output g
);

  wire and_1_out, and_2_out, and_3_out, and_4_out, and_5_out, and_6_out, and_7_out, and_8_out, and_9_out,
       and_10_out, and_11_out, and_12_out, and_13_out, and_14_out, and_15_out, and_16_out, and_17_out,
       and_18_out, and_19_out, and_20_out, and_21_out, and_22_out, and_23_out, and_24_out, and_25_out,
       and_26_out, not_1_out, not_2_out, not_3_out, not_4_out, not_5_out, not_6_out, not_7_out, not_8_out,
       not_9_out, not_10_out, not_11_out, not_12_out, not_13_out, not_14_out, not_15_out, not_16_out,
       not_17_out, not_18_out, not_19_out, not_20_out, not_21_out, not_22_out, not_23_out, not_24_out,
       not_25_out, not_26_out, not_27_out, not_28_out, not_29_out, not_30_out, not_31_out, not_32_out,
       not_33_out, not_34_out, not_35_out, not_36_out, not_37_out, not_38_out, not_39_out, not_40_out,
       not_41_out, not_42_out, not_43_out, not_44_out, not_45_out, not_46_out, not_47_out, not_48_out,
       not_49_out, not_50_out, not_51_out, not_52_out;

  not not_1 (not_1_out, y);
  and and_1 (and_1_out, not_1_out, not_2_out, not_3_out);
  not not_2 (not_2_out, z);
  not not_3 (not_3_out, w);
  not not_4 (not_4_out, x);
  and and_2 (and_2_out, not_4_out, z);
  not not_5 (not_5_out, x);
  and and_3 (and_3_out, not_5_out, y, w);
  and and_4 (and_4_out, x, not_6_out, not_7_out);
  not not_6 (not_6_out, y);
  not not_7 (not_7_out, z);
  not not_8 (not_8_out, x);
  and and_5 (and_5_out, not_8_out, not_9_out);
  not not_9 (not_9_out, y);
  not not_10 (not_10_out, x);
  not not_11 (not_11_out, z);
  and and_6 (and_6_out, not_10_out, not_11_out, not_12_out);
  not not_12 (not_12_out, w);
  not not_13 (not_13_out, y);
  and and_7 (and_7_out, not_13_out, not_14_out);
  not not_14 (not_14_out, z);
  not not_15 (not_15_out, x);
  and and_8 (and_8_out, not_15_out, z, w);
  not not_16 (not_16_out, y);
  and and_9 (and_9_out, not_16_out, not_17_out);
  not not_17 (not_17_out, z);
  not not_18 (not_18_out, x);
  and and_10 (and_10_out, not_18_out, w);
  not not_19 (not_19_out, x);
  and and_11 (and_11_out, not_19_out, y);
  not not_20 (not_20_out, x);
  not not_21 (not_21_out, y);
  not not_22 (not_22_out, w);
  not not_23 (not_23_out, x);
  not not_24 (not_24_out, y);
  not not_25 (not_25_out, x);
  not not_26 (not_26_out, w);
  not not_27 (not_27_out, x);
  not not_28 (not_28_out, z);
  not not_29 (not_29_out, y);
  not not_30 (not_30_out, z);
  not not_31 (not_31_out, y);
  not not_32 (not_32_out, z);
  and and_12 (and_12_out, not_31_out, not_32_out, not_33_out);
  not not_33 (not_33_out, w);
  not not_34 (not_34_out, x);
  and and_13 (and_13_out, not_34_out, z, not_35_out);
  not not_35 (not_35_out, w);
  not not_36 (not_36_out, x);
  not not_37 (not_37_out, z);
  and and_14 (and_14_out, not_36_out, not_37_out, not_38_out);
  not not_38 (not_38_out, w);
  not not_39 (not_39_out, x);
  and and_15 (and_15_out, not_39_out, y, not_40_out);
  not not_40 (not_40_out, z);
  not not_41 (not_41_out, x);
  and and_16 (and_16_out, not_41_out, y, not_42_out);
  not not_42 (not_42_out, w);
  not not_43 (not_43_out, y);
  and and_17 (and_17_out, x, not_43_out, not_44_out);
  not not_44 (not_44_out, z);
  not not_45 (not_45_out, x);
  and and_18 (and_18_out, not_45_out, not_46_out, z);
  not not_46 (not_46_out, y);
  not not_47 (not_47_out, x);
  and and_19 (and_19_out, not_47_out, y, not_48_out);
  not not_48 (not_48_out, z);
  not not_49 (not_49_out, x);
  and and_20 (and_20_out, not_49_out, y, not_50_out);
  not not_50 (not_50_out, w);
  and and_21 (and_21_out, x, not_51_out, not_52_out);
  not not_51 (not_51_out, y);
  not not_52 (not_52_out, z);
  or or_1 (a, and_1_out, and_2_out, and_3_out, and_4_out);
  or or_2 (b, and_5_out, and_6_out, and_7_out, and_8_out);
  or or_3 (c, and_9_out, and_10_out, and_11_out);
  and and_22 (and_22_out, not_20_out, not_21_out, not_22_out);
  and and_23 (and_23_out, not_23_out, not_24_out, z);
  and and_24 (and_24_out, not_25_out, z, not_26_out);
  and and_25 (and_25_out, not_27_out, y, not_28_out, w);
  and and_26 (and_26_out, x, not_29_out, not_30_out);
  or or_4 (e, and_12_out, and_13_out);
  or or_5 (f, and_14_out, and_15_out, and_16_out, and_17_out);
  or or_6 (g, and_18_out, and_19_out, and_20_out, and_21_out);
  or or_7 (d, and_22_out, and_23_out, and_24_out, and_25_out, and_26_out);
endmodule

module \实验一__7段数码管显示译码器_不显示_9  (
);

  wire clock_1_out, \实验一_7段数码管显示译码器不显示_9的组件_1_a , \实验一_7段数码管显示译码器不显示_9的组件_1_b , \实验一_7段数码管显示译码器不显示_9的组件_1_c ,
       \实验一_7段数码管显示译码器不显示_9的组件_1_d , \实验一_7段数码管显示译码器不显示_9的组件_1_e , \实验一_7段数码管显示译码器不显示_9的组件_1_f ,
       \实验一_7段数码管显示译码器不显示_9的组件_1_g ;
  wire [3:0] counter_1_q;

  Counter #(.width(4), .max('hf), .ongoal("wrap"), .trigger("rising"), .behavior("new")) counter_1 (
    .D(counter_1_q), .Q(counter_1_q), .clk(clock_1_out));  // open: load, count, carry, clr, preset, down
  Clock #(.highDuration(8), .lowDuration(8)) clock_1 (.out(clock_1_out));
  \实验一__7段数码管显示译码器不显示_9的组件  \u_实验一_7段数码管显示译码器不显示_9的组件_1  (
    .x(counter_1_q[3]), .y(counter_1_q[2]), .z(counter_1_q[1]), .w(counter_1_q[0]),
    .a(\实验一_7段数码管显示译码器不显示_9的组件_1_a ), .b(\实验一_7段数码管显示译码器不显示_9的组件_1_b ), .c(\实验一_7段数码管显示译码器不显示_9的组件_1_c ),
    .d(\实验一_7段数码管显示译码器不显示_9的组件_1_d ), .e(\实验一_7段数码管显示译码器不显示_9的组件_1_e ), .f(\实验一_7段数码管显示译码器不显示_9的组件_1_f ),
    .g(\实验一_7段数码管显示译码器不显示_9的组件_1_g ));
  _7_Segment_Display #(.active("true")) u_7_segment_display_1 (
    .g(\实验一_7段数码管显示译码器不显示_9的组件_1_g ), .f(\实验一_7段数码管显示译码器不显示_9的组件_1_f ), .a(\实验一_7段数码管显示译码器不显示_9的组件_1_a ),
    .b(\实验一_7段数码管显示译码器不显示_9的组件_1_b ), .e(\实验一_7段数码管显示译码器不显示_9的组件_1_e ), .d(\实验一_7段数码管显示译码器不显示_9的组件_1_d ),
    .c(\实验一_7段数码管显示译码器不显示_9的组件_1_c ));  // open: dp
endmodule

module \实验二_乘法器_组合逻辑电路  (
  input  in_1,
  input  in_2,
  input  in_3,
  input  in_4,
  input  in_5,
  input  in_6,
  input  in_7,
  input  in_8,
  input  [7:0] B,
  input  [7:0] A,
  output [15:0] \结果 
);

  wire A0B1_out, A0B2_out, A0B3_out, A0B4_out, A0B5_out, A0B6_2_out, A0B6_out, A1B0_out, A1B1_out, A1B2_out,
       A1B3_out, A1B4_out, A1B5_out, A1B6_2_out, A1B6_out, A2B0_out, A2B1_out, A2B2_out, A2B3_out, A2B4_out,
       A2B5_out, A2B6_2_out, A2B6_out, A3B0_out, A3B1_out, A3B2_out, A3B3_out, A3B4_out, A3B5_out,
       A3B6_2_out, A3B6_out, A4B0_out, A4B1_out, A4B2_out, A4B3_out, A4B4_out, A4B5_out, A4B6_2_out,
       A4B6_out, A5B0_out, A5B1_out, A5B2_out, A5B3_out, A5B4_out, A5B5_out, A5B6_2_out, A5B6_out, A6B0_out,
       A6B1_out, A6B2_out, A6B3_out, A6B4_out, A6B5_out, A6B6_2_out, A6B6_out, A7B0_out, A7B1_out, A7B2_out,
       A7B3_out, A7B4_out, A7B5_out, A7B6_2_out, A7B6_out, \平时作业1_全加器子电路_1_carry , \平时作业1_全加器子电路_1_sum ,
       \平时作业1_全加器子电路_3_carry , \平时作业1_全加器子电路_4_carry , \平时作业1_全加器子电路_4_sum , \平时作业1_全加器子电路_5_carry ,
       \平时作业1_全加器子电路_5_sum , \平时作业1_全加器子电路_6_carry , \平时作业1_全加器子电路_7_carry , \平时作业1_全加器子电路_7_sum ,
       \平时作业1_全加器子电路_8_carry , \平时作业1_全加器子电路_9_carry , \平时作业1_全加器子电路_9_sum , \平时作业1_全加器子电路_10_carry ,
       \平时作业1_全加器子电路_10_sum , \平时作业1_全加器子电路_11_carry , \平时作业1_全加器子电路_12_carry , \平时作业1_全加器子电路_12_sum ,
       \平时作业1_全加器子电路_13_carry , \平时作业1_全加器子电路_13_sum , \平时作业1_全加器子电路_14_carry , \平时作业1_全加器子电路_14_sum ,
       \平时作业1_全加器子电路_15_carry , \平时作业1_全加器子电路_15_sum , \平时作业1_全加器子电路_16_carry , \平时作业1_全加器子电路_16_sum ,
       \平时作业1_全加器子电路_17_carry , \平时作业1_全加器子电路_17_sum , \平时作业1_全加器子电路_18_carry , \平时作业1_全加器子电路_19_carry ,
       \平时作业1_全加器子电路_19_sum , \平时作业1_全加器子电路_20_carry , \平时作业1_全加器子电路_20_sum , \平时作业1_全加器子电路_21_carry ,
       \平时作业1_全加器子电路_21_sum , \平时作业1_全加器子电路_22_carry , \平时作业1_全加器子电路_22_sum , \平时作业1_全加器子电路_23_carry ,
       \平时作业1_全加器子电路_24_carry , \平时作业1_全加器子电路_24_sum , \平时作业1_全加器子电路_25_carry , \平时作业1_全加器子电路_25_sum ,
       \平时作业1_全加器子电路_26_carry , \平时作业1_全加器子电路_26_sum , \平时作业1_全加器子电路_27_carry , \平时作业1_全加器子电路_27_sum ,
       \平时作业1_全加器子电路_28_carry , \平时作业1_全加器子电路_29_carry , \平时作业1_全加器子电路_29_sum , \平时作业1_全加器子电路_30_carry ,
       \平时作业1_全加器子电路_30_sum , \平时作业1_全加器子电路_31_carry , \平时作业1_全加器子电路_31_sum , \平时作业1_全加器子电路_32_carry ,
       \平时作业1_全加器子电路_32_sum , \平时作业1_全加器子电路_33_carry , \平时作业1_全加器子电路_33_sum , \平时作业1_全加器子电路_34_carry ,
       \平时作业1_全加器子电路_34_sum , \平时作业1_全加器子电路_35_carry , \平时作业1_全加器子电路_35_sum , \平时作业1_全加器子电路_36_carry ,
       \平时作业1_全加器子电路_36_sum , \平时作业1_全加器子电路_37_carry , \平时作业1_全加器子电路_37_sum , \平时作业1_全加器子电路_38_carry ,
       \平时作业1_全加器子电路_38_sum , \平时作业1_全加器子电路_39_carry , \平时作业1_全加器子电路_39_sum , \平时作业1_全加器子电路_40_carry ,
       \平时作业1_全加器子电路_41_carry , \平时作业1_全加器子电路_41_sum , \平时作业1_全加器子电路_42_carry , \平时作业1_全加器子电路_42_sum ,
       \平时作业1_全加器子电路_43_carry , \平时作业1_全加器子电路_43_sum , \平时作业1_全加器子电路_44_carry , \平时作业1_全加器子电路_44_sum ,
       \平时作业1_全加器子电路_45_carry , \平时作业1_全加器子电路_46_carry , \平时作业1_全加器子电路_46_sum , \平时作业1_全加器子电路_47_carry ,
       \平时作业1_全加器子电路_48_carry , \平时作业1_全加器子电路_48_sum , \平时作业1_全加器子电路_49_carry , \平时作业1_全加器子电路_49_sum ,
       \平时作业1_全加器子电路_50_carry , \平时作业1_全加器子电路_50_sum , \平时作业1_全加器子电路_51_carry , \平时作业1_全加器子电路_51_sum ,
       \平时作业1_全加器子电路_52_carry , \平时作业1_全加器子电路_52_sum , \平时作业1_全加器子电路_53_carry , \平时作业1_全加器子电路_54_carry ,
       \平时作业1_全加器子电路_54_sum , \平时作业1_全加器子电路_55_carry , \平时作业1_全加器子电路_56_carry ;

  \平时作业1_全加器子电路  \u_平时作业1_全加器子电路_1  (
    .x(A7B6_2_out), .y(\平时作业1_全加器子电路_4_carry ), .Cin(\平时作业1_全加器子电路_5_carry ), .Carry(\平时作业1_全加器子电路_1_carry ),
    .sum(\平时作业1_全加器子电路_1_sum ));
  and A7B6 (A7B6_out, A[7], B[7]);
  \平时作业1_全加器子电路  \u_平时作业1_全加器子电路_2  (
    .x(A7B6_out), .y(\平时作业1_全加器子电路_1_carry ), .Cin(\平时作业1_全加器子电路_3_carry ), .Carry(\结果 [15]), .sum(\结果 [14]));
  and A6B6 (A6B6_out, A[6], B[7]);
  \平时作业1_全加器子电路  \u_平时作业1_全加器子电路_3  (
    .x(\平时作业1_全加器子电路_1_sum ), .y(A6B6_out), .Cin(\平时作业1_全加器子电路_6_carry ), .Carry(\平时作业1_全加器子电路_3_carry ),
    .sum(\结果 [13]));
  \平时作业1_全加器子电路  \u_平时作业1_全加器子电路_4  (
    .x(A7B5_out), .y(\平时作业1_全加器子电路_9_carry ), .Cin(\平时作业1_全加器子电路_10_carry ), .Carry(\平时作业1_全加器子电路_4_carry ),
    .sum(\平时作业1_全加器子电路_4_sum ));
  and A6B6_2 (A6B6_2_out, A[6], B[6]);
  and A7B6_2 (A7B6_2_out, A[7], B[6]);
  \平时作业1_全加器子电路  \u_平时作业1_全加器子电路_5  (
    .x(\平时作业1_全加器子电路_4_sum ), .y(A6B6_2_out), .Cin(\平时作业1_全加器子电路_7_carry ), .Carry(\平时作业1_全加器子电路_5_carry ),
    .sum(\平时作业1_全加器子电路_5_sum ));
  and A5B6 (A5B6_out, A[5], B[7]);
  \平时作业1_全加器子电路  \u_平时作业1_全加器子电路_6  (
    .x(\平时作业1_全加器子电路_5_sum ), .y(A5B6_out), .Cin(\平时作业1_全加器子电路_8_carry ), .Carry(\平时作业1_全加器子电路_6_carry ),
    .sum(\结果 [12]));
  // Probe on B
  and A7B5 (A7B5_out, A[7], B[5]);
  and A6B5 (A6B5_out, A[6], B[5]);
  and A5B6_2 (A5B6_2_out, A[5], B[6]);
  \平时作业1_全加器子电路  \u_平时作业1_全加器子电路_7  (
    .x(\平时作业1_全加器子电路_10_sum ), .y(A5B6_2_out), .Cin(\平时作业1_全加器子电路_17_carry ), .Carry(\平时作业1_全加器子电路_7_carry ),
    .sum(\平时作业1_全加器子电路_7_sum ));
  and A4B6 (A4B6_out, A[4], B[7]);
  \平时作业1_全加器子电路  \u_平时作业1_全加器子电路_8  (
    .x(\平时作业1_全加器子电路_7_sum ), .y(A4B6_out), .Cin(\平时作业1_全加器子电路_11_carry ), .Carry(\平时作业1_全加器子电路_8_carry ),
    .sum(\结果 [11]));
  and A7B4 (A7B4_out, A[7], B[4]);
  \平时作业1_全加器子电路  \u_平时作业1_全加器子电路_9  (
    .x(A7B4_out), .y(\平时作业1_全加器子电路_14_carry ), .Cin(\平时作业1_全加器子电路_15_carry ), .Carry(\平时作业1_全加器子电路_9_carry ),
    .sum(\平时作业1_全加器子电路_9_sum ));
  \平时作业1_全加器子电路  \u_平时作业1_全加器子电路_10  (
    .x(\平时作业1_全加器子电路_9_sum ), .y(A6B5_out), .Cin(\平时作业1_全加器子电路_16_carry ), .Carry(\平时作业1_全加器子电路_10_carry ),
    .sum(\平时作业1_全加器子电路_10_sum ));
  and A4B6_2 (A4B6_2_out, A[4], B[6]);
  and A3B6 (A3B6_out, A[3], B[7]);
  \平时作业1_全加器子电路  \u_平时作业1_全加器子电路_11  (
    .x(\平时作业1_全加器子电路_17_sum ), .y(A3B6_out), .Cin(\平时作业1_全加器子电路_18_carry ), .Carry(\平时作业1_全加器子电路_11_carry ),
    .sum(\结果 [10]));
  \平时作业1_全加器子电路  \u_平时作业1_全加器子电路_12  (
    .x(in_1), .y(A7B1_out), .Cin(\平时作业1_全加器子电路_34_carry ), .Carry(\平时作业1_全加器子电路_12_carry ),
    .sum(\平时作业1_全加器子电路_12_sum ));
  \平时作业1_全加器子电路  \u_平时作业1_全加器子电路_13  (
    .x(\平时作业1_全加器子电路_12_carry ), .y(A7B2_out), .Cin(\平时作业1_全加器子电路_29_carry ),
    .Carry(\平时作业1_全加器子电路_13_carry ), .sum(\平时作业1_全加器子电路_13_sum ));
  and A7B3 (A7B3_out, A[7], B[3]);
  \平时作业1_全加器子电路  \u_平时作业1_全加器子电路_14  (
    .x(\平时作业1_全加器子电路_13_carry ), .y(A7B3_out), .Cin(\平时作业1_全加器子电路_19_carry ),
    .Carry(\平时作业1_全加器子电路_14_carry ), .sum(\平时作业1_全加器子电路_14_sum ));
  and A6B4 (A6B4_out, A[6], B[4]);
  \平时作业1_全加器子电路  \u_平时作业1_全加器子电路_15  (
    .x(\平时作业1_全加器子电路_14_sum ), .y(A6B4_out), .Cin(\平时作业1_全加器子电路_20_carry ), .Carry(\平时作业1_全加器子电路_15_carry ),
    .sum(\平时作业1_全加器子电路_15_sum ));
  and A5B5 (A5B5_out, A[5], B[5]);
  \平时作业1_全加器子电路  \u_平时作业1_全加器子电路_16  (
    .x(\平时作业1_全加器子电路_15_sum ), .y(A5B5_out), .Cin(\平时作业1_全加器子电路_21_carry ), .Carry(\平时作业1_全加器子电路_16_carry ),
    .sum(\平时作业1_全加器子电路_16_sum ));
  and A3B6_2 (A3B6_2_out, A[3], B[6]);
  \平时作业1_全加器子电路  \u_平时作业1_全加器子电路_17  (
    .x(\平时作业1_全加器子电路_16_sum ), .y(A4B6_2_out), .Cin(\平时作业1_全加器子电路_22_carry ),
    .Carry(\平时作业1_全加器子电路_17_carry ), .sum(\平时作业1_全加器子电路_17_sum ));
  and A2B6 (A2B6_out, A[2], B[7]);
  \平时作业1_全加器子电路  \u_平时作业1_全加器子电路_18  (
    .x(\平时作业1_全加器子电路_22_sum ), .y(A2B6_out), .Cin(\平时作业1_全加器子电路_23_carry ), .Carry(\平时作业1_全加器子电路_18_carry ),
    .sum(\结果 [9]));
  // Probe on A
  and A6B3 (A6B3_out, A[6], B[3]);
  \平时作业1_全加器子电路  \u_平时作业1_全加器子电路_19  (
    .x(\平时作业1_全加器子电路_13_sum ), .y(A6B3_out), .Cin(\平时作业1_全加器子电路_24_carry ), .Carry(\平时作业1_全加器子电路_19_carry ),
    .sum(\平时作业1_全加器子电路_19_sum ));
  and A5B4 (A5B4_out, A[5], B[4]);
  \平时作业1_全加器子电路  \u_平时作业1_全加器子电路_20  (
    .x(\平时作业1_全加器子电路_19_sum ), .y(A5B4_out), .Cin(\平时作业1_全加器子电路_25_carry ), .Carry(\平时作业1_全加器子电路_20_carry ),
    .sum(\平时作业1_全加器子电路_20_sum ));
  and A4B5 (A4B5_out, A[4], B[5]);
  \平时作业1_全加器子电路  \u_平时作业1_全加器子电路_21  (
    .x(\平时作业1_全加器子电路_20_sum ), .y(A4B5_out), .Cin(\平时作业1_全加器子电路_26_carry ), .Carry(\平时作业1_全加器子电路_21_carry ),
    .sum(\平时作业1_全加器子电路_21_sum ));
  and A2B6_2 (A2B6_2_out, A[2], B[6]);
  \平时作业1_全加器子电路  \u_平时作业1_全加器子电路_22  (
    .x(\平时作业1_全加器子电路_21_sum ), .y(A3B6_2_out), .Cin(\平时作业1_全加器子电路_27_carry ),
    .Carry(\平时作业1_全加器子电路_22_carry ), .sum(\平时作业1_全加器子电路_22_sum ));
  and A1B6 (A1B6_out, A[1], B[7]);
  \平时作业1_全加器子电路  \u_平时作业1_全加器子电路_23  (
    .x(\平时作业1_全加器子电路_27_sum ), .y(A1B6_out), .Cin(\平时作业1_全加器子电路_28_carry ), .Carry(\平时作业1_全加器子电路_23_carry ),
    .sum(\结果 [8]));
  and A6B2 (A6B2_out, B[2], A[6]);
  and A7B2 (A7B2_out, A[7], B[2]);
  and A5B3 (A5B3_out, A[5], B[3]);
  \平时作业1_全加器子电路  \u_平时作业1_全加器子电路_24  (
    .x(\平时作业1_全加器子电路_29_sum ), .y(A5B3_out), .Cin(\平时作业1_全加器子电路_30_carry ), .Carry(\平时作业1_全加器子电路_24_carry ),
    .sum(\平时作业1_全加器子电路_24_sum ));
  and A4B4 (A4B4_out, A[4], B[4]);
  \平时作业1_全加器子电路  \u_平时作业1_全加器子电路_25  (
    .x(\平时作业1_全加器子电路_24_sum ), .y(A4B4_out), .Cin(\平时作业1_全加器子电路_31_carry ), .Carry(\平时作业1_全加器子电路_25_carry ),
    .sum(\平时作业1_全加器子电路_25_sum ));
  and A3B5 (A3B5_out, A[3], B[5]);
  \平时作业1_全加器子电路  \u_平时作业1_全加器子电路_26  (
    .x(\平时作业1_全加器子电路_25_sum ), .y(A3B5_out), .Cin(\平时作业1_全加器子电路_32_carry ), .Carry(\平时作业1_全加器子电路_26_carry ),
    .sum(\平时作业1_全加器子电路_26_sum ));
  and A1B6_2 (A1B6_2_out, A[1], B[6]);
  \平时作业1_全加器子电路  \u_平时作业1_全加器子电路_27  (
    .x(\平时作业1_全加器子电路_26_sum ), .y(A2B6_2_out), .Cin(\平时作业1_全加器子电路_33_carry ),
    .Carry(\平时作业1_全加器子电路_27_carry ), .sum(\平时作业1_全加器子电路_27_sum ));
  and A0B6 (A0B6_out, A[0], B[7]);
  \平时作业1_全加器子电路  \u_平时作业1_全加器子电路_28  (
    .x(\平时作业1_全加器子电路_33_sum ), .y(A0B6_out), .Cin(in_8), .Carry(\平时作业1_全加器子电路_28_carry ), .sum(\结果 [7]));
  // Probe on \结果 
  and A7B1 (A7B1_out, A[7], B[1]);
  and A5B2 (A5B2_out, B[2], A[5]);
  \平时作业1_全加器子电路  \u_平时作业1_全加器子电路_29  (
    .x(\平时作业1_全加器子电路_12_sum ), .y(A6B2_out), .Cin(\平时作业1_全加器子电路_36_carry ), .Carry(\平时作业1_全加器子电路_29_carry ),
    .sum(\平时作业1_全加器子电路_29_sum ));
  and A4B3 (A4B3_out, A[4], B[3]);
  \平时作业1_全加器子电路  \u_平时作业1_全加器子电路_30  (
    .x(\平时作业1_全加器子电路_36_sum ), .y(A4B3_out), .Cin(\平时作业1_全加器子电路_37_carry ), .Carry(\平时作业1_全加器子电路_30_carry ),
    .sum(\平时作业1_全加器子电路_30_sum ));
  and A3B4 (A3B4_out, A[3], B[4]);
  \平时作业1_全加器子电路  \u_平时作业1_全加器子电路_31  (
    .x(\平时作业1_全加器子电路_30_sum ), .y(A3B4_out), .Cin(\平时作业1_全加器子电路_38_carry ), .Carry(\平时作业1_全加器子电路_31_carry ),
    .sum(\平时作业1_全加器子电路_31_sum ));
  and A2B5 (A2B5_out, A[2], B[5]);
  \平时作业1_全加器子电路  \u_平时作业1_全加器子电路_32  (
    .x(\平时作业1_全加器子电路_31_sum ), .y(A2B5_out), .Cin(\平时作业1_全加器子电路_39_carry ), .Carry(\平时作业1_全加器子电路_32_carry ),
    .sum(\平时作业1_全加器子电路_32_sum ));
  and A0B6_2 (A0B6_2_out, A[0], B[6]);
  \平时作业1_全加器子电路  \u_平时作业1_全加器子电路_33  (
    .x(\平时作业1_全加器子电路_32_sum ), .y(A1B6_2_out), .Cin(\平时作业1_全加器子电路_40_carry ),
    .Carry(\平时作业1_全加器子电路_33_carry ), .sum(\平时作业1_全加器子电路_33_sum ));
  and A7B0 (A7B0_out, A[7], B[0]);
  and A5B1 (A5B1_out, B[1], A[5]);
  and A6B1 (A6B1_out, A[6], B[1]);
  \平时作业1_全加器子电路  \u_平时作业1_全加器子电路_34  (
    .x(A7B0_out), .y(A6B1_out), .Cin(\平时作业1_全加器子电路_41_carry ), .Carry(\平时作业1_全加器子电路_34_carry ),
    .sum(\平时作业1_全加器子电路_34_sum ));
  and A4B2 (A4B2_out, B[2], A[4]);
  \平时作业1_全加器子电路  \u_平时作业1_全加器子电路_35  (
    .x(\平时作业1_全加器子电路_41_sum ), .y(A4B2_out), .Cin(\平时作业1_全加器子电路_42_carry ), .Carry(\平时作业1_全加器子电路_35_carry ),
    .sum(\平时作业1_全加器子电路_35_sum ));
  \平时作业1_全加器子电路  \u_平时作业1_全加器子电路_36  (
    .x(\平时作业1_全加器子电路_34_sum ), .y(A5B2_out), .Cin(\平时作业1_全加器子电路_35_carry ), .Carry(\平时作业1_全加器子电路_36_carry ),
    .sum(\平时作业1_全加器子电路_36_sum ));
  and A3B3 (A3B3_out, A[3], B[3]);
  \平时作业1_全加器子电路  \u_平时作业1_全加器子电路_37  (
    .x(\平时作业1_全加器子电路_35_sum ), .y(A3B3_out), .Cin(\平时作业1_全加器子电路_43_carry ), .Carry(\平时作业1_全加器子电路_37_carry ),
    .sum(\平时作业1_全加器子电路_37_sum ));
  and A2B4 (A2B4_out, A[2], B[4]);
  \平时作业1_全加器子电路  \u_平时作业1_全加器子电路_38  (
    .x(\平时作业1_全加器子电路_37_sum ), .y(A2B4_out), .Cin(\平时作业1_全加器子电路_44_carry ), .Carry(\平时作业1_全加器子电路_38_carry ),
    .sum(\平时作业1_全加器子电路_38_sum ));
  and A1B5 (A1B5_out, A[1], B[5]);
  \平时作业1_全加器子电路  \u_平时作业1_全加器子电路_39  (
    .x(\平时作业1_全加器子电路_38_sum ), .y(A1B5_out), .Cin(\平时作业1_全加器子电路_45_carry ), .Carry(\平时作业1_全加器子电路_39_carry ),
    .sum(\平时作业1_全加器子电路_39_sum ));
  \平时作业1_全加器子电路  \u_平时作业1_全加器子电路_40  (
    .x(\平时作业1_全加器子电路_39_sum ), .y(A0B6_2_out), .Cin(in_7), .Carry(\平时作业1_全加器子电路_40_carry ), .sum(\结果 [6]));
  and A6B0 (A6B0_out, A[6], B[0]);
  and A4B1 (A4B1_out, B[1], A[4]);
  \平时作业1_全加器子电路  \u_平时作业1_全加器子电路_41  (
    .x(A6B0_out), .y(A5B1_out), .Cin(\平时作业1_全加器子电路_46_carry ), .Carry(\平时作业1_全加器子电路_41_carry ),
    .sum(\平时作业1_全加器子电路_41_sum ));
  and A3B2 (A3B2_out, A[3], B[2]);
  \平时作业1_全加器子电路  \u_平时作业1_全加器子电路_42  (
    .x(\平时作业1_全加器子电路_46_sum ), .y(A3B2_out), .Cin(\平时作业1_全加器子电路_49_carry ), .Carry(\平时作业1_全加器子电路_42_carry ),
    .sum(\平时作业1_全加器子电路_42_sum ));
  and A2B3 (A2B3_out, A[2], B[3]);
  \平时作业1_全加器子电路  \u_平时作业1_全加器子电路_43  (
    .x(\平时作业1_全加器子电路_42_sum ), .y(A2B3_out), .Cin(\平时作业1_全加器子电路_50_carry ), .Carry(\平时作业1_全加器子电路_43_carry ),
    .sum(\平时作业1_全加器子电路_43_sum ));
  and A1B4 (A1B4_out, A[1], B[4]);
  \平时作业1_全加器子电路  \u_平时作业1_全加器子电路_44  (
    .x(\平时作业1_全加器子电路_43_sum ), .y(A1B4_out), .Cin(\平时作业1_全加器子电路_47_carry ), .Carry(\平时作业1_全加器子电路_44_carry ),
    .sum(\平时作业1_全加器子电路_44_sum ));
  and A0B5 (A0B5_out, A[0], B[5]);
  \平时作业1_全加器子电路  \u_平时作业1_全加器子电路_45  (
    .x(\平时作业1_全加器子电路_44_sum ), .y(A0B5_out), .Cin(in_6), .Carry(\平时作业1_全加器子电路_45_carry ), .sum(\结果 [5]));
  and A5B0 (A5B0_out, A[5], B[0]);
  \平时作业1_全加器子电路  \u_平时作业1_全加器子电路_46  (
    .x(A5B0_out), .y(A4B1_out), .Cin(\平时作业1_全加器子电路_48_carry ), .Carry(\平时作业1_全加器子电路_46_carry ),
    .sum(\平时作业1_全加器子电路_46_sum ));
  and A1B3 (A1B3_out, A[1], B[3]);
  and A0B4 (A0B4_out, A[0], B[4]);
  \平时作业1_全加器子电路  \u_平时作业1_全加器子电路_47  (
    .x(\平时作业1_全加器子电路_50_sum ), .y(A0B4_out), .Cin(in_5), .Carry(\平时作业1_全加器子电路_47_carry ), .sum(\结果 [4]));
  and A3B1 (A3B1_out, B[1], A[3]);
  and A4B0 (A4B0_out, A[4], B[0]);
  \平时作业1_全加器子电路  \u_平时作业1_全加器子电路_48  (
    .x(A4B0_out), .y(A3B1_out), .Cin(\平时作业1_全加器子电路_51_carry ), .Carry(\平时作业1_全加器子电路_48_carry ),
    .sum(\平时作业1_全加器子电路_48_sum ));
  and A2B2 (A2B2_out, A[2], B[2]);
  \平时作业1_全加器子电路  \u_平时作业1_全加器子电路_49  (
    .x(\平时作业1_全加器子电路_48_sum ), .y(A2B2_out), .Cin(\平时作业1_全加器子电路_52_carry ), .Carry(\平时作业1_全加器子电路_49_carry ),
    .sum(\平时作业1_全加器子电路_49_sum ));
  and A0B3 (A0B3_out, A[0], B[3]);
  \平时作业1_全加器子电路  \u_平时作业1_全加器子电路_50  (
    .x(\平时作业1_全加器子电路_49_sum ), .y(A1B3_out), .Cin(\平时作业1_全加器子电路_53_carry ), .Carry(\平时作业1_全加器子电路_50_carry ),
    .sum(\平时作业1_全加器子电路_50_sum ));
  and A2B1 (A2B1_out, B[1], A[2]);
  and A3B0 (A3B0_out, A[3], B[0]);
  \平时作业1_全加器子电路  \u_平时作业1_全加器子电路_51  (
    .x(A3B0_out), .y(A2B1_out), .Cin(\平时作业1_全加器子电路_54_carry ), .Carry(\平时作业1_全加器子电路_51_carry ),
    .sum(\平时作业1_全加器子电路_51_sum ));
  and A0B2 (A0B2_out, B[2], A[0]);
  and A1B2 (A1B2_out, A[1], B[2]);
  \平时作业1_全加器子电路  \u_平时作业1_全加器子电路_52  (
    .x(\平时作业1_全加器子电路_51_sum ), .y(A1B2_out), .Cin(\平时作业1_全加器子电路_55_carry ), .Carry(\平时作业1_全加器子电路_52_carry ),
    .sum(\平时作业1_全加器子电路_52_sum ));
  \平时作业1_全加器子电路  \u_平时作业1_全加器子电路_53  (
    .x(\平时作业1_全加器子电路_52_sum ), .y(A0B3_out), .Cin(in_4), .Carry(\平时作业1_全加器子电路_53_carry ), .sum(\结果 [3]));
  and A1B1 (A1B1_out, B[1], A[1]);
  and A2B0 (A2B0_out, B[0], A[2]);
  \平时作业1_全加器子电路  \u_平时作业1_全加器子电路_54  (
    .x(A2B0_out), .y(A1B1_out), .Cin(\平时作业1_全加器子电路_56_carry ), .Carry(\平时作业1_全加器子电路_54_carry ),
    .sum(\平时作业1_全加器子电路_54_sum ));
  \平时作业1_全加器子电路  \u_平时作业1_全加器子电路_55  (
    .x(\平时作业1_全加器子电路_54_sum ), .y(A0B2_out), .Cin(in_3), .Carry(\平时作业1_全加器子电路_55_carry ), .sum(\结果 [2]));
  and A0B1 (A0B1_out, B[1], A[0]);
  \平时作业1_全加器子电路  \u_平时作业1_全加器子电路_56  (
    .x(A1B0_out), .y(A0B1_out), .Cin(in_2), .Carry(\平时作业1_全加器子电路_56_carry ), .sum(\结果 [1]));
  and A1B0 (A1B0_out, B[0], A[1]);
  and A0B0 (\结果 [0], B[0], A[0]);

  // Notes on the sheet:
  //   X
  //   =
endmodule

module \实验二乘法控制器_Moore型状态机  (
  input  Start,
  input  B,
  input  B0,
  input  CLK,
  input  Reset,
  output Enable,
  output LoadA,
  output LoadB,
  output Done,
  output ShiftA,
  output ShiftB
);

  wire and_1_out, and_2_out, and_3_out, and_5_out, and_6_out, and_8_out, and_9_out, and_10_out, and_11_out;
  wire [2:0] or_1_out, register_1_q;

  and and_1 (and_1_out, ~register_1_q[2], ~register_1_q[1], register_1_q[0], Start, B, B0);  // AND_Gate
  and and_2 (and_2_out, ~register_1_q[2], register_1_q[1]);  // AND_Gate
  and and_3 (and_3_out, ~register_1_q[2], ~register_1_q[1], ~register_1_q[0], Start);  // AND_Gate
  and and_4 (or_1_out[1], ~register_1_q[2], ~register_1_q[1], register_1_q[0], Start, B);  // AND_Gate
  and and_5 (and_5_out, ~register_1_q[2], ~register_1_q[1], register_1_q[0], Start, ~B);  // AND_Gate
  and and_6 (and_6_out, register_1_q[2], ~register_1_q[1], ~register_1_q[0]);  // AND_Gate
  or or_1 (or_1_out[0], and_1_out, and_2_out, and_3_out);
  or or_2 (or_1_out[2], and_5_out, and_6_out);
  Register #(.width(3), .trigger("rising"), .Select("low")) register_1 (
    .D(or_1_out), .Q(register_1_q), .clk(CLK), .clr(Reset));  // open: en
  and and_7 (Enable, ~register_1_q[2], register_1_q[1], register_1_q[0]);  // AND_Gate
  and and_8 (and_8_out, ~register_1_q[2], ~register_1_q[1], ~register_1_q[0]);  // AND_Gate
  and and_9 (and_9_out, register_1_q[1], ~register_1_q[2]);  // AND_Gate
  and and_10 (and_10_out, ~register_1_q[2], ~register_1_q[1], ~register_1_q[0]);  // AND_Gate
  and and_11 (and_11_out, register_1_q[1], ~register_1_q[2]);  // AND_Gate
  and and_12 (Done, register_1_q[2], ~register_1_q[1], ~register_1_q[0]);  // AND_Gate
  and and_13 (ShiftA, ~register_1_q[2], register_1_q[1]);  // AND_Gate
  and and_14 (ShiftB, ~register_1_q[2], register_1_q[1]);  // AND_Gate
  or or_3 (LoadA, and_8_out, and_9_out);
  or or_4 (LoadB, and_10_out, and_11_out);
endmodule

module \实验二单精度定点乘法器  (
  input  [7:0] A,
  input  [7:0] B,
  input  in_3,
  output [15:0] C
);

  wire bitselector_1_out, bitselector_2_out, bitselector_3_out, CLK, clock_1_out, comparator_1_eq, Done,
       not_1_out, Reset, xor_1_out, \实验二乘法控制器_moore型状态机_1_enable , \实验二乘法控制器_moore型状态机_1_loada ,
       \实验二乘法控制器_moore型状态机_1_loadb , \实验二乘法控制器_moore型状态机_1_shifta , \实验二乘法控制器_moore型状态机_1_shiftb ;
  wire [7:0] multiplexer_1_out, multiplexer_4_out, multiplexer_5_out, negator_1_out, negator_2_out,
       register_3_q, shifter_2_out;
  wire [15:0] adder_1_out, bit_extender_1_out, multiplexer_2_out, multiplexer_3_out, negator_3_out,
       register_1_q, register_2_q, shifter_1_out;

  Negator #(.width(8)) negator_1 (.in(A), .out(negator_1_out));
  BitSelector #(.width(8), .group(1)) bitselector_1 (.in(A), .out(bitselector_1_out), .sel(3'b111));
  Multiplexer #(.select(1), .width(8), .disabled("Z"), .enable("false")) multiplexer_1 (
    .in0(A), .in1(negator_1_out), .out(multiplexer_1_out), .sel(bitselector_1_out));
  LED #(.active("true")) led_1 (.in(Done));
  assign bit_extender_1_out = {{8{1'b0}}, multiplexer_1_out};  // Bit_Extender bit_extender_1
  Multiplexer #(.select(1), .width(16), .disabled("Z"), .enable("false")) multiplexer_2 (
    .in0(bit_extender_1_out), .in1(shifter_1_out), .out(multiplexer_2_out),
    .sel(\实验二乘法控制器_moore型状态机_1_shifta ));
  xor xor_1 (xor_1_out, bitselector_2_out, bitselector_1_out);
  // Probe on A
  Negator #(.width(8)) negator_2 (.in(B), .out(negator_2_out));
  BitSelector #(.width(8), .group(1)) bitselector_2 (.in(B), .out(bitselector_2_out), .sel(3'b111));
  Register #(.width(16), .trigger("rising"), .Select("low")) register_1 (
    .D(multiplexer_2_out), .en(\实验二乘法控制器_moore型状态机_1_loada ), .Q(register_1_q), .clk(CLK), .clr(Reset));
  Multiplexer #(.select(1), .width(16), .disabled("Z"), .enable("false")) multiplexer_3 (
    .in1(register_2_q), .out(multiplexer_3_out), .sel(Done));  // open: in0
  // Probe on B
  Multiplexer #(.select(1), .width(8), .disabled("Z"), .enable("false")) multiplexer_4 (
    .in0(B), .in1(negator_2_out), .out(multiplexer_4_out), .sel(bitselector_2_out));
  Shifter #(.width(16), .shift("ll")) shifter_1 (.in(register_1_q), .\dist (4'b0001), .out(shifter_1_out));
  Adder #(.width(16)) adder_1 (.a(register_2_q), .b(register_1_q), .out(adder_1_out));  // open: cin, cout
  Register #(.width(16), .trigger("rising"), .Select("low")) register_2 (
    .D(adder_1_out), .en(\实验二乘法控制器_moore型状态机_1_enable ), .Q(register_2_q), .clk(CLK), .clr(Reset));
  // Probe on C
  Multiplexer #(.select(1), .width(8), .disabled("Z"), .enable("false")) multiplexer_5 (
    .in0(multiplexer_4_out), .in1(shifter_2_out), .out(multiplexer_5_out), .sel(\实验二乘法控制器_moore型状态机_1_shiftb ));
  Register #(.width(8), .trigger("rising"), .Select("low")) register_3 (
    .D(multiplexer_5_out), .en(\实验二乘法控制器_moore型状态机_1_loadb ), .Q(register_3_q), .clk(CLK), .clr(Reset));
  Negator #(.width(16)) negator_3 (.in(multiplexer_3_out), .out(negator_3_out));
  Shifter #(.width(8), .shift("lr")) shifter_2 (.in(register_3_q), .\dist (3'b001), .out(shifter_2_out));
  Comparator #(.width(8), .mode("twosComplement")) comparator_1 (
    .a(register_3_q), .b({8{1'b0}}), .eq(comparator_1_eq));  // open: gt, lt
  Multiplexer #(.select(1), .width(16), .disabled("Z"), .enable("false")) multiplexer_6 (
    .in0(multiplexer_3_out), .in1(negator_3_out), .out(C), .sel(xor_1_out));
  BitSelector #(.width(8), .group(1)) bitselector_3 (.in(register_3_q), .out(bitselector_3_out), .sel(3'b000));
  not not_1 (not_1_out, comparator_1_eq);
  \实验二乘法控制器_Moore型状态机  \u_实验二乘法控制器_moore型状态机_1  (
    .Start(in_3), .B(not_1_out), .B0(bitselector_3_out), .CLK(CLK), .Reset(Reset),
    .Enable(\实验二乘法控制器_moore型状态机_1_enable ), .LoadA(\实验二乘法控制器_moore型状态机_1_loada ),
    .LoadB(\实验二乘法控制器_moore型状态机_1_loadb ), .Done(Done), .ShiftA(\实验二乘法控制器_moore型状态机_1_shifta ),
    .ShiftB(\实验二乘法控制器_moore型状态机_1_shiftb ));
  Clock #(.highDuration(1), .lowDuration(1)) clock_1 (.out(clock_1_out));
  and and_1 (CLK, clock_1_out, in_3);
  Button button_1 (.out(Reset));

  // Other names for the same wires on the sheet: Start = in_3

  // Notes on the sheet:
  //   显示区
  //   X
  //   =
endmodule

module \实验二快速乘法器  (
  input  [7:0] in_1,
  input  [7:0] in_2,
  output [15:0] out_3
);

  wire bitselector_1_out, bitselector_2_out, CLK, Restart, Start, xor_1_out;
  wire [1:0] bitselector_3_out;
  wire [7:0] counter_1_q, multiplexer_1_out, multiplexer_2_out, negator_1_out, negator_2_out;
  wire [15:0] adder_1_out, adder_2_out, bit_extender_1_out, bit_extender_2_out, multiplexer_3_out,
       multiplexer_4_out, multiplexer_5_out, negator_3_out, register_1_q, register_2_q, register_3_q,
       shifter_1_out, shifter_2_out, shifter_3_out;

  Negator #(.width(8)) negator_1 (.in(in_1), .out(negator_1_out));
  BitSelector #(.width(8), .group(1)) bitselector_1 (.in(in_1), .out(bitselector_1_out), .sel(3'b111));
  Multiplexer #(.select(1), .width(8), .disabled("Z"), .enable("false")) multiplexer_1 (
    .in0(in_1), .in1(negator_1_out), .out(multiplexer_1_out), .sel(bitselector_1_out));
  Negator #(.width(8)) negator_2 (.in(in_2), .out(negator_2_out));
  BitSelector #(.width(8), .group(1)) bitselector_2 (.in(in_2), .out(bitselector_2_out), .sel(3'b111));
  Multiplexer #(.select(1), .width(8), .disabled("Z"), .enable("false")) multiplexer_2 (
    .in0(in_2), .in1(negator_2_out), .out(multiplexer_2_out), .sel(bitselector_2_out));
  assign bit_extender_1_out = {{8{1'b0}}, multiplexer_1_out};  // Bit_Extender bit_extender_1
  Multiplexer #(.select(1), .width(16), .disabled("Z"), .enable("false")) multiplexer_3 (
    .in0(bit_extender_1_out), .in1(shifter_1_out), .out(multiplexer_3_out), .sel(Start));
  Register #(.width(16), .trigger("rising"), .Select("low")) register_1 (
    .D(multiplexer_3_out), .Q(register_1_q), .clk(CLK), .clr(Restart));  // open: en
  assign bit_extender_2_out = {{8{1'b0}}, multiplexer_2_out};  // Bit_Extender bit_extender_2
  Multiplexer #(.select(1), .width(16), .disabled("Z"), .enable("false")) multiplexer_4 (
    .in0(bit_extender_2_out), .in1(shifter_3_out), .out(multiplexer_4_out), .sel(Start));
  Shifter #(.width(16), .shift("ll")) shifter_1 (.in(register_1_q), .\dist (4'b0010), .out(shifter_1_out));
  Register #(.width(16), .trigger("rising"), .Select("low")) register_2 (
    .D(multiplexer_4_out), .Q(register_2_q), .clk(CLK), .clr(Restart));  // open: en
  // Probe on in_1
  Shifter #(.width(16), .shift("ll")) shifter_2 (.in(register_1_q), .\dist (4'b0001), .out(shifter_2_out));
  Adder #(.width(16)) adder_1 (.a(shifter_2_out), .b(register_1_q), .out(adder_1_out));  // open: cin, cout
  BitSelector #(.width(16), .group(2)) bitselector_3 (.in(register_2_q), .out(bitselector_3_out), .sel(3'b000));
  Shifter #(.width(16), .shift("lr")) shifter_3 (.in(register_2_q), .\dist (4'b0010), .out(shifter_3_out));
  // Probe on in_2
  // Probe on out_3
  Multiplexer #(.select(2), .width(16), .disabled("Z"), .enable("false")) multiplexer_5 (
    .in0({16{1'b0}}), .in1(register_1_q), .in2(shifter_2_out), .in3(adder_1_out), .out(multiplexer_5_out),
    .sel(bitselector_3_out));
  xor xor_1 (xor_1_out, bitselector_1_out, bitselector_2_out);
  Clock #(.highDuration(1), .lowDuration(1)) clock_1 (.out(CLK));
  Button button_1 (.out(Restart));
  Counter #(.width(8), .max('hff), .ongoal("wrap"), .trigger("rising"), .behavior("new")) counter_1 (
    .Q(counter_1_q), .clk(CLK), .clr(Restart));  // open: load, D, count, carry, preset, down
  Adder #(.width(16)) adder_2 (.a(multiplexer_5_out), .b(register_3_q), .out(adder_2_out));  // open: cin, cout
  Comparator #(.width(8), .mode("twosComplement")) comparator_1 (
    .a(counter_1_q), .b({8{1'b0}}), .gt(Start));  // open: eq, lt
  Register #(.width(16), .trigger("rising"), .Select("low")) register_3 (
    .D(adder_2_out), .Q(register_3_q), .clk(CLK), .clr(Restart));  // open: en
  Multiplexer #(.select(1), .width(16), .disabled("Z"), .enable("false")) multiplexer_6 (
    .in0(register_3_q), .in1(negator_3_out), .out(out_3), .sel(xor_1_out));
  Negator #(.width(16)) negator_3 (.in(register_3_q), .out(negator_3_out));

  // Notes on the sheet:
  //   被乘数B
  //   乘数C
  //   显示区
  //   x
  //   2B
  //   =
endmodule

module \实验三_ALU  (
  input  [31:0] X,
  input  [31:0] Y,
  input  [2:0] AluOP,
  output \结果是否为0 ,
  output [31:0] Result
);

  wire [24:0] \运算指示 ;

  // Probe on X
  // Probe on X
  // Probe on Y
  // Probe on Y
  // Probe on AluOP
  // Probe on Result
  // Probe on Result
  DotMatrix #(.inputtype("column"), .matrixcols(5), .matrixrows(5), .persist(0), .dotshape("square")) dotmatrix_1 (
    .col0(\运算指示 [24:20]), .col1(\运算指示 [19:15]), .col2(\运算指示 [14:10]), .col3(\运算指示 [9:5]), .col4(\运算指示 [4:0]));
  Multiplexer #(.select(3), .width(25), .disabled("Z"), .enable("false")) multiplexer_1 (
    .in0(25'h124081), .in1(25'h1020490), .in2(25'h427c84), .in3({25{1'b0}}), .in4(25'h124091),
    .in5(25'h1020490), .in6(25'h421084), .in7(25'h402811), .out(\运算指示 ), .sel(AluOP));

  // Other names for the same wires on the sheet: S[2:0] = AluOP; Zero = \结果是否为0 

  // Notes on the sheet:
  //   Y: pull=down
  //   X: pull=down
  //   AluOP: pull=down
  //   不要改变此引脚区域内容，也不要改变ALU封装形式
  //   请在下方利用上方输入输出引脚的隧道信号构建ALU电路，ctrl+d复制选择部件
  //   输入引脚
  //   探测区域
  //   输出引脚
  //   功能说明：
  //   000：X AND Y      100：X AND Y'
  //   001：X OR Y        101：X OR Y'  
  //   010：X + Y           110：X - Y  
  //   011：未使用         111：SLT  
endmodule

module \实验三_RAM  (
  input  CS,
  input  Store,
  input  CLK,
  input  [31:0] Address_Bus,
  input  [31:0] Data_Bus_In,
  input  Load,
  input  Clear,
  output [31:0] Data_Bus_Out
);

  wire nand_1_out, nand_2_out, nand_3_out, nand_4_out, nand_5_out, nand_6_out, nand_7_out, nand_8_out,
       nand_9_out, nand_10_out, nand_11_out, nand_12_out, nand_13_out, nand_14_out, nand_15_out, nand_16_out,
       nand_17_out, nand_18_out, nand_19_out, nand_20_out, nand_21_out, nand_22_out, nand_23_out,
       nand_24_out, nand_25_out, nand_26_out, nand_27_out, nand_28_out, nand_29_out, nand_30_out,
       nand_31_out, nand_32_out, nand_33_out, nand_34_out, nand_35_out, nand_36_out, nand_37_out,
       nand_38_out, nand_39_out, nand_40_out, nand_41_out, nand_42_out, nand_43_out, nand_44_out,
       nand_45_out, nand_46_out, nand_47_out, nand_48_out, nand_49_out, nand_50_out, nand_51_out,
       nand_52_out, nand_53_out, nand_54_out, nand_55_out, nand_56_out, nand_57_out, nand_58_out,
       nand_59_out, nand_60_out, nand_61_out, nand_62_out, nand_63_out, nand_64_out, undriven, undriven_2,
       undriven_3, undriven_4, undriven_5, undriven_6, undriven_7, undriven_8, undriven_9, undriven_10,
       undriven_11, undriven_12, undriven_13, undriven_14, undriven_15, undriven_17, undriven_18,
       undriven_19, undriven_20, undriven_21;
  wire [23:0] undriven_16;
  wire [31:0] ram_1_data, undriven_22;

  nand nand_1 (nand_1_out, undriven_9, undriven_8);
  nand nand_2 (nand_2_out, undriven_9, undriven_7);
  nand nand_3 (nand_3_out, undriven_9, undriven_6);
  nand nand_4 (nand_4_out, undriven_9, undriven_5);
  nand nand_5 (nand_5_out, undriven_9, undriven_4);
  nand nand_6 (nand_6_out, undriven_9, undriven_3);
  nand nand_7 (nand_7_out, undriven_9, undriven_2);
  nand nand_8 (nand_8_out, undriven_9, undriven);
  RAM #(.addrWidth(24), .dataWidth(32), .bus("separate"), .Select("low")) ram_1 (
    .addr(undriven_16), .din(undriven_22), .data(ram_1_data), .str(undriven_18), .sel(nand_1_out),
    .clk(undriven_20), .ld(undriven_21), .clr(undriven_19));
  RAM #(.addrWidth(24), .dataWidth(32), .bus("separate"), .Select("low")) ram_2 (
    .addr(undriven_16), .din(undriven_22), .data(ram_1_data), .str(undriven_18), .sel(nand_2_out),
    .clk(undriven_20), .ld(undriven_21), .clr(undriven_19));
  RAM #(.addrWidth(24), .dataWidth(32), .bus("separate"), .Select("low")) ram_3 (
    .addr(undriven_16), .din(undriven_22), .data(ram_1_data), .str(undriven_18), .sel(nand_3_out),
    .clk(undriven_20), .ld(undriven_21), .clr(undriven_19));
  RAM #(.addrWidth(24), .dataWidth(32), .bus("separate"), .Select("low")) ram_4 (
    .addr(undriven_16), .din(undriven_22), .data(ram_1_data), .str(undriven_18), .sel(nand_4_out),
    .clk(undriven_20), .ld(undriven_21), .clr(undriven_19));
  RAM #(.addrWidth(24), .dataWidth(32), .bus("separate"), .Select("low")) ram_5 (
    .addr(undriven_16), .din(undriven_22), .data(ram_1_data), .str(undriven_18), .sel(nand_5_out),
    .clk(undriven_20), .ld(undriven_21), .clr(undriven_19));
  RAM #(.addrWidth(24), .dataWidth(32), .bus("separate"), .Select("low")) ram_6 (
    .addr(undriven_16), .din(undriven_22), .data(ram_1_data), .str(undriven_18), .sel(nand_6_out),
    .clk(undriven_20), .ld(undriven_21), .clr(undriven_19));
  RAM #(.addrWidth(24), .dataWidth(32), .bus("separate"), .Select("low")) ram_7 (
    .addr(undriven_16), .din(undriven_22), .data(ram_1_data), .str(undriven_18), .sel(nand_7_out),
    .clk(undriven_20), .ld(undriven_21), .clr(undriven_19));
  RAM #(.addrWidth(24), .dataWidth(32), .bus("separate"), .Select("low")) ram_8 (
    .addr(undriven_16), .din(undriven_22), .data(ram_1_data), .str(undriven_18), .sel(nand_8_out),
    .clk(undriven_20), .ld(undriven_21), .clr(undriven_19));
  nand nand_9 (nand_9_out, undriven_10, undriven_8);
  nand nand_10 (nand_10_out, undriven_10, undriven_7);
  nand nand_11 (nand_11_out, undriven_10, undriven_6);
  nand nand_12 (nand_12_out, undriven_10, undriven_5);
  nand nand_13 (nand_13_out, undriven_10, undriven_4);
  nand nand_14 (nand_14_out, undriven_10, undriven_3);
  nand nand_15 (nand_15_out, undriven_10, undriven_2);
  nand nand_16 (nand_16_out, undriven_10, undriven);
  RAM #(.addrWidth(24), .dataWidth(32), .bus("separate"), .Select("low")) ram_9 (
    .addr(undriven_16), .din(undriven_22), .data(ram_1_data), .str(undriven_18), .sel(nand_9_out),
    .clk(undriven_20), .ld(undriven_21), .clr(undriven_19));
  RAM #(.addrWidth(24), .dataWidth(32), .bus("separate"), .Select("low")) ram_10 (
    .addr(undriven_16), .din(undriven_22), .data(ram_1_data), .str(undriven_18), .sel(nand_10_out),
    .clk(undriven_20), .ld(undriven_21), .clr(undriven_19));
  RAM #(.addrWidth(24), .dataWidth(32), .bus("separate"), .Select("low")) ram_11 (
    .addr(undriven_16), .din(undriven_22), .data(ram_1_data), .str(undriven_18), .sel(nand_11_out),
    .clk(undriven_20), .ld(undriven_21), .clr(undriven_19));
  RAM #(.addrWidth(24), .dataWidth(32), .bus("separate"), .Select("low")) ram_12 (
    .addr(undriven_16), .din(undriven_22), .data(ram_1_data), .str(undriven_18), .sel(nand_12_out),
    .clk(undriven_20), .ld(undriven_21), .clr(undriven_19));
  RAM #(.addrWidth(24), .dataWidth(32), .bus("separate"), .Select("low")) ram_13 (
    .addr(undriven_16), .din(undriven_22), .data(ram_1_data), .str(undriven_18), .sel(nand_13_out),
    .clk(undriven_20), .ld(undriven_21), .clr(undriven_19));
  RAM #(.addrWidth(24), .dataWidth(32), .bus("separate"), .Select("low")) ram_14 (
    .addr(undriven_16), .din(undriven_22), .data(ram_1_data), .str(undriven_18), .sel(nand_14_out),
    .clk(undriven_20), .ld(undriven_21), .clr(undriven_19));
  RAM #(.addrWidth(24), .dataWidth(32), .bus("separate"), .Select("low")) ram_15 (
    .addr(undriven_16), .din(undriven_22), .data(ram_1_data), .str(undriven_18), .sel(nand_15_out),
    .clk(undriven_20), .ld(undriven_21), .clr(undriven_19));
  RAM #(.addrWidth(24), .dataWidth(32), .bus("separate"), .Select("low")) ram_16 (
    .addr(undriven_16), .din(undriven_22), .data(ram_1_data), .str(undriven_18), .sel(nand_16_out),
    .clk(undriven_20), .ld(undriven_21), .clr(undriven_19));
  nand nand_17 (nand_17_out, undriven_11, undriven_8);
  nand nand_18 (nand_18_out, undriven_11, undriven_7);
  nand nand_19 (nand_19_out, undriven_11, undriven_6);
  nand nand_20 (nand_20_out, undriven_11, undriven_5);
  nand nand_21 (nand_21_out, undriven_11, undriven_4);
  nand nand_22 (nand_22_out, undriven_11, undriven_3);
  nand nand_23 (nand_23_out, undriven_11, undriven_2);
  nand nand_24 (nand_24_out, undriven_11, undriven);
  RAM #(.addrWidth(24), .dataWidth(32), .bus("separate"), .Select("low")) ram_17 (
    .addr(undriven_16), .din(undriven_22), .data(ram_1_data), .str(undriven_18), .sel(nand_17_out),
    .clk(undriven_20), .ld(undriven_21), .clr(undriven_19));
  RAM #(.addrWidth(24), .dataWidth(32), .bus("separate"), .Select("low")) ram_18 (
    .addr(undriven_16), .din(undriven_22), .data(ram_1_data), .str(undriven_18), .sel(nand_18_out),
    .clk(undriven_20), .ld(undriven_21), .clr(undriven_19));
  RAM #(.addrWidth(24), .dataWidth(32), .bus("separate"), .Select("low")) ram_19 (
    .addr(undriven_16), .din(undriven_22), .data(ram_1_data), .str(undriven_18), .sel(nand_19_out),
    .clk(undriven_20), .ld(undriven_21), .clr(undriven_19));
  RAM #(.addrWidth(24), .dataWidth(32), .bus("separate"), .Select("low")) ram_20 (
    .addr(undriven_16), .din(undriven_22), .data(ram_1_data), .str(undriven_18), .sel(nand_20_out),
    .clk(undriven_20), .ld(undriven_21), .clr(undriven_19));
  RAM #(.addrWidth(24), .dataWidth(32), .bus("separate"), .Select("low")) ram_21 (
    .addr(undriven_16), .din(undriven_22), .data(ram_1_data), .str(undriven_18), .sel(nand_21_out),
    .clk(undriven_20), .ld(undriven_21), .clr(undriven_19));
  RAM #(.addrWidth(24), .dataWidth(32), .bus("separate"), .Select("low")) ram_22 (
    .addr(undriven_16), .din(undriven_22), .data(ram_1_data), .str(undriven_18), .sel(nand_22_out),
    .clk(undriven_20), .ld(undriven_21), .clr(undriven_19));
  RAM #(.addrWidth(24), .dataWidth(32), .bus("separate"), .Select("low")) ram_23 (
    .addr(undriven_16), .din(undriven_22), .data(ram_1_data), .str(undriven_18), .sel(nand_23_out),
    .clk(undriven_20), .ld(undriven_21), .clr(undriven_19));
  RAM #(.addrWidth(24), .dataWidth(32), .bus("separate"), .Select("low")) ram_24 (
    .addr(undriven_16), .din(undriven_22), .data(ram_1_data), .str(undriven_18), .sel(nand_24_out),
    .clk(undriven_20), .ld(undriven_21), .clr(undriven_19));
  nand nand_25 (nand_25_out, undriven_12, undriven_8);
  nand nand_26 (nand_26_out, undriven_12, undriven_7);
  nand nand_27 (nand_27_out, undriven_12, undriven_6);
  nand nand_28 (nand_28_out, undriven_12, undriven_5);
  nand nand_29 (nand_29_out, undriven_12, undriven_4);
  nand nand_30 (nand_30_out, undriven_12, undriven_3);
  nand nand_31 (nand_31_out, undriven_12, undriven_2);
  nand nand_32 (nand_32_out, undriven_12, undriven);
  RAM #(.addrWidth(24), .dataWidth(32), .bus("separate"), .Select("low")) ram_25 (
    .addr(undriven_16), .din(undriven_22), .data(ram_1_data), .str(undriven_18), .sel(nand_25_out),
    .clk(undriven_20), .ld(undriven_21), .clr(undriven_19));
  RAM #(.addrWidth(24), .dataWidth(32), .bus("separate"), .Select("low")) ram_26 (
    .addr(undriven_16), .din(undriven_22), .data(ram_1_data), .str(undriven_18), .sel(nand_26_out),
    .clk(undriven_20), .ld(undriven_21), .clr(undriven_19));
  RAM #(.addrWidth(24), .dataWidth(32), .bus("separate"), .Select("low")) ram_27 (
    .addr(undriven_16), .din(undriven_22), .data(ram_1_data), .str(undriven_18), .sel(nand_27_out),
    .clk(undriven_20), .ld(undriven_21), .clr(undriven_19));
  RAM #(.addrWidth(24), .dataWidth(32), .bus("separate"), .Select("low")) ram_28 (
    .addr(undriven_16), .din(undriven_22), .data(ram_1_data), .str(undriven_18), .sel(nand_28_out),
    .clk(undriven_20), .ld(undriven_21), .clr(undriven_19));
  RAM #(.addrWidth(24), .dataWidth(32), .bus("separate"), .Select("low")) ram_29 (
    .addr(undriven_16), .din(undriven_22), .data(ram_1_data), .str(undriven_18), .sel(nand_29_out),
    .clk(undriven_20), .ld(undriven_21), .clr(undriven_19));
  RAM #(.addrWidth(24), .dataWidth(32), .bus("separate"), .Select("low")) ram_30 (
    .addr(undriven_16), .din(undriven_22), .data(ram_1_data), .str(undriven_18), .sel(nand_30_out),
    .clk(undriven_20), .ld(undriven_21), .clr(undriven_19));
  RAM #(.addrWidth(24), .dataWidth(32), .bus("separate"), .Select("low")) ram_31 (
    .addr(undriven_16), .din(undriven_22), .data(ram_1_data), .str(undriven_18), .sel(nand_31_out),
    .clk(undriven_20), .ld(undriven_21), .clr(undriven_19));
  RAM #(.addrWidth(24), .dataWidth(32), .bus("separate"), .Select("low")) ram_32 (
    .addr(undriven_16), .din(undriven_22), .data(ram_1_data), .str(undriven_18), .sel(nand_32_out),
    .clk(undriven_20), .ld(undriven_21), .clr(undriven_19));
  nand nand_33 (nand_33_out, undriven_13, undriven_8);
  nand nand_34 (nand_34_out, undriven_13, undriven_7);
  nand nand_35 (nand_35_out, undriven_13, undriven_6);
  nand nand_36 (nand_36_out, undriven_13, undriven_5);
  nand nand_37 (nand_37_out, undriven_13, undriven_4);
  nand nand_38 (nand_38_out, undriven_13, undriven_3);
  nand nand_39 (nand_39_out, undriven_13, undriven_2);
  nand nand_40 (nand_40_out, undriven_13, undriven);
  RAM #(.addrWidth(24), .dataWidth(32), .bus("separate"), .Select("low")) ram_33 (
    .addr(undriven_16), .din(undriven_22), .data(ram_1_data), .str(undriven_18), .sel(nand_33_out),
    .clk(undriven_20), .ld(undriven_21), .clr(undriven_19));
  RAM #(.addrWidth(24), .dataWidth(32), .bus("separate"), .Select("low")) ram_34 (
    .addr(undriven_16), .din(undriven_22), .data(ram_1_data), .str(undriven_18), .sel(nand_34_out),
    .clk(undriven_20), .ld(undriven_21), .clr(undriven_19));
  RAM #(.addrWidth(24), .dataWidth(32), .bus("separate"), .Select("low")) ram_35 (
    .addr(undriven_16), .din(undriven_22), .data(ram_1_data), .str(undriven_18), .sel(nand_35_out),
    .clk(undriven_20), .ld(undriven_21), .clr(undriven_19));
  RAM #(.addrWidth(24), .dataWidth(32), .bus("separate"), .Select("low")) ram_36 (
    .addr(undriven_16), .din(undriven_22), .data(ram_1_data), .str(undriven_18), .sel(nand_36_out),
    .clk(undriven_20), .ld(undriven_21), .clr(undriven_19));
  RAM #(.addrWidth(24), .dataWidth(32), .bus("separate"), .Select("low")) ram_37 (
    .addr(undriven_16), .din(undriven_22), .data(ram_1_data), .str(undriven_18), .sel(nand_37_out),
    .clk(undriven_20), .ld(undriven_21), .clr(undriven_19));
  RAM #(.addrWidth(24), .dataWidth(32), .bus("separate"), .Select("low")) ram_38 (
    .addr(undriven_16), .din(undriven_22), .data(ram_1_data), .str(undriven_18), .sel(nand_38_out),
    .clk(undriven_20), .ld(undriven_21), .clr(undriven_19));
  RAM #(.addrWidth(24), .dataWidth(32), .bus("separate"), .Select("low")) ram_39 (
    .addr(undriven_16), .din(undriven_22), .data(ram_1_data), .str(undriven_18), .sel(nand_39_out),
    .clk(undriven_20), .ld(undriven_21), .clr(undriven_19));
  RAM #(.addrWidth(24), .dataWidth(32), .bus("separate"), .Select("low")) ram_40 (
    .addr(undriven_16), .din(undriven_22), .data(ram_1_data), .str(undriven_18), .sel(nand_40_out),
    .clk(undriven_20), .ld(undriven_21), .clr(undriven_19));
  nand nand_41 (nand_41_out, undriven_14, undriven_8);
  nand nand_42 (nand_42_out, undriven_14, undriven_7);
  nand nand_43 (nand_43_out, undriven_14, undriven_6);
  nand nand_44 (nand_44_out, undriven_14, undriven_5);
  nand nand_45 (nand_45_out, undriven_14, undriven_4);
  nand nand_46 (nand_46_out, undriven_14, undriven_3);
  nand nand_47 (nand_47_out, undriven_14, undriven_2);
  nand nand_48 (nand_48_out, undriven_14, undriven);
  RAM #(.addrWidth(24), .dataWidth(32), .bus("separate"), .Select("low")) ram_41 (
    .addr(undriven_16), .din(undriven_22), .data(ram_1_data), .str(undriven_18), .sel(nand_41_out),
    .clk(undriven_20), .ld(undriven_21), .clr(undriven_19));
  RAM #(.addrWidth(24), .dataWidth(32), .bus("separate"), .Select("low")) ram_42 (
    .addr(undriven_16), .din(undriven_22), .data(ram_1_data), .str(undriven_18), .sel(nand_42_out),
    .clk(undriven_20), .ld(undriven_21), .clr(undriven_19));
  RAM #(.addrWidth(24), .dataWidth(32), .bus("separate"), .Select("low")) ram_43 (
    .addr(undriven_16), .din(undriven_22), .data(ram_1_data), .str(undriven_18), .sel(nand_43_out),
    .clk(undriven_20), .ld(undriven_21), .clr(undriven_19));
  RAM #(.addrWidth(24), .dataWidth(32), .bus("separate"), .Select("low")) ram_44 (
    .addr(undriven_16), .din(undriven_22), .data(ram_1_data), .str(undriven_18), .sel(nand_44_out),
    .clk(undriven_20), .ld(undriven_21), .clr(undriven_19));
  RAM #(.addrWidth(24), .dataWidth(32), .bus("separate"), .Select("low")) ram_45 (
    .addr(undriven_16), .din(undriven_22), .data(ram_1_data), .str(undriven_18), .sel(nand_45_out),
    .clk(undriven_20), .ld(undriven_21), .clr(undriven_19));
  RAM #(.addrWidth(24), .dataWidth(32), .bus("separate"), .Select("low")) ram_46 (
    .addr(undriven_16), .din(undriven_22), .data(ram_1_data), .str(undriven_18), .sel(nand_46_out),
    .clk(undriven_20), .ld(undriven_21), .clr(undriven_19));
  RAM #(.addrWidth(24), .dataWidth(32), .bus("separate"), .Select("low")) ram_47 (
    .addr(undriven_16), .din(undriven_22), .data(ram_1_data), .str(undriven_18), .sel(nand_47_out),
    .clk(undriven_20), .ld(undriven_21), .clr(undriven_19));
  RAM #(.addrWidth(24), .dataWidth(32), .bus("separate"), .Select("low")) ram_48 (
    .addr(undriven_16), .din(undriven_22), .data(ram_1_data), .str(undriven_18), .sel(nand_48_out),
    .clk(undriven_20), .ld(undriven_21), .clr(undriven_19));
  nand nand_49 (nand_49_out, undriven_15, undriven_8);
  nand nand_50 (nand_50_out, undriven_15, undriven_7);
  nand nand_51 (nand_51_out, undriven_15, undriven_6);
  nand nand_52 (nand_52_out, undriven_15, undriven_5);
  nand nand_53 (nand_53_out, undriven_15, undriven_4);
  nand nand_54 (nand_54_out, undriven_15, undriven_3);
  nand nand_55 (nand_55_out, undriven_15, undriven_2);
  nand nand_56 (nand_56_out, undriven_15, undriven);
  RAM #(.addrWidth(24), .dataWidth(32), .bus("separate"), .Select("low")) ram_49 (
    .addr(undriven_16), .din(undriven_22), .data(ram_1_data), .str(undriven_18), .sel(nand_49_out),
    .clk(undriven_20), .ld(undriven_21), .clr(undriven_19));
  RAM #(.addrWidth(24), .dataWidth(32), .bus("separate"), .Select("low")) ram_50 (
    .addr(undriven_16), .din(undriven_22), .data(ram_1_data), .str(undriven_18), .sel(nand_50_out),
    .clk(undriven_20), .ld(undriven_21), .clr(undriven_19));
  RAM #(.addrWidth(24), .dataWidth(32), .bus("separate"), .Select("low")) ram_51 (
    .addr(undriven_16), .din(undriven_22), .data(ram_1_data), .str(undriven_18), .sel(nand_51_out),
    .clk(undriven_20), .ld(undriven_21), .clr(undriven_19));
  RAM #(.addrWidth(24), .dataWidth(32), .bus("separate"), .Select("low")) ram_52 (
    .addr(undriven_16), .din(undriven_22), .data(ram_1_data), .str(undriven_18), .sel(nand_52_out),
    .clk(undriven_20), .ld(undriven_21), .clr(undriven_19));
  RAM #(.addrWidth(24), .dataWidth(32), .bus("separate"), .Select("low")) ram_53 (
    .addr(undriven_16), .din(undriven_22), .data(ram_1_data), .str(undriven_18), .sel(nand_53_out),
    .clk(undriven_20), .ld(undriven_21), .clr(undriven_19));
  RAM #(.addrWidth(24), .dataWidth(32), .bus("separate"), .Select("low")) ram_54 (
    .addr(undriven_16), .din(undriven_22), .data(ram_1_data), .str(undriven_18), .sel(nand_54_out),
    .clk(undriven_20), .ld(undriven_21), .clr(undriven_19));
  RAM #(.addrWidth(24), .dataWidth(32), .bus("separate"), .Select("low")) ram_55 (
    .addr(undriven_16), .din(undriven_22), .data(ram_1_data), .str(undriven_18), .sel(nand_55_out),
    .clk(undriven_20), .ld(undriven_21), .clr(undriven_19));
  RAM #(.addrWidth(24), .dataWidth(32), .bus("separate"), .Select("low")) ram_56 (
    .addr(undriven_16), .din(undriven_22), .data(ram_1_data), .str(undriven_18), .sel(nand_56_out),
    .clk(undriven_20), .ld(undriven_21), .clr(undriven_19));
  nand nand_57 (nand_57_out, undriven_17, undriven_8);
  nand nand_58 (nand_58_out, undriven_17, undriven_7);
  nand nand_59 (nand_59_out, undriven_17, undriven_6);
  nand nand_60 (nand_60_out, undriven_17, undriven_5);
  nand nand_61 (nand_61_out, undriven_17, undriven_4);
  nand nand_62 (nand_62_out, undriven_17, undriven_3);
  nand nand_63 (nand_63_out, undriven_17, undriven_2);
  nand nand_64 (nand_64_out, undriven_17, undriven);
  RAM #(.addrWidth(24), .dataWidth(32), .bus("separate"), .Select("low")) ram_57 (
    .addr(undriven_16), .din(undriven_22), .data(ram_1_data), .str(undriven_18), .sel(nand_57_out),
    .clk(undriven_20), .ld(undriven_21), .clr(undriven_19));
  RAM #(.addrWidth(24), .dataWidth(32), .bus("separate"), .Select("low")) ram_58 (
    .addr(undriven_16), .din(undriven_22), .data(ram_1_data), .str(undriven_18), .sel(nand_58_out),
    .clk(undriven_20), .ld(undriven_21), .clr(undriven_19));
  RAM #(.addrWidth(24), .dataWidth(32), .bus("separate"), .Select("low")) ram_59 (
    .addr(undriven_16), .din(undriven_22), .data(ram_1_data), .str(undriven_18), .sel(nand_59_out),
    .clk(undriven_20), .ld(undriven_21), .clr(undriven_19));
  RAM #(.addrWidth(24), .dataWidth(32), .bus("separate"), .Select("low")) ram_60 (
    .addr(undriven_16), .din(undriven_22), .data(ram_1_data), .str(undriven_18), .sel(nand_60_out),
    .clk(undriven_20), .ld(undriven_21), .clr(undriven_19));
  RAM #(.addrWidth(24), .dataWidth(32), .bus("separate"), .Select("low")) ram_61 (
    .addr(undriven_16), .din(undriven_22), .data(ram_1_data), .str(undriven_18), .sel(nand_61_out),
    .clk(undriven_20), .ld(undriven_21), .clr(undriven_19));
  RAM #(.addrWidth(24), .dataWidth(32), .bus("separate"), .Select("low")) ram_62 (
    .addr(undriven_16), .din(undriven_22), .data(ram_1_data), .str(undriven_18), .sel(nand_62_out),
    .clk(undriven_20), .ld(undriven_21), .clr(undriven_19));
  RAM #(.addrWidth(24), .dataWidth(32), .bus("separate"), .Select("low")) ram_63 (
    .addr(undriven_16), .din(undriven_22), .data(ram_1_data), .str(undriven_18), .sel(nand_63_out),
    .clk(undriven_20), .ld(undriven_21), .clr(undriven_19));
  RAM #(.addrWidth(24), .dataWidth(32), .bus("separate"), .Select("low")) ram_64 (
    .addr(undriven_16), .din(undriven_22), .data(ram_1_data), .str(undriven_18), .sel(nand_64_out),
    .clk(undriven_20), .ld(undriven_21), .clr(undriven_19));

  // Other names for the same wires on the sheet: Ad_TP[31:0] = Address_Bus; Data_Bus_In_TP[31:0] = Data_Bus_In;
  //   DataOut[31:0] = Data_Bus_Out

  // Notes on the sheet:
  //   外部各接口定义与原RAM相同
  //   按照字节编址，但按照字对齐访问
endmodule

module \实验三_ROM  (
  input  CS,
  input  [31:0] Address_Bus,
  output [31:0] Data_Bus_Out
);

  wire nand_1_out, nand_2_out, nand_3_out, nand_4_out, nand_5_out, nand_6_out, nand_7_out, nand_8_out,
       nand_9_out, nand_10_out, nand_11_out, nand_12_out, nand_13_out, nand_14_out, nand_15_out, nand_16_out,
       nand_17_out, nand_18_out, nand_19_out, nand_20_out, nand_21_out, nand_22_out, nand_23_out,
       nand_24_out, nand_25_out, nand_26_out, nand_27_out, nand_28_out, nand_29_out, nand_30_out,
       nand_31_out, nand_32_out, nand_33_out, nand_34_out, nand_35_out, nand_36_out, nand_37_out,
       nand_38_out, nand_39_out, nand_40_out, nand_41_out, nand_42_out, nand_43_out, nand_44_out,
       nand_45_out, nand_46_out, nand_47_out, nand_48_out, nand_49_out, nand_50_out, nand_51_out,
       nand_52_out, nand_53_out, nand_54_out, nand_55_out, nand_56_out, nand_57_out, nand_58_out,
       nand_59_out, nand_60_out, nand_61_out, nand_62_out, nand_63_out, nand_64_out, undriven, undriven_2,
       undriven_3, undriven_4, undriven_5, undriven_6, undriven_7, undriven_8, undriven_9, undriven_10,
       undriven_11, undriven_12, undriven_13, undriven_14, undriven_15, undriven_16;
  wire [23:0] undriven_17;
  wire [31:0] rom_1_data;

  nand nand_1 (nand_1_out, undriven_9, undriven_8);
  nand nand_2 (nand_2_out, undriven_9, undriven_7);
  nand nand_3 (nand_3_out, undriven_9, undriven_6);
  nand nand_4 (nand_4_out, undriven_9, undriven_5);
  nand nand_5 (nand_5_out, undriven_9, undriven_4);
  nand nand_6 (nand_6_out, undriven_9, undriven_3);
  nand nand_7 (nand_7_out, undriven_9, undriven_2);
  nand nand_8 (nand_8_out, undriven_9, undriven);
  ROM #(.addrWidth(24), .dataWidth(32), .Select("low")) rom_1 (.addr(undriven_17), .data(rom_1_data), .sel(nand_1_out));
  ROM #(.addrWidth(24), .dataWidth(32), .Select("low")) rom_2 (.addr(undriven_17), .data(rom_1_data), .sel(nand_2_out));
  ROM #(.addrWidth(24), .dataWidth(32), .Select("low")) rom_3 (.addr(undriven_17), .data(rom_1_data), .sel(nand_3_out));
  ROM #(.addrWidth(24), .dataWidth(32), .Select("low")) rom_4 (.addr(undriven_17), .data(rom_1_data), .sel(nand_4_out));
  ROM #(.addrWidth(24), .dataWidth(32), .Select("low")) rom_5 (.addr(undriven_17), .data(rom_1_data), .sel(nand_5_out));
  ROM #(.addrWidth(24), .dataWidth(32), .Select("low")) rom_6 (.addr(undriven_17), .data(rom_1_data), .sel(nand_6_out));
  ROM #(.addrWidth(24), .dataWidth(32), .Select("low")) rom_7 (.addr(undriven_17), .data(rom_1_data), .sel(nand_7_out));
  ROM #(.addrWidth(24), .dataWidth(32), .Select("low")) rom_8 (.addr(undriven_17), .data(rom_1_data), .sel(nand_8_out));
  nand nand_9 (nand_9_out, undriven_10, undriven_8);
  nand nand_10 (nand_10_out, undriven_10, undriven_7);
  nand nand_11 (nand_11_out, undriven_10, undriven_6);
  nand nand_12 (nand_12_out, undriven_10, undriven_5);
  nand nand_13 (nand_13_out, undriven_10, undriven_4);
  nand nand_14 (nand_14_out, undriven_10, undriven_3);
  nand nand_15 (nand_15_out, undriven_10, undriven_2);
  nand nand_16 (nand_16_out, undriven_10, undriven);
  ROM #(.addrWidth(24), .dataWidth(32), .Select("low")) rom_9 (.addr(undriven_17), .data(rom_1_data), .sel(nand_9_out));
  ROM #(.addrWidth(24), .dataWidth(32), .Select("low")) rom_10 (
    .addr(undriven_17), .data(rom_1_data), .sel(nand_10_out));
  ROM #(.addrWidth(24), .dataWidth(32), .Select("low")) rom_11 (
    .addr(undriven_17), .data(rom_1_data), .sel(nand_11_out));
  ROM #(.addrWidth(24), .dataWidth(32), .Select("low")) rom_12 (
    .addr(undriven_17), .data(rom_1_data), .sel(nand_12_out));
  ROM #(.addrWidth(24), .dataWidth(32), .Select("low")) rom_13 (
    .addr(undriven_17), .data(rom_1_data), .sel(nand_13_out));
  ROM #(.addrWidth(24), .dataWidth(32), .Select("low")) rom_14 (
    .addr(undriven_17), .data(rom_1_data), .sel(nand_14_out));
  ROM #(.addrWidth(24), .dataWidth(32), .Select("low")) rom_15 (
    .addr(undriven_17), .data(rom_1_data), .sel(nand_15_out));
  ROM #(.addrWidth(24), .dataWidth(32), .Select("low")) rom_16 (
    .addr(undriven_17), .data(rom_1_data), .sel(nand_16_out));
  nand nand_17 (nand_17_out, undriven_11, undriven_8);
  nand nand_18 (nand_18_out, undriven_11, undriven_7);
  nand nand_19 (nand_19_out, undriven_11, undriven_6);
  nand nand_20 (nand_20_out, undriven_11, undriven_5);
  nand nand_21 (nand_21_out, undriven_11, undriven_4);
  nand nand_22 (nand_22_out, undriven_11, undriven_3);
  nand nand_23 (nand_23_out, undriven_11, undriven_2);
  nand nand_24 (nand_24_out, undriven_11, undriven);
  ROM #(.addrWidth(24), .dataWidth(32), .Select("low")) rom_17 (
    .addr(undriven_17), .data(rom_1_data), .sel(nand_17_out));
  ROM #(.addrWidth(24), .dataWidth(32), .Select("low")) rom_18 (
    .addr(undriven_17), .data(rom_1_data), .sel(nand_18_out));
  ROM #(.addrWidth(24), .dataWidth(32), .Select("low")) rom_19 (
    .addr(undriven_17), .data(rom_1_data), .sel(nand_19_out));
  ROM #(.addrWidth(24), .dataWidth(32), .Select("low")) rom_20 (
    .addr(undriven_17), .data(rom_1_data), .sel(nand_20_out));
  ROM #(.addrWidth(24), .dataWidth(32), .Select("low")) rom_21 (
    .addr(undriven_17), .data(rom_1_data), .sel(nand_21_out));
  ROM #(.addrWidth(24), .dataWidth(32), .Select("low")) rom_22 (
    .addr(undriven_17), .data(rom_1_data), .sel(nand_22_out));
  ROM #(.addrWidth(24), .dataWidth(32), .Select("low")) rom_23 (
    .addr(undriven_17), .data(rom_1_data), .sel(nand_23_out));
  ROM #(.addrWidth(24), .dataWidth(32), .Select("low")) rom_24 (
    .addr(undriven_17), .data(rom_1_data), .sel(nand_24_out));
  nand nand_25 (nand_25_out, undriven_12, undriven_8);
  nand nand_26 (nand_26_out, undriven_12, undriven_7);
  nand nand_27 (nand_27_out, undriven_12, undriven_6);
  nand nand_28 (nand_28_out, undriven_12, undriven_5);
  nand nand_29 (nand_29_out, undriven_12, undriven_4);
  nand nand_30 (nand_30_out, undriven_12, undriven_3);
  nand nand_31 (nand_31_out, undriven_12, undriven_2);
  nand nand_32 (nand_32_out, undriven_12, undriven);
  ROM #(.addrWidth(24), .dataWidth(32), .Select("low")) rom_25 (
    .addr(undriven_17), .data(rom_1_data), .sel(nand_25_out));
  ROM #(.addrWidth(24), .dataWidth(32), .Select("low")) rom_26 (
    .addr(undriven_17), .data(rom_1_data), .sel(nand_26_out));
  ROM #(.addrWidth(24), .dataWidth(32), .Select("low")) rom_27 (
    .addr(undriven_17), .data(rom_1_data), .sel(nand_27_out));
  ROM #(.addrWidth(24), .dataWidth(32), .Select("low")) rom_28 (
    .addr(undriven_17), .data(rom_1_data), .sel(nand_28_out));
  ROM #(.addrWidth(24), .dataWidth(32), .Select("low")) rom_29 (
    .addr(undriven_17), .data(rom_1_data), .sel(nand_29_out));
  ROM #(.addrWidth(24), .dataWidth(32), .Select("low")) rom_30 (
    .addr(undriven_17), .data(rom_1_data), .sel(nand_30_out));
  ROM #(.addrWidth(24), .dataWidth(32), .Select("low")) rom_31 (
    .addr(undriven_17), .data(rom_1_data), .sel(nand_31_out));
  ROM #(.addrWidth(24), .dataWidth(32), .Select("low")) rom_32 (
    .addr(undriven_17), .data(rom_1_data), .sel(nand_32_out));
  nand nand_33 (nand_33_out, undriven_13, undriven_8);
  nand nand_34 (nand_34_out, undriven_13, undriven_7);
  nand nand_35 (nand_35_out, undriven_13, undriven_6);
  nand nand_36 (nand_36_out, undriven_13, undriven_5);
  nand nand_37 (nand_37_out, undriven_13, undriven_4);
  nand nand_38 (nand_38_out, undriven_13, undriven_3);
  nand nand_39 (nand_39_out, undriven_13, undriven_2);
  nand nand_40 (nand_40_out, undriven_13, undriven);
  ROM #(.addrWidth(24), .dataWidth(32), .Select("low")) rom_33 (
    .addr(undriven_17), .data(rom_1_data), .sel(nand_33_out));
  ROM #(.addrWidth(24), .dataWidth(32), .Select("low")) rom_34 (
    .addr(undriven_17), .data(rom_1_data), .sel(nand_34_out));
  ROM #(.addrWidth(24), .dataWidth(32), .Select("low")) rom_35 (
    .addr(undriven_17), .data(rom_1_data), .sel(nand_35_out));
  ROM #(.addrWidth(24), .dataWidth(32), .Select("low")) rom_36 (
    .addr(undriven_17), .data(rom_1_data), .sel(nand_36_out));
  ROM #(.addrWidth(24), .dataWidth(32), .Select("low")) rom_37 (
    .addr(undriven_17), .data(rom_1_data), .sel(nand_37_out));
  ROM #(.addrWidth(24), .dataWidth(32), .Select("low")) rom_38 (
    .addr(undriven_17), .data(rom_1_data), .sel(nand_38_out));
  ROM #(.addrWidth(24), .dataWidth(32), .Select("low")) rom_39 (
    .addr(undriven_17), .data(rom_1_data), .sel(nand_39_out));
  ROM #(.addrWidth(24), .dataWidth(32), .Select("low")) rom_40 (
    .addr(undriven_17), .data(rom_1_data), .sel(nand_40_out));
  nand nand_41 (nand_41_out, undriven_14, undriven_8);
  nand nand_42 (nand_42_out, undriven_14, undriven_7);
  nand nand_43 (nand_43_out, undriven_14, undriven_6);
  nand nand_44 (nand_44_out, undriven_14, undriven_5);
  nand nand_45 (nand_45_out, undriven_14, undriven_4);
  nand nand_46 (nand_46_out, undriven_14, undriven_3);
  nand nand_47 (nand_47_out, undriven_14, undriven_2);
  nand nand_48 (nand_48_out, undriven_14, undriven);
  ROM #(.addrWidth(24), .dataWidth(32), .Select("low")) rom_41 (
    .addr(undriven_17), .data(rom_1_data), .sel(nand_41_out));
  ROM #(.addrWidth(24), .dataWidth(32), .Select("low")) rom_42 (
    .addr(undriven_17), .data(rom_1_data), .sel(nand_42_out));
  ROM #(.addrWidth(24), .dataWidth(32), .Select("low")) rom_43 (
    .addr(undriven_17), .data(rom_1_data), .sel(nand_43_out));
  ROM #(.addrWidth(24), .dataWidth(32), .Select("low")) rom_44 (
    .addr(undriven_17), .data(rom_1_data), .sel(nand_44_out));
  ROM #(.addrWidth(24), .dataWidth(32), .Select("low")) rom_45 (
    .addr(undriven_17), .data(rom_1_data), .sel(nand_45_out));
  ROM #(.addrWidth(24), .dataWidth(32), .Select("low")) rom_46 (
    .addr(undriven_17), .data(rom_1_data), .sel(nand_46_out));
  ROM #(.addrWidth(24), .dataWidth(32), .Select("low")) rom_47 (
    .addr(undriven_17), .data(rom_1_data), .sel(nand_47_out));
  ROM #(.addrWidth(24), .dataWidth(32), .Select("low")) rom_48 (
    .addr(undriven_17), .data(rom_1_data), .sel(nand_48_out));
  nand nand_49 (nand_49_out, undriven_15, undriven_8);
  nand nand_50 (nand_50_out, undriven_15, undriven_7);
  nand nand_51 (nand_51_out, undriven_15, undriven_6);
  nand nand_52 (nand_52_out, undriven_15, undriven_5);
  nand nand_53 (nand_53_out, undriven_15, undriven_4);
  nand nand_54 (nand_54_out, undriven_15, undriven_3);
  nand nand_55 (nand_55_out, undriven_15, undriven_2);
  nand nand_56 (nand_56_out, undriven_15, undriven);
  ROM #(.addrWidth(24), .dataWidth(32), .Select("low")) rom_49 (
    .addr(undriven_17), .data(rom_1_data), .sel(nand_49_out));
  ROM #(.addrWidth(24), .dataWidth(32), .Select("low")) rom_50 (
    .addr(undriven_17), .data(rom_1_data), .sel(nand_50_out));
  ROM #(.addrWidth(24), .dataWidth(32), .Select("low")) rom_51 (
    .addr(undriven_17), .data(rom_1_data), .sel(nand_51_out));
  ROM #(.addrWidth(24), .dataWidth(32), .Select("low")) rom_52 (
    .addr(undriven_17), .data(rom_1_data), .sel(nand_52_out));
  ROM #(.addrWidth(24), .dataWidth(32), .Select("low")) rom_53 (
    .addr(undriven_17), .data(rom_1_data), .sel(nand_53_out));
  ROM #(.addrWidth(24), .dataWidth(32), .Select("low")) rom_54 (
    .addr(undriven_17), .data(rom_1_data), .sel(nand_54_out));
  ROM #(.addrWidth(24), .dataWidth(32), .Select("low")) rom_55 (
    .addr(undriven_17), .data(rom_1_data), .sel(nand_55_out));
  ROM #(.addrWidth(24), .dataWidth(32), .Select("low")) rom_56 (
    .addr(undriven_17), .data(rom_1_data), .sel(nand_56_out));
  nand nand_57 (nand_57_out, undriven_16, undriven_8);
  nand nand_58 (nand_58_out, undriven_16, undriven_7);
  nand nand_59 (nand_59_out, undriven_16, undriven_6);
  nand nand_60 (nand_60_out, undriven_16, undriven_5);
  nand nand_61 (nand_61_out, undriven_16, undriven_4);
  nand nand_62 (nand_62_out, undriven_16, undriven_3);
  nand nand_63 (nand_63_out, undriven_16, undriven_2);
  nand nand_64 (nand_64_out, undriven_16, undriven);
  ROM #(.addrWidth(24), .dataWidth(32), .Select("low")) rom_57 (
    .addr(undriven_17), .data(rom_1_data), .sel(nand_57_out));
  ROM #(.addrWidth(24), .dataWidth(32), .Select("low")) rom_58 (
    .addr(undriven_17), .data(rom_1_data), .sel(nand_58_out));
  ROM #(.addrWidth(24), .dataWidth(32), .Select("low")) rom_59 (
    .addr(undriven_17), .data(rom_1_data), .sel(nand_59_out));
  ROM #(.addrWidth(24), .dataWidth(32), .Select("low")) rom_60 (
    .addr(undriven_17), .data(rom_1_data), .sel(nand_60_out));
  ROM #(.addrWidth(24), .dataWidth(32), .Select("low")) rom_61 (
    .addr(undriven_17), .data(rom_1_data), .sel(nand_61_out));
  ROM #(.addrWidth(24), .dataWidth(32), .Select("low")) rom_62 (
    .addr(undriven_17), .data(rom_1_data), .sel(nand_62_out));
  ROM #(.addrWidth(24), .dataWidth(32), .Select("low")) rom_63 (
    .addr(undriven_17), .data(rom_1_data), .sel(nand_63_out));
  ROM #(.addrWidth(24), .dataWidth(32), .Select("low")) rom_64 (
    .addr(undriven_17), .data(rom_1_data), .sel(nand_64_out));

  // Other names for the same wires on the sheet: Ad_TP[31:0] = Address_Bus; DataOut[31:0] = Data_Bus_Out

  // Notes on the sheet:
  //   外部各接口定义与原ROM相同
  //   按照字节编址，但按照字对齐访问
endmodule

module \实验三_MIPS  (
  input  [4:0] A1_address,
  input  [31:0] W_data,
  input  [4:0] A2_address,
  input  [4:0] W_address,
  input  W_Enable,
  input  CLK,
  output [31:0] R_data1,
  output [31:0] R_data2
);


  // Other names for the same wires on the sheet: A1[4:0] = A1_address; A2[4:0] = A2_address; A3[4:0] = W_address;
  //   RD1[31:0] = R_data1; RD2[31:0] = R_data2; WD3[31:0] = W_data; WE3 = W_Enable
endmodule

module \平时作业1_全加器子电路  (
  input  x,
  input  y,
  input  Cin,
  output Carry,
  output sum
);

  wire and_1_out, and_2_out, and_3_out, and_4_out, and_5_out, and_6_out, and_7_out, not_1_out, not_2_out,
       not_3_out, not_4_out, not_5_out, not_6_out;

  and and_1 (and_1_out, y, Cin);
  and and_2 (and_2_out, x, Cin);
  and and_3 (and_3_out, x, y);
  not not_1 (not_1_out, x);
  not not_2 (not_2_out, y);
  not not_3 (not_3_out, x);
  not not_4 (not_4_out, Cin);
  not not_5 (not_5_out, y);
  not not_6 (not_6_out, Cin);
  or or_1 (Carry, and_1_out, and_2_out, and_3_out);
  and and_4 (and_4_out, not_1_out, not_2_out, Cin);
  and and_5 (and_5_out, not_3_out, y, not_4_out);
  and and_6 (and_6_out, x, not_5_out, not_6_out);
  and and_7 (and_7_out, x, y, Cin);
  or or_2 (sum, and_4_out, and_5_out, and_6_out, and_7_out);
endmodule

module \平时作业1_溢出判断  (
  input  Sa,
  input  Sb,
  input  Sf,
  output Overflow
);

  wire and_1_out, and_2_out, not_1_out, not_2_out, not_3_out;

  not not_1 (not_1_out, Sa);
  not not_2 (not_2_out, Sb);
  not not_3 (not_3_out, Sf);
  and and_1 (and_1_out, not_1_out, not_2_out, Sf);
  and and_2 (and_2_out, Sa, Sb, not_3_out);
  or or_1 (Overflow, and_1_out, and_2_out);
endmodule

module \平时作业1_带有溢出判断和进位输出的4_bit加法器  (
  input  [3:0] in_1,
  input  [3:0] in_2,
  output Overflow,
  output [3:0] out_4
);

  wire \平时作业1_全加器子电路_2_carry , \平时作业1_全加器子电路_3_carry , \平时作业1_全加器子电路_4_carry ;

  // Probe on in_1
  // Probe on in_2
  \平时作业1_全加器子电路  \u_平时作业1_全加器子电路_1  (
    .x(in_1[3]), .y(in_2[3]), .Cin(\平时作业1_全加器子电路_2_carry ), .Carry(Overflow), .sum(out_4[3]));
  // Probe on out_4
  \平时作业1_全加器子电路  \u_平时作业1_全加器子电路_2  (
    .x(in_1[2]), .y(in_2[2]), .Cin(\平时作业1_全加器子电路_3_carry ), .Carry(\平时作业1_全加器子电路_2_carry ), .sum(out_4[2]));
  \平时作业1_全加器子电路  \u_平时作业1_全加器子电路_3  (
    .x(in_1[1]), .y(in_2[1]), .Cin(\平时作业1_全加器子电路_4_carry ), .Carry(\平时作业1_全加器子电路_3_carry ), .sum(out_4[1]));
  \平时作业1_全加器子电路  \u_平时作业1_全加器子电路_4  (
    .x(in_1[0]), .y(in_2[0]), .Cin(1'b0), .Carry(\平时作业1_全加器子电路_4_carry ), .sum(out_4[0]));

  // Notes on the sheet:
  //   带有溢出判断和进位输出的4-bit加法器
endmodule

module \平时作业1_带有溢出判断和进位输出的4_bit有符号数的补码加法器1  (
  input  [3:0] in_1,
  input  [3:0] in_2,
  output Overflow,
  output [3:0] out_4
);

  wire \平时作业1_全加器子电路_2_carry , \平时作业1_全加器子电路_3_carry , \平时作业1_全加器子电路_4_carry ;

  // Probe on in_1
  // Probe on in_2
  \平时作业1_溢出判断  \u_平时作业1_溢出判断_1  (.Sa(in_1[3]), .Sb(in_2[3]), .Sf(\平时作业1_全加器子电路_2_carry ), .Overflow(Overflow));
  // Probe on out_4
  \平时作业1_全加器子电路  \u_平时作业1_全加器子电路_1  (
    .x(in_1[3]), .y(in_2[3]), .Cin(\平时作业1_全加器子电路_2_carry ), .sum(out_4[3]));  // open: Carry
  \平时作业1_全加器子电路  \u_平时作业1_全加器子电路_2  (
    .x(in_1[2]), .y(in_2[2]), .Cin(\平时作业1_全加器子电路_3_carry ), .Carry(\平时作业1_全加器子电路_2_carry ), .sum(out_4[2]));
  \平时作业1_全加器子电路  \u_平时作业1_全加器子电路_3  (
    .x(in_1[1]), .y(in_2[1]), .Cin(\平时作业1_全加器子电路_4_carry ), .Carry(\平时作业1_全加器子电路_3_carry ), .sum(out_4[1]));
  \平时作业1_全加器子电路  \u_平时作业1_全加器子电路_4  (
    .x(in_1[0]), .y(in_2[0]), .Cin(1'b0), .Carry(\平时作业1_全加器子电路_4_carry ), .sum(out_4[0]));

  // Notes on the sheet:
  //   带有溢出判断和进位输出的4-bit有符号数的补码加法器
  //   第一种
endmodule

module \平时作业1_带有溢出判断和进位输出的4_bit有符号数的补码加法器2  (
  input  [3:0] in_1,
  input  [3:0] in_2,
  output Overflow,
  output [3:0] out_4
);

  wire \平时作业1_全加器子电路_1_carry , \平时作业1_全加器子电路_2_carry , \平时作业1_全加器子电路_3_carry , \平时作业1_全加器子电路_4_carry ;

  xor xor_1 (Overflow, \平时作业1_全加器子电路_1_carry , \平时作业1_全加器子电路_2_carry );
  // Probe on in_1
  // Probe on in_2
  // Probe on out_4
  \平时作业1_全加器子电路  \u_平时作业1_全加器子电路_1  (
    .x(in_1[3]), .y(in_2[3]), .Cin(\平时作业1_全加器子电路_2_carry ), .Carry(\平时作业1_全加器子电路_1_carry ), .sum(out_4[3]));
  \平时作业1_全加器子电路  \u_平时作业1_全加器子电路_2  (
    .x(in_1[2]), .y(in_2[2]), .Cin(\平时作业1_全加器子电路_3_carry ), .Carry(\平时作业1_全加器子电路_2_carry ), .sum(out_4[2]));
  \平时作业1_全加器子电路  \u_平时作业1_全加器子电路_3  (
    .x(in_1[1]), .y(in_2[1]), .Cin(\平时作业1_全加器子电路_4_carry ), .Carry(\平时作业1_全加器子电路_3_carry ), .sum(out_4[1]));
  \平时作业1_全加器子电路  \u_平时作业1_全加器子电路_4  (
    .x(in_1[0]), .y(in_2[0]), .Cin(1'b0), .Carry(\平时作业1_全加器子电路_4_carry ), .sum(out_4[0]));

  // Notes on the sheet:
  //   第二种：异或
endmodule

module \平时作业1_带有溢出判断和进位输出的4_bit有符号数的补码加法器3  (
  input  [3:0] in_1,
  input  [3:0] in_2,
  output Overflow,
  output [3:0] out_4
);

  wire \平时作业1_全加器子电路_1_sum , \平时作业1_全加器子电路_2_carry , \平时作业1_全加器子电路_3_carry , \平时作业1_全加器子电路_4_carry ,
       \平时作业1_全加器子电路_5_carry ;

  xor xor_1 (Overflow, \平时作业1_全加器子电路_1_sum , \平时作业1_全加器子电路_3_carry );
  \平时作业1_全加器子电路  \u_平时作业1_全加器子电路_1  (
    .x(in_2[3]), .y(in_1[3]), .Cin(\平时作业1_全加器子电路_2_carry ), .sum(\平时作业1_全加器子电路_1_sum ));  // open: Carry
  // Probe on in_1
  // Probe on in_2
  // Probe on out_4
  \平时作业1_全加器子电路  \u_平时作业1_全加器子电路_2  (
    .x(in_1[3]), .y(in_2[3]), .Cin(\平时作业1_全加器子电路_3_carry ), .Carry(\平时作业1_全加器子电路_2_carry ), .sum(out_4[3]));
  \平时作业1_全加器子电路  \u_平时作业1_全加器子电路_3  (
    .x(in_1[2]), .y(in_2[2]), .Cin(\平时作业1_全加器子电路_4_carry ), .Carry(\平时作业1_全加器子电路_3_carry ), .sum(out_4[2]));
  \平时作业1_全加器子电路  \u_平时作业1_全加器子电路_4  (
    .x(in_1[1]), .y(in_2[1]), .Cin(\平时作业1_全加器子电路_5_carry ), .Carry(\平时作业1_全加器子电路_4_carry ), .sum(out_4[1]));
  \平时作业1_全加器子电路  \u_平时作业1_全加器子电路_5  (
    .x(in_1[0]), .y(in_2[0]), .Cin(1'b0), .Carry(\平时作业1_全加器子电路_5_carry ), .sum(out_4[0]));

  // Notes on the sheet:
  //   第三种：双符号位
endmodule

module \平时作业2_红绿灯1  (
  input  First,
  input  Second,
  input  Third,
  output Red,
  output Yellow,
  output Green,
  output Second_Out,
  output Third_Out
);

  wire not_1_out, not_2_out, not_3_out;

  not not_1 (not_1_out, Second);
  not not_2 (not_2_out, Second);
  not not_3 (not_3_out, Third);
  and and_1 (Yellow, not_1_out, Third);
  and and_2 (Green, not_2_out, not_3_out);

  assign Red = Second;
  assign Second_Out = First;
  assign Third_Out = Second;

  // Notes on the sheet:
  //   不管第一段有没有车通过，都有灯亮起
endmodule

module \平时作业2_红绿灯2  (
  input  First,
  input  Second,
  input  Third
);

  wire and_1_out, and_2_out, and_3_out, not_1_out, not_2_out, not_3_out;

  not not_1 (not_1_out, Second);
  not not_2 (not_2_out, Second);
  not not_3 (not_3_out, Third);
  and and_1 (and_1_out, First, Second);
  and and_2 (and_2_out, First, not_1_out, Third);
  and and_3 (and_3_out, First, not_2_out, not_3_out);
  LED #(.active("true")) led_1 (.in(and_1_out));
  LED #(.active("true")) led_2 (.in(and_2_out));
  LED #(.active("true")) led_3 (.in(and_3_out));

  // Notes on the sheet:
  //   只有第一段有车通过，才会亮灯
endmodule

module \平时作业2_多段铁路红绿灯连接  (
  input  in_1,
  input  in_2,
  input  in_3,
  output out_4,
  output out_5
);

  wire \平时作业2_红绿灯1_1_green , \平时作业2_红绿灯1_1_red , \平时作业2_红绿灯1_1_second_out , \平时作业2_红绿灯1_1_third_out ,
       \平时作业2_红绿灯1_1_yellow , \平时作业2_红绿灯1_2_green , \平时作业2_红绿灯1_2_red , \平时作业2_红绿灯1_2_second_out ,
       \平时作业2_红绿灯1_2_third_out , \平时作业2_红绿灯1_2_yellow , \平时作业2_红绿灯1_3_green , \平时作业2_红绿灯1_3_red ,
       \平时作业2_红绿灯1_3_yellow ;

  \平时作业2_红绿灯1  \u_平时作业2_红绿灯1_1  (
    .First(in_1), .Second(1'b0), .Third(1'b0), .Red(\平时作业2_红绿灯1_1_red ), .Yellow(\平时作业2_红绿灯1_1_yellow ),
    .Green(\平时作业2_红绿灯1_1_green ), .Second_Out(\平时作业2_红绿灯1_1_second_out ), .Third_Out(\平时作业2_红绿灯1_1_third_out ));
  \平时作业2_红绿灯1  \u_平时作业2_红绿灯1_2  (
    .First(in_2), .Second(\平时作业2_红绿灯1_1_second_out ), .Third(\平时作业2_红绿灯1_1_third_out ),
    .Red(\平时作业2_红绿灯1_2_red ), .Yellow(\平时作业2_红绿灯1_2_yellow ), .Green(\平时作业2_红绿灯1_2_green ),
    .Second_Out(\平时作业2_红绿灯1_2_second_out ), .Third_Out(\平时作业2_红绿灯1_2_third_out ));
  \平时作业2_红绿灯1  \u_平时作业2_红绿灯1_3  (
    .First(in_3), .Second(\平时作业2_红绿灯1_2_second_out ), .Third(\平时作业2_红绿灯1_2_third_out ),
    .Red(\平时作业2_红绿灯1_3_red ), .Yellow(\平时作业2_红绿灯1_3_yellow ), .Green(\平时作业2_红绿灯1_3_green ),
    .Second_Out(out_4), .Third_Out(out_5));
  LED #(.active("true")) led_1 (.in(\平时作业2_红绿灯1_1_red ));
  LED #(.active("true")) led_2 (.in(\平时作业2_红绿灯1_1_yellow ));
  LED #(.active("true")) led_3 (.in(\平时作业2_红绿灯1_1_green ));
  LED #(.active("true")) led_4 (.in(\平时作业2_红绿灯1_2_red ));
  LED #(.active("true")) led_5 (.in(\平时作业2_红绿灯1_2_yellow ));
  LED #(.active("true")) led_6 (.in(\平时作业2_红绿灯1_2_green ));
  LED #(.active("true")) led_7 (.in(\平时作业2_红绿灯1_3_red ));
  LED #(.active("true")) led_8 (.in(\平时作业2_红绿灯1_3_yellow ));
  LED #(.active("true")) led_9 (.in(\平时作业2_红绿灯1_3_green ));

  // Notes on the sheet:
  //   第 i+1 段
  //   第 i 段
  //   第 i-1 段
endmodule
module \平时作业2_28段轨道的红绿灯  (
  input  in_1,
  input  in_2,
  input  in_3,
  input  in_4,
  input  in_5,
  input  in_6,
  input  in_7,
  input  in_8,
  input  in_9,
  input  in_10,
  input  in_11,
  input  in_12,
  input  in_13,
  input  in_14,
  input  in_15,
  input  in_16,
  input  in_17,
  input  in_18,
  input  in_19,
  input  in_20,
  input  in_21,
  input  in_22,
  input  in_23,
  input  in_24,
  input  in_25,
  input  in_26,
  input  in_27,
  input  in_28,
  output out_29,
  output out_30
);

  wire \平时作业2_红绿灯1_1_green , \平时作业2_红绿灯1_1_red , \平时作业2_红绿灯1_1_second_out , \平时作业2_红绿灯1_1_third_out ,
       \平时作业2_红绿灯1_1_yellow , \平时作业2_红绿灯1_2_green , \平时作业2_红绿灯1_2_red , \平时作业2_红绿灯1_2_second_out ,
       \平时作业2_红绿灯1_2_third_out , \平时作业2_红绿灯1_2_yellow , \平时作业2_红绿灯1_3_green , \平时作业2_红绿灯1_3_red ,
       \平时作业2_红绿灯1_3_second_out , \平时作业2_红绿灯1_3_third_out , \平时作业2_红绿灯1_3_yellow , \平时作业2_红绿灯1_4_green ,
       \平时作业2_红绿灯1_4_red , \平时作业2_红绿灯1_4_second_out , \平时作业2_红绿灯1_4_third_out , \平时作业2_红绿灯1_4_yellow ,
       \平时作业2_红绿灯1_5_green , \平时作业2_红绿灯1_5_red , \平时作业2_红绿灯1_5_second_out , \平时作业2_红绿灯1_5_third_out ,
       \平时作业2_红绿灯1_5_yellow , \平时作业2_红绿灯1_6_green , \平时作业2_红绿灯1_6_red , \平时作业2_红绿灯1_6_second_out ,
       \平时作业2_红绿灯1_6_third_out , \平时作业2_红绿灯1_6_yellow , \平时作业2_红绿灯1_7_green , \平时作业2_红绿灯1_7_red ,
       \平时作业2_红绿灯1_7_second_out , \平时作业2_红绿灯1_7_third_out , \平时作业2_红绿灯1_7_yellow , \平时作业2_红绿灯1_8_green ,
       \平时作业2_红绿灯1_8_red , \平时作业2_红绿灯1_8_second_out , \平时作业2_红绿灯1_8_third_out , \平时作业2_红绿灯1_8_yellow ,
       \平时作业2_红绿灯1_9_green , \平时作业2_红绿灯1_9_red , \平时作业2_红绿灯1_9_second_out , \平时作业2_红绿灯1_9_third_out ,
       \平时作业2_红绿灯1_9_yellow , \平时作业2_红绿灯1_10_green , \平时作业2_红绿灯1_10_red , \平时作业2_红绿灯1_10_second_out ,
       \平时作业2_红绿灯1_10_third_out , \平时作业2_红绿灯1_10_yellow , \平时作业2_红绿灯1_11_green , \平时作业2_红绿灯1_11_red ,
       \平时作业2_红绿灯1_11_second_out , \平时作业2_红绿灯1_11_third_out , \平时作业2_红绿灯1_11_yellow , \平时作业2_红绿灯1_12_green ,
       \平时作业2_红绿灯1_12_red , \平时作业2_红绿灯1_12_second_out , \平时作业2_红绿灯1_12_third_out , \平时作业2_红绿灯1_12_yellow ,
       \平时作业2_红绿灯1_13_green , \平时作业2_红绿灯1_13_red , \平时作业2_红绿灯1_13_second_out , \平时作业2_红绿灯1_13_third_out ,
       \平时作业2_红绿灯1_13_yellow , \平时作业2_红绿灯1_14_green , \平时作业2_红绿灯1_14_red , \平时作业2_红绿灯1_14_second_out ,
       \平时作业2_红绿灯1_14_third_out , \平时作业2_红绿灯1_14_yellow , \平时作业2_红绿灯1_15_green , \平时作业2_红绿灯1_15_red ,
       \平时作业2_红绿灯1_15_second_out , \平时作业2_红绿灯1_15_third_out , \平时作业2_红绿灯1_15_yellow , \平时作业2_红绿灯1_16_green ,
       \平时作业2_红绿灯1_16_red , \平时作业2_红绿灯1_16_second_out , \平时作业2_红绿灯1_16_third_out , \平时作业2_红绿灯1_16_yellow ,
       \平时作业2_红绿灯1_17_green , \平时作业2_红绿灯1_17_red , \平时作业2_红绿灯1_17_second_out , \平时作业2_红绿灯1_17_third_out ,
       \平时作业2_红绿灯1_17_yellow , \平时作业2_红绿灯1_18_green , \平时作业2_红绿灯1_18_red , \平时作业2_红绿灯1_18_second_out ,
       \平时作业2_红绿灯1_18_third_out , \平时作业2_红绿灯1_18_yellow , \平时作业2_红绿灯1_19_green , \平时作业2_红绿灯1_19_red ,
       \平时作业2_红绿灯1_19_second_out , \平时作业2_红绿灯1_19_third_out , \平时作业2_红绿灯1_19_yellow , \平时作业2_红绿灯1_20_green ,
       \平时作业2_红绿灯1_20_red , \平时作业2_红绿灯1_20_second_out , \平时作业2_红绿灯1_20_third_out , \平时作业2_红绿灯1_20_yellow ,
       \平时作业2_红绿灯1_21_green , \平时作业2_红绿灯1_21_red , \平时作业2_红绿灯1_21_second_out , \平时作业2_红绿灯1_21_third_out ,
       \平时作业2_红绿灯1_21_yellow , \平时作业2_红绿灯1_22_green , \平时作业2_红绿灯1_22_red , \平时作业2_红绿灯1_22_second_out ,
       \平时作业2_红绿灯1_22_third_out , \平时作业2_红绿灯1_22_yellow , \平时作业2_红绿灯1_23_green , \平时作业2_红绿灯1_23_red ,
       \平时作业2_红绿灯1_23_second_out , \平时作业2_红绿灯1_23_third_out , \平时作业2_红绿灯1_23_yellow , \平时作业2_红绿灯1_24_green ,
       \平时作业2_红绿灯1_24_red , \平时作业2_红绿灯1_24_second_out , \平时作业2_红绿灯1_24_third_out , \平时作业2_红绿灯1_24_yellow ,
       \平时作业2_红绿灯1_25_green , \平时作业2_红绿灯1_25_red , \平时作业2_红绿灯1_25_second_out , \平时作业2_红绿灯1_25_third_out ,
       \平时作业2_红绿灯1_25_yellow , \平时作业2_红绿灯1_26_green , \平时作业2_红绿灯1_26_red , \平时作业2_红绿灯1_26_second_out ,
       \平时作业2_红绿灯1_26_third_out , \平时作业2_红绿灯1_26_yellow , \平时作业2_红绿灯1_27_green , \平时作业2_红绿灯1_27_red ,
       \平时作业2_红绿灯1_27_second_out , \平时作业2_红绿灯1_27_third_out , \平时作业2_红绿灯1_27_yellow , \平时作业2_红绿灯1_28_green ,
       \平时作业2_红绿灯1_28_red , \平时作业2_红绿灯1_28_yellow ;

  \平时作业2_红绿灯1  \u_平时作业2_红绿灯1_1  (
    .First(in_1), .Second(1'b0), .Third(1'b0), .Red(\平时作业2_红绿灯1_1_red ), .Yellow(\平时作业2_红绿灯1_1_yellow ),
    .Green(\平时作业2_红绿灯1_1_green ), .Second_Out(\平时作业2_红绿灯1_1_second_out ), .Third_Out(\平时作业2_红绿灯1_1_third_out ));
  \平时作业2_红绿灯1  \u_平时作业2_红绿灯1_2  (
    .First(in_2), .Second(\平时作业2_红绿灯1_1_second_out ), .Third(\平时作业2_红绿灯1_1_third_out ),
    .Red(\平时作业2_红绿灯1_2_red ), .Yellow(\平时作业2_红绿灯1_2_yellow ), .Green(\平时作业2_红绿灯1_2_green ),
    .Second_Out(\平时作业2_红绿灯1_2_second_out ), .Third_Out(\平时作业2_红绿灯1_2_third_out ));
  \平时作业2_红绿灯1  \u_平时作业2_红绿灯1_3  (
    .First(in_3), .Second(\平时作业2_红绿灯1_2_second_out ), .Third(\平时作业2_红绿灯1_2_third_out ),
    .Red(\平时作业2_红绿灯1_3_red ), .Yellow(\平时作业2_红绿灯1_3_yellow ), .Green(\平时作业2_红绿灯1_3_green ),
    .Second_Out(\平时作业2_红绿灯1_3_second_out ), .Third_Out(\平时作业2_红绿灯1_3_third_out ));
  \平时作业2_红绿灯1  \u_平时作业2_红绿灯1_4  (
    .First(in_4), .Second(\平时作业2_红绿灯1_3_second_out ), .Third(\平时作业2_红绿灯1_3_third_out ),
    .Red(\平时作业2_红绿灯1_4_red ), .Yellow(\平时作业2_红绿灯1_4_yellow ), .Green(\平时作业2_红绿灯1_4_green ),
    .Second_Out(\平时作业2_红绿灯1_4_second_out ), .Third_Out(\平时作业2_红绿灯1_4_third_out ));
  \平时作业2_红绿灯1  \u_平时作业2_红绿灯1_5  (
    .First(in_5), .Second(\平时作业2_红绿灯1_4_second_out ), .Third(\平时作业2_红绿灯1_4_third_out ),
    .Red(\平时作业2_红绿灯1_5_red ), .Yellow(\平时作业2_红绿灯1_5_yellow ), .Green(\平时作业2_红绿灯1_5_green ),
    .Second_Out(\平时作业2_红绿灯1_5_second_out ), .Third_Out(\平时作业2_红绿灯1_5_third_out ));
  \平时作业2_红绿灯1  \u_平时作业2_红绿灯1_6  (
    .First(in_6), .Second(\平时作业2_红绿灯1_5_second_out ), .Third(\平时作业2_红绿灯1_5_third_out ),
    .Red(\平时作业2_红绿灯1_6_red ), .Yellow(\平时作业2_红绿灯1_6_yellow ), .Green(\平时作业2_红绿灯1_6_green ),
    .Second_Out(\平时作业2_红绿灯1_6_second_out ), .Third_Out(\平时作业2_红绿灯1_6_third_out ));
  \平时作业2_红绿灯1  \u_平时作业2_红绿灯1_7  (
    .First(in_7), .Second(\平时作业2_红绿灯1_6_second_out ), .Third(\平时作业2_红绿灯1_6_third_out ),
    .Red(\平时作业2_红绿灯1_7_red ), .Yellow(\平时作业2_红绿灯1_7_yellow ), .Green(\平时作业2_红绿灯1_7_green ),
    .Second_Out(\平时作业2_红绿灯1_7_second_out ), .Third_Out(\平时作业2_红绿灯1_7_third_out ));
  \平时作业2_红绿灯1  \u_平时作业2_红绿灯1_8  (
    .First(in_8), .Second(\平时作业2_红绿灯1_7_second_out ), .Third(\平时作业2_红绿灯1_7_third_out ),
    .Red(\平时作业2_红绿灯1_8_red ), .Yellow(\平时作业2_红绿灯1_8_yellow ), .Green(\平时作业2_红绿灯1_8_green ),
    .Second_Out(\平时作业2_红绿灯1_8_second_out ), .Third_Out(\平时作业2_红绿灯1_8_third_out ));
  \平时作业2_红绿灯1  \u_平时作业2_红绿灯1_9  (
    .First(in_9), .Second(\平时作业2_红绿灯1_8_second_out ), .Third(\平时作业2_红绿灯1_8_third_out ),
    .Red(\平时作业2_红绿灯1_9_red ), .Yellow(\平时作业2_红绿灯1_9_yellow ), .Green(\平时作业2_红绿灯1_9_green ),
    .Second_Out(\平时作业2_红绿灯1_9_second_out ), .Third_Out(\平时作业2_红绿灯1_9_third_out ));
  \平时作业2_红绿灯1  \u_平时作业2_红绿灯1_10  (
    .First(in_10), .Second(\平时作业2_红绿灯1_9_second_out ), .Third(\平时作业2_红绿灯1_9_third_out ),
    .Red(\平时作业2_红绿灯1_10_red ), .Yellow(\平时作业2_红绿灯1_10_yellow ), .Green(\平时作业2_红绿灯1_10_green ),
    .Second_Out(\平时作业2_红绿灯1_10_second_out ), .Third_Out(\平时作业2_红绿灯1_10_third_out ));
  \平时作业2_红绿灯1  \u_平时作业2_红绿灯1_11  (
    .First(in_11), .Second(\平时作业2_红绿灯1_10_second_out ), .Third(\平时作业2_红绿灯1_10_third_out ),
    .Red(\平时作业2_红绿灯1_11_red ), .Yellow(\平时作业2_红绿灯1_11_yellow ), .Green(\平时作业2_红绿灯1_11_green ),
    .Second_Out(\平时作业2_红绿灯1_11_second_out ), .Third_Out(\平时作业2_红绿灯1_11_third_out ));
  \平时作业2_红绿灯1  \u_平时作业2_红绿灯1_12  (
    .First(in_12), .Second(\平时作业2_红绿灯1_11_second_out ), .Third(\平时作业2_红绿灯1_11_third_out ),
    .Red(\平时作业2_红绿灯1_12_red ), .Yellow(\平时作业2_红绿灯1_12_yellow ), .Green(\平时作业2_红绿灯1_12_green ),
    .Second_Out(\平时作业2_红绿灯1_12_second_out ), .Third_Out(\平时作业2_红绿灯1_12_third_out ));
  \平时作业2_红绿灯1  \u_平时作业2_红绿灯1_13  (
    .First(in_13), .Second(\平时作业2_红绿灯1_12_second_out ), .Third(\平时作业2_红绿灯1_12_third_out ),
    .Red(\平时作业2_红绿灯1_13_red ), .Yellow(\平时作业2_红绿灯1_13_yellow ), .Green(\平时作业2_红绿灯1_13_green ),
    .Second_Out(\平时作业2_红绿灯1_13_second_out ), .Third_Out(\平时作业2_红绿灯1_13_third_out ));
  \平时作业2_红绿灯1  \u_平时作业2_红绿灯1_14  (
    .First(in_14), .Second(\平时作业2_红绿灯1_13_second_out ), .Third(\平时作业2_红绿灯1_13_third_out ),
    .Red(\平时作业2_红绿灯1_14_red ), .Yellow(\平时作业2_红绿灯1_14_yellow ), .Green(\平时作业2_红绿灯1_14_green ),
    .Second_Out(\平时作业2_红绿灯1_14_second_out ), .Third_Out(\平时作业2_红绿灯1_14_third_out ));
  \平时作业2_红绿灯1  \u_平时作业2_红绿灯1_15  (
    .First(in_15), .Second(\平时作业2_红绿灯1_14_second_out ), .Third(\平时作业2_红绿灯1_14_third_out ),
    .Red(\平时作业2_红绿灯1_15_red ), .Yellow(\平时作业2_红绿灯1_15_yellow ), .Green(\平时作业2_红绿灯1_15_green ),
    .Second_Out(\平时作业2_红绿灯1_15_second_out ), .Third_Out(\平时作业2_红绿灯1_15_third_out ));
  \平时作业2_红绿灯1  \u_平时作业2_红绿灯1_16  (
    .First(in_16), .Second(\平时作业2_红绿灯1_15_second_out ), .Third(\平时作业2_红绿灯1_15_third_out ),
    .Red(\平时作业2_红绿灯1_16_red ), .Yellow(\平时作业2_红绿灯1_16_yellow ), .Green(\平时作业2_红绿灯1_16_green ),
    .Second_Out(\平时作业2_红绿灯1_16_second_out ), .Third_Out(\平时作业2_红绿灯1_16_third_out ));
  \平时作业2_红绿灯1  \u_平时作业2_红绿灯1_17  (
    .First(in_17), .Second(\平时作业2_红绿灯1_16_second_out ), .Third(\平时作业2_红绿灯1_16_third_out ),
    .Red(\平时作业2_红绿灯1_17_red ), .Yellow(\平时作业2_红绿灯1_17_yellow ), .Green(\平时作业2_红绿灯1_17_green ),
    .Second_Out(\平时作业2_红绿灯1_17_second_out ), .Third_Out(\平时作业2_红绿灯1_17_third_out ));
  \平时作业2_红绿灯1  \u_平时作业2_红绿灯1_18  (
    .First(in_18), .Second(\平时作业2_红绿灯1_17_second_out ), .Third(\平时作业2_红绿灯1_17_third_out ),
    .Red(\平时作业2_红绿灯1_18_red ), .Yellow(\平时作业2_红绿灯1_18_yellow ), .Green(\平时作业2_红绿灯1_18_green ),
    .Second_Out(\平时作业2_红绿灯1_18_second_out ), .Third_Out(\平时作业2_红绿灯1_18_third_out ));
  \平时作业2_红绿灯1  \u_平时作业2_红绿灯1_19  (
    .First(in_19), .Second(\平时作业2_红绿灯1_18_second_out ), .Third(\平时作业2_红绿灯1_18_third_out ),
    .Red(\平时作业2_红绿灯1_19_red ), .Yellow(\平时作业2_红绿灯1_19_yellow ), .Green(\平时作业2_红绿灯1_19_green ),
    .Second_Out(\平时作业2_红绿灯1_19_second_out ), .Third_Out(\平时作业2_红绿灯1_19_third_out ));
  \平时作业2_红绿灯1  \u_平时作业2_红绿灯1_20  (
    .First(in_20), .Second(\平时作业2_红绿灯1_19_second_out ), .Third(\平时作业2_红绿灯1_19_third_out ),
    .Red(\平时作业2_红绿灯1_20_red ), .Yellow(\平时作业2_红绿灯1_20_yellow ), .Green(\平时作业2_红绿灯1_20_green ),
    .Second_Out(\平时作业2_红绿灯1_20_second_out ), .Third_Out(\平时作业2_红绿灯1_20_third_out ));
  \平时作业2_红绿灯1  \u_平时作业2_红绿灯1_21  (
    .First(in_21), .Second(\平时作业2_红绿灯1_20_second_out ), .Third(\平时作业2_红绿灯1_20_third_out ),
    .Red(\平时作业2_红绿灯1_21_red ), .Yellow(\平时作业2_红绿灯1_21_yellow ), .Green(\平时作业2_红绿灯1_21_green ),
    .Second_Out(\平时作业2_红绿灯1_21_second_out ), .Third_Out(\平时作业2_红绿灯1_21_third_out ));
  \平时作业2_红绿灯1  \u_平时作业2_红绿灯1_22  (
    .First(in_22), .Second(\平时作业2_红绿灯1_21_second_out ), .Third(\平时作业2_红绿灯1_21_third_out ),
    .Red(\平时作业2_红绿灯1_22_red ), .Yellow(\平时作业2_红绿灯1_22_yellow ), .Green(\平时作业2_红绿灯1_22_green ),
    .Second_Out(\平时作业2_红绿灯1_22_second_out ), .Third_Out(\平时作业2_红绿灯1_22_third_out ));
  \平时作业2_红绿灯1  \u_平时作业2_红绿灯1_23  (
    .First(in_23), .Second(\平时作业2_红绿灯1_22_second_out ), .Third(\平时作业2_红绿灯1_22_third_out ),
    .Red(\平时作业2_红绿灯1_23_red ), .Yellow(\平时作业2_红绿灯1_23_yellow ), .Green(\平时作业2_红绿灯1_23_green ),
    .Second_Out(\平时作业2_红绿灯1_23_second_out ), .Third_Out(\平时作业2_红绿灯1_23_third_out ));
  \平时作业2_红绿灯1  \u_平时作业2_红绿灯1_24  (
    .First(in_24), .Second(\平时作业2_红绿灯1_23_second_out ), .Third(\平时作业2_红绿灯1_23_third_out ),
    .Red(\平时作业2_红绿灯1_24_red ), .Yellow(\平时作业2_红绿灯1_24_yellow ), .Green(\平时作业2_红绿灯1_24_green ),
    .Second_Out(\平时作业2_红绿灯1_24_second_out ), .Third_Out(\平时作业2_红绿灯1_24_third_out ));
  \平时作业2_红绿灯1  \u_平时作业2_红绿灯1_25  (
    .First(in_25), .Second(\平时作业2_红绿灯1_24_second_out ), .Third(\平时作业2_红绿灯1_24_third_out ),
    .Red(\平时作业2_红绿灯1_25_red ), .Yellow(\平时作业2_红绿灯1_25_yellow ), .Green(\平时作业2_红绿灯1_25_green ),
    .Second_Out(\平时作业2_红绿灯1_25_second_out ), .Third_Out(\平时作业2_红绿灯1_25_third_out ));
  \平时作业2_红绿灯1  \u_平时作业2_红绿灯1_26  (
    .First(in_26), .Second(\平时作业2_红绿灯1_25_second_out ), .Third(\平时作业2_红绿灯1_25_third_out ),
    .Red(\平时作业2_红绿灯1_26_red ), .Yellow(\平时作业2_红绿灯1_26_yellow ), .Green(\平时作业2_红绿灯1_26_green ),
    .Second_Out(\平时作业2_红绿灯1_26_second_out ), .Third_Out(\平时作业2_红绿灯1_26_third_out ));
  \平时作业2_红绿灯1  \u_平时作业2_红绿灯1_27  (
    .First(in_27), .Second(\平时作业2_红绿灯1_26_second_out ), .Third(\平时作业2_红绿灯1_26_third_out ),
    .Red(\平时作业2_红绿灯1_27_red ), .Yellow(\平时作业2_红绿灯1_27_yellow ), .Green(\平时作业2_红绿灯1_27_green ),
    .Second_Out(\平时作业2_红绿灯1_27_second_out ), .Third_Out(\平时作业2_红绿灯1_27_third_out ));
  \平时作业2_红绿灯1  \u_平时作业2_红绿灯1_28  (
    .First(in_28), .Second(\平时作业2_红绿灯1_27_second_out ), .Third(\平时作业2_红绿灯1_27_third_out ),
    .Red(\平时作业2_红绿灯1_28_red ), .Yellow(\平时作业2_红绿灯1_28_yellow ), .Green(\平时作业2_红绿灯1_28_green ),
    .Second_Out(out_29), .Third_Out(out_30));
  LED #(.active("true")) led_1 (.in(\平时作业2_红绿灯1_1_red ));
  LED #(.active("true")) led_2 (.in(\平时作业2_红绿灯1_1_yellow ));
  LED #(.active("true")) led_3 (.in(\平时作业2_红绿灯1_1_green ));
  LED #(.active("true")) led_4 (.in(\平时作业2_红绿灯1_2_red ));
  LED #(.active("true")) led_5 (.in(\平时作业2_红绿灯1_2_yellow ));
  LED #(.active("true")) led_6 (.in(\平时作业2_红绿灯1_2_green ));
  LED #(.active("true")) led_7 (.in(\平时作业2_红绿灯1_3_red ));
  LED #(.active("true")) led_8 (.in(\平时作业2_红绿灯1_3_yellow ));
  LED #(.active("true")) led_9 (.in(\平时作业2_红绿灯1_3_green ));
  LED #(.active("true")) led_10 (.in(\平时作业2_红绿灯1_4_red ));
  LED #(.active("true")) led_11 (.in(\平时作业2_红绿灯1_4_yellow ));
  LED #(.active("true")) led_12 (.in(\平时作业2_红绿灯1_4_green ));
  LED #(.active("true")) led_13 (.in(\平时作业2_红绿灯1_5_red ));
  LED #(.active("true")) led_14 (.in(\平时作业2_红绿灯1_5_yellow ));
  LED #(.active("true")) led_15 (.in(\平时作业2_红绿灯1_5_green ));
  LED #(.active("true")) led_16 (.in(\平时作业2_红绿灯1_6_red ));
  LED #(.active("true")) led_17 (.in(\平时作业2_红绿灯1_6_yellow ));
  LED #(.active("true")) led_18 (.in(\平时作业2_红绿灯1_6_green ));
  LED #(.active("true")) led_19 (.in(\平时作业2_红绿灯1_7_red ));
  LED #(.active("true")) led_20 (.in(\平时作业2_红绿灯1_7_yellow ));
  LED #(.active("true")) led_21 (.in(\平时作业2_红绿灯1_7_green ));
  LED #(.active("true")) led_22 (.in(\平时作业2_红绿灯1_8_red ));
  LED #(.active("true")) led_23 (.in(\平时作业2_红绿灯1_8_yellow ));
  LED #(.active("true")) led_24 (.in(\平时作业2_红绿灯1_8_green ));
  LED #(.active("true")) led_25 (.in(\平时作业2_红绿灯1_9_red ));
  LED #(.active("true")) led_26 (.in(\平时作业2_红绿灯1_9_yellow ));
  LED #(.active("true")) led_27 (.in(\平时作业2_红绿灯1_9_green ));
  LED #(.active("true")) led_28 (.in(\平时作业2_红绿灯1_10_red ));
  LED #(.active("true")) led_29 (.in(\平时作业2_红绿灯1_10_yellow ));
  LED #(.active("true")) led_30 (.in(\平时作业2_红绿灯1_10_green ));
  LED #(.active("true")) led_31 (.in(\平时作业2_红绿灯1_11_red ));
  LED #(.active("true")) led_32 (.in(\平时作业2_红绿灯1_11_yellow ));
  LED #(.active("true")) led_33 (.in(\平时作业2_红绿灯1_11_green ));
  LED #(.active("true")) led_34 (.in(\平时作业2_红绿灯1_12_red ));
  LED #(.active("true")) led_35 (.in(\平时作业2_红绿灯1_12_yellow ));
  LED #(.active("true")) led_36 (.in(\平时作业2_红绿灯1_12_green ));
  LED #(.active("true")) led_37 (.in(\平时作业2_红绿灯1_13_red ));
  LED #(.active("true")) led_38 (.in(\平时作业2_红绿灯1_13_yellow ));
  LED #(.active("true")) led_39 (.in(\平时作业2_红绿灯1_13_green ));
  LED #(.active("true")) led_40 (.in(\平时作业2_红绿灯1_14_red ));
  LED #(.active("true")) led_41 (.in(\平时作业2_红绿灯1_14_yellow ));
  LED #(.active("true")) led_42 (.in(\平时作业2_红绿灯1_14_green ));
  LED #(.active("true")) led_43 (.in(\平时作业2_红绿灯1_15_red ));
  LED #(.active("true")) led_44 (.in(\平时作业2_红绿灯1_15_yellow ));
  LED #(.active("true")) led_45 (.in(\平时作业2_红绿灯1_15_green ));
  LED #(.active("true")) led_46 (.in(\平时作业2_红绿灯1_16_red ));
  LED #(.active("true")) led_47 (.in(\平时作业2_红绿灯1_16_yellow ));
  LED #(.active("true")) led_48 (.in(\平时作业2_红绿灯1_16_green ));
  LED #(.active("true")) led_49 (.in(\平时作业2_红绿灯1_17_red ));
  LED #(.active("true")) led_50 (.in(\平时作业2_红绿灯1_17_yellow ));
  LED #(.active("true")) led_51 (.in(\平时作业2_红绿灯1_17_green ));
  LED #(.active("true")) led_52 (.in(\平时作业2_红绿灯1_18_red ));
  LED #(.active("true")) led_53 (.in(\平时作业2_红绿灯1_18_yellow ));
  LED #(.active("true")) led_54 (.in(\平时作业2_红绿灯1_18_green ));
  LED #(.active("true")) led_55 (.in(\平时作业2_红绿灯1_19_red ));
  LED #(.active("true")) led_56 (.in(\平时作业2_红绿灯1_19_yellow ));
  LED #(.active("true")) led_57 (.in(\平时作业2_红绿灯1_19_green ));
  LED #(.active("true")) led_58 (.in(\平时作业2_红绿灯1_20_red ));
  LED #(.active("true")) led_59 (.in(\平时作业2_红绿灯1_20_yellow ));
  LED #(.active("true")) led_60 (.in(\平时作业2_红绿灯1_20_green ));
  LED #(.active("true")) led_61 (.in(\平时作业2_红绿灯1_21_red ));
  LED #(.active("true")) led_62 (.in(\平时作业2_红绿灯1_21_yellow ));
  LED #(.active("true")) led_63 (.in(\平时作业2_红绿灯1_21_green ));
  LED #(.active("true")) led_64 (.in(\平时作业2_红绿灯1_22_red ));
  LED #(.active("true")) led_65 (.in(\平时作业2_红绿灯1_22_yellow ));
  LED #(.active("true")) led_66 (.in(\平时作业2_红绿灯1_22_green ));
  LED #(.active("true")) led_67 (.in(\平时作业2_红绿灯1_23_red ));
  LED #(.active("true")) led_68 (.in(\平时作业2_红绿灯1_23_yellow ));
  LED #(.active("true")) led_69 (.in(\平时作业2_红绿灯1_23_green ));
  LED #(.active("true")) led_70 (.in(\平时作业2_红绿灯1_24_red ));
  LED #(.active("true")) led_71 (.in(\平时作业2_红绿灯1_24_yellow ));
  LED #(.active("true")) led_72 (.in(\平时作业2_红绿灯1_24_green ));
  LED #(.active("true")) led_73 (.in(\平时作业2_红绿灯1_25_red ));
  LED #(.active("true")) led_74 (.in(\平时作业2_红绿灯1_25_yellow ));
  LED #(.active("true")) led_75 (.in(\平时作业2_红绿灯1_25_green ));
  LED #(.active("true")) led_76 (.in(\平时作业2_红绿灯1_26_red ));
  LED #(.active("true")) led_77 (.in(\平时作业2_红绿灯1_26_yellow ));
  LED #(.active("true")) led_78 (.in(\平时作业2_红绿灯1_26_green ));
  LED #(.active("true")) led_79 (.in(\平时作业2_红绿灯1_27_red ));
  LED #(.active("true")) led_80 (.in(\平时作业2_红绿灯1_27_yellow ));
  LED #(.active("true")) led_81 (.in(\平时作业2_红绿灯1_27_green ));
  LED #(.active("true")) led_82 (.in(\平时作业2_红绿灯1_28_red ));
  LED #(.active("true")) led_83 (.in(\平时作业2_红绿灯1_28_yellow ));
  LED #(.active("true")) led_84 (.in(\平时作业2_红绿灯1_28_green ));

  // Notes on the sheet:
  //   红灯
  //   黄灯
  //   绿灯
  //   红灯
  //   黄灯
  //   绿灯
  //   红灯
  //   黄灯
  //   绿灯
  //   红灯
  //   黄灯
  //   绿灯
  //   红灯
  //   红灯
  //   黄灯
  //   绿灯
  //   红灯
  //   黄灯
  //   绿灯
  //   下面都是红灯/黄灯/绿灯
endmodule

module \平时作业3_SR锁存器  (
  input  R,
  input  S,
  output Q,
  output Q_prime
);

  nor nor_1 (Q, R, Q_prime);
  nor nor_2 (Q_prime, Q, S);
endmodule

module \平时作业3_D锁存器  (
  input  Reset,
  input  CLK,
  input  D,
  output Q,
  output Q_prime
);

  wire and_1_out, and_2_out, not_1_out, or_1_out;

  and and_1 (and_1_out, CLK, not_1_out);
  not not_1 (not_1_out, D);
  and and_2 (and_2_out, CLK, D);
  or or_1 (or_1_out, Reset, and_1_out);
  \平时作业3_SR锁存器  \u_平时作业3_sr锁存器_1  (.R(or_1_out), .S(and_2_out), .Q(Q), .Q_prime(Q_prime));
endmodule

module \平时作业3_D触发器_带Reset  (
  input  CLK,
  input  D,
  input  Reset,
  output Q,
  output Q_prime
);

  wire not_1_out, \平时作业3_d锁存器_1_q ;

  not not_1 (not_1_out, CLK);
  \平时作业3_D锁存器  \u_平时作业3_d锁存器_1  (.CLK(not_1_out), .D(D), .Q(\平时作业3_d锁存器_1_q ), .Reset(Reset));  // open: Q_prime
  \平时作业3_D锁存器  \u_平时作业3_d锁存器_2  (.CLK(CLK), .D(\平时作业3_d锁存器_1_q ), .Q(Q), .Q_prime(Q_prime), .Reset(Reset));
endmodule

module \平时作业3_2位状态寄存器  (
  input  CLK,
  input  S1_prime,
  input  S0_prime,
  input  Reset,
  output S1,
  output S0
);

  \平时作业3_D触发器_带Reset  \u_平时作业3_d触发器_带reset_1  (.D(S1_prime), .Q(S1), .CLK(CLK), .Reset(Reset));  // open: Q_prime
  \平时作业3_D触发器_带Reset  \u_平时作业3_d触发器_带reset_2  (.D(S0_prime), .Q(S0), .CLK(CLK), .Reset(Reset));  // open: Q_prime
endmodule

module \平时作业3_交通控制器_有限状态机  (
  input  CLK,
  input  TA,
  input  TB,
  input  Reset,
  output AR,
  output AY,
  output AG,
  output BR,
  output BY,
  output BG
);

  wire and_1_out, and_2_out, and_3_out, and_4_out, not_1_out, or_1_out, xor_1_out, \平时作业3_2位状态寄存器_1_s0 ,
       \平时作业3_2位状态寄存器_1_s1 ;

  and and_1 (and_1_out, ~\平时作业3_2位状态寄存器_1_s1 , ~\平时作业3_2位状态寄存器_1_s0 , ~TA);  // AND_Gate
  and and_2 (and_2_out, \平时作业3_2位状态寄存器_1_s1 , ~\平时作业3_2位状态寄存器_1_s0 , ~TB);  // AND_Gate
  xor xor_1 (xor_1_out, \平时作业3_2位状态寄存器_1_s1 , \平时作业3_2位状态寄存器_1_s0 );
  or or_1 (or_1_out, and_1_out, and_2_out);
  \平时作业3_2位状态寄存器  \u_平时作业3_2位状态寄存器_1  (
    .S1_prime(xor_1_out), .S0_prime(or_1_out), .S1(\平时作业3_2位状态寄存器_1_s1 ), .S0(\平时作业3_2位状态寄存器_1_s0 ),
    .CLK(CLK), .Reset(Reset));
  and and_3 (and_3_out, ~\平时作业3_2位状态寄存器_1_s1 , \平时作业3_2位状态寄存器_1_s0 );  // AND_Gate
  not not_1 (not_1_out, \平时作业3_2位状态寄存器_1_s1 );
  and and_4 (and_4_out, \平时作业3_2位状态寄存器_1_s1 , \平时作业3_2位状态寄存器_1_s0 );
  and and_5 (AR, \平时作业3_2位状态寄存器_1_s1 , ~and_3_out);  // AND_Gate
  and and_6 (AY, ~\平时作业3_2位状态寄存器_1_s1 , and_3_out);  // AND_Gate
  and and_7 (AG, ~\平时作业3_2位状态寄存器_1_s1 , ~and_3_out);  // AND_Gate
  and and_8 (BR, not_1_out, ~and_4_out);  // AND_Gate
  and and_9 (BY, ~not_1_out, and_4_out);  // AND_Gate
  and and_10 (BG, ~not_1_out, ~and_4_out);  // AND_Gate
endmodule

module \平时作业3_交通控制器显示  (
  input  TA,
  input  TB,
  input  Reset
);

  wire AG, AR, AY, BG, BR, BY, clock_1_out;

  Clock #(.highDuration(1), .lowDuration(1)) clock_1 (.out(clock_1_out));
  \平时作业3_交通控制器_有限状态机  \u_平时作业3_交通控制器_有限状态机_1  (
    .CLK(clock_1_out), .TA(TA), .TB(TB), .Reset(Reset), .AR(AR), .AY(AY), .AG(AG), .BR(BR), .BY(BY), .BG(BG));
  LED #(.active("true")) led_1 (.in(AR));
  LED #(.active("true")) led_2 (.in(AY));
  LED #(.active("true")) led_3 (.in(AG));
  LED #(.active("true")) led_4 (.in(BR));
  LED #(.active("true")) led_5 (.in(BG));
  LED #(.active("true")) led_6 (.in(BY));
  LED #(.active("true")) led_7 (.in(BG));
  LED #(.active("true")) led_8 (.in(BY));
  LED #(.active("true")) led_9 (.in(BR));
  LED #(.active("true")) led_10 (.in(AG));
  LED #(.active("true")) led_11 (.in(AY));
  LED #(.active("true")) led_12 (.in(AR));
endmodule

module Practice_01 (
  input  x,
  input  y,
  input  z,
  input  [3:0] in_4,
  input  [2:0] in_5,
  input  in_6,
  input  in_7,
  input  in_8,
  input  in_9,
  output out_10,
  output [3:0] out_11,
  output out_12
);

  wire and_3_out, and_4_out, G, not_1_out, not_2_out, or_2_out, P;

  not not_1 (not_1_out, y);
  // Probe on in_4
  assign out_11 = in_4 & {in_6, in_5};  // AND_Gate and_1, 4 bits wide
  // Probe on {in_6, in_5}
  and and_2 (G, in_7, in_8);
  or or_1 (P, in_7, in_8);
  and and_3 (and_3_out, in_9, G);
  or or_2 (or_2_out, x, not_1_out);
  // Probe on out_11
  or or_3 (out_12, and_3_out, P);
  not not_2 (not_2_out, x);
  and and_4 (and_4_out, or_2_out, z);
  or or_4 (out_10, not_2_out, and_4_out);

  // Notes on the sheet:
  //   9.13
  //   探针
  //   分线器
  //   隧道
endmodule

module Practice_02 (
  input  A,
  input  B,
  input  C,
  input  x,
  input  y,
  input  z,
  output out_7,
  output out_8
);

  wire and_1_out, and_2_out, and_3_out, and_4_out, and_5_out, and_6_out, not_1_out, not_2_out, not_3_out,
       not_4_out, not_5_out, not_6_out;

  not not_1 (not_1_out, A);
  not not_2 (not_2_out, B);
  not not_3 (not_3_out, x);
  and and_1 (and_1_out, not_1_out, B);
  and and_2 (and_2_out, not_2_out, C);
  not not_4 (not_4_out, C);
  and and_3 (and_3_out, not_3_out, y, z);
  not not_5 (not_5_out, y);
  and and_4 (and_4_out, not_5_out, x, z);
  not not_6 (not_6_out, z);
  and and_5 (and_5_out, A, not_4_out);
  and and_6 (and_6_out, not_3_out, not_5_out, not_6_out);
  or or_1 (out_7, and_1_out, and_2_out, and_5_out);
  or or_2 (out_8, and_3_out, and_6_out, and_4_out);

  // Notes on the sheet:
  //   9.19
  //   h(x,y,z)=x'yz+xy'z+x'y'z'
  //   F=A'B+AC'+B'C
endmodule

module \Practice_03半加器  (
  input  x,
  input  y,
  output Carry,
  output Sum
);

  and and_1 (Carry, x, y);
  xor xor_1 (Sum, x, y);

  // Notes on the sheet:
  //   半加器：没有进位
endmodule

module \Practice_04真值表自动生成  (
  input  a,
  input  b,
  output x,
  output y
);

  wire and_2_out, and_3_out, not_1_out, not_2_out;

  and and_1 (x, a, b);
  not not_1 (not_1_out, a);
  not not_2 (not_2_out, b);
  and and_2 (and_2_out, not_1_out, b);
  and and_3 (and_3_out, a, not_2_out);
  or or_1 (y, and_2_out, and_3_out);

  // Notes on the sheet:
  //   分析组合逻辑电路
  //   半加器子电路
endmodule

module \Practice_06半加器___全加器  (
  input  in_1,
  input  in_2,
  input  in_3,
  input  \_8位全加器 ,
  input  in_5,
  input  in_6,
  input  in_7,
  input  in_8,
  input  in_9,
  input  in_10,
  input  in_11,
  output Sout,
  output Carry,
  output out_14,
  output out_15,
  output out_16,
  output out_17,
  output out_18
);

  wire \practice_03半加器_1_carry , \practice_03半加器_1_sum , \practice_03半加器_2_carry , \平时作业1_全加器子电路_2_carry ,
       \平时作业1_全加器子电路_3_carry , \平时作业1_全加器子电路_4_carry ;

  \Practice_03半加器  \practice_03半加器_1  (
    .Carry(\practice_03半加器_1_carry ), .x(in_1), .y(in_2), .Sum(\practice_03半加器_1_sum ));
  \Practice_03半加器  \practice_03半加器_2  (
    .Carry(\practice_03半加器_2_carry ), .x(\practice_03半加器_1_sum ), .y(in_3), .Sum(Sout));
  \平时作业1_全加器子电路  \u_平时作业1_全加器子电路_1  (
    .x(in_5), .y(\_8位全加器 ), .Cin(\平时作业1_全加器子电路_2_carry ), .Carry(out_14), .sum(out_15));
  or or_1 (Carry, \practice_03半加器_1_carry , \practice_03半加器_2_carry );
  \平时作业1_全加器子电路  \u_平时作业1_全加器子电路_2  (
    .x(in_7), .y(in_6), .Cin(\平时作业1_全加器子电路_3_carry ), .Carry(\平时作业1_全加器子电路_2_carry ), .sum(out_16));
  \平时作业1_全加器子电路  \u_平时作业1_全加器子电路_3  (
    .x(in_9), .y(in_8), .Cin(\平时作业1_全加器子电路_4_carry ), .Carry(\平时作业1_全加器子电路_3_carry ), .sum(out_17));
  \平时作业1_全加器子电路  \u_平时作业1_全加器子电路_4  (.x(in_11), .y(in_10), .Cin(1'b0), .Carry(\平时作业1_全加器子电路_4_carry ), .sum(out_18));

  // Notes on the sheet:
  //   Sum
  //   Cout
endmodule

module \Practice_10多路选择器  (
  input  A,
  input  B,
  input  C,
  output Y
);

  wire and_1_out, and_2_out, and_3_out, not_1_out, not_2_out, not_3_out, not_4_out;

  not not_1 (not_1_out, B);
  not not_2 (not_2_out, C);
  not not_3 (not_3_out, A);
  not not_4 (not_4_out, B);
  and and_1 (and_1_out, not_1_out, not_2_out);
  and and_2 (and_2_out, not_3_out, B, C);
  and and_3 (and_3_out, A, not_4_out);
  or or_1 (Y, and_1_out, and_2_out, and_3_out);

  // Notes on the sheet:
  //   四选一多路选择器
endmodule

module \Practice_11译码器  (
  input  [6:0] \数据总线 ,
  input  in_2,
  input  A1,
  input  A2
);

  wire and_1_out, and_2_out, and_3_out, and_4_out, clock_1_out, not_1_out, not_2_out;

  not not_1 (not_1_out, A1);
  not not_2 (not_2_out, A2);
  and and_1 (and_1_out, A1, A2);
  and and_2 (and_2_out, A1, not_2_out);
  and and_3 (and_3_out, not_1_out, A2);
  and and_4 (and_4_out, not_1_out, not_2_out);
  Clock #(.highDuration(1), .lowDuration(1)) clock_1 (.out(clock_1_out));
  TTY #(.Char_bit_width(7), .rows(1), .cols(32), .trigger("rising")) tty_1 (
    .data(\数据总线 ), .clk(clock_1_out), .we(and_1_out), .clr(in_2));
  TTY #(.Char_bit_width(7), .rows(1), .cols(32), .trigger("rising")) tty_2 (
    .data(\数据总线 ), .clk(clock_1_out), .we(and_2_out), .clr(in_2));
  TTY #(.Char_bit_width(7), .rows(1), .cols(32), .trigger("rising")) tty_3 (
    .data(\数据总线 ), .clk(clock_1_out), .we(and_3_out), .clr(in_2));
  TTY #(.Char_bit_width(7), .rows(1), .cols(32), .trigger("rising")) tty_4 (
    .data(\数据总线 ), .clk(clock_1_out), .we(and_4_out), .clr(in_2));

  // Notes on the sheet:
  //   24译码器
endmodule

module \Practic_12带使能端的触发器__二选一多路选择器  (
  input  Q,
  input  D,
  input  En,
  output Y
);

  wire and_1_out, and_2_out, not_1_out;

  not not_1 (not_1_out, En);
  and and_1 (and_1_out, D, En);
  and and_2 (and_2_out, Q, not_1_out);
  or or_1 (Y, and_1_out, and_2_out);
endmodule

module \Practic_12带使能端的触发器  (
  input  En,
  input  D,
  input  En_2,
  input  D_2,
  output Q,
  output Q_prime,
  output Q_2,
  output Q_prime_2
);

  wire and_1_out, clock_1_out, clock_2_out, \practic_12带使能端的触发器_二选一多路选择器_1_y ;

  Clock #(.highDuration(1), .lowDuration(1)) clock_1 (.out(clock_1_out));
  and and_1 (and_1_out, clock_1_out, En);
  \平时作业3_D锁存器  \u_平时作业3_d锁存器_1  (.CLK(and_1_out), .D(D), .Q(Q), .Q_prime(Q_prime));  // open: Reset
  \Practic_12带使能端的触发器__二选一多路选择器  \practic_12带使能端的触发器_二选一多路选择器_1  (
    .Q(Q_2), .Y(\practic_12带使能端的触发器_二选一多路选择器_1_y ), .D(D_2), .En(En_2));
  Clock #(.highDuration(1), .lowDuration(1)) clock_2 (.out(clock_2_out));
  \平时作业3_D锁存器  \u_平时作业3_d锁存器_2  (
    .CLK(clock_2_out), .D(\practic_12带使能端的触发器_二选一多路选择器_1_y ), .Q(Q_2), .Q_prime(Q_prime_2));  // open: Reset
endmodule

module Practice_12_Resettable_Settable_Flip_Flops (
  input  D,
  input  Reset,
  input  D_2,
  input  Set,
  output Q,
  output Q_2
);

  wire and_1_out, clock_1_out, clock_2_out, nor_1_out, \平时作业3_d锁存器_2_q ;

  and and_1 (and_1_out, D, Reset);
  nor nor_1 (nor_1_out, D_2, Set);
  Clock #(.highDuration(1), .lowDuration(1)) clock_1 (.out(clock_1_out));
  \平时作业3_D锁存器  \u_平时作业3_d锁存器_1  (.CLK(clock_1_out), .D(and_1_out), .Q(Q));  // open: Q_prime, Reset
  Clock #(.highDuration(1), .lowDuration(1)) clock_2 (.out(clock_2_out));
  \平时作业3_D锁存器  \u_平时作业3_d锁存器_2  (.CLK(clock_2_out), .D(nor_1_out), .Q(\平时作业3_d锁存器_2_q ));  // open: Q_prime, Reset
  not not_1 (Q_2, \平时作业3_d锁存器_2_q );
endmodule

module Practice_12_2_to_4_decoder (
  input  A1,
  input  A2,
  input  En,
  output x,
  output y,
  output z,
  output w
);

  wire not_1_out, not_2_out, not_3_out, not_4_out;

  and and_1 (x, A1, A2, En);
  not not_1 (not_1_out, A2);
  not not_2 (not_2_out, A1);
  not not_3 (not_3_out, A1);
  not not_4 (not_4_out, A2);
  and and_2 (y, A1, not_1_out, En);
  and and_3 (z, not_2_out, A2, En);
  and and_4 (w, not_3_out, not_4_out, En);
endmodule

module \Practice_12_4位Register_File  (
  input  [1:0] Write_Address,
  input  [1:0] A_Address,
  input  Write_Enable,
  input  [3:0] Write_Date,
  output [3:0] out_5
);

  wire practice_12_2_to_4_decoder_1_w, practice_12_2_to_4_decoder_1_x, practice_12_2_to_4_decoder_1_z,
       \平时作业3_d锁存器_12_q ;
  wire [3:0] \平时作业3_d锁存器_7_q_prime , \平时作业3_d锁存器_11_q , \平时作业3_d锁存器_15_q , \平时作业3_d锁存器_16_q ;

  Practice_12_2_to_4_decoder practice_12_2_to_4_decoder_1 (
    .A1(Write_Address[0]), .A2(Write_Address[1]), .En(Write_Enable), .x(practice_12_2_to_4_decoder_1_x),
    .y(Write_Date[1]), .z(practice_12_2_to_4_decoder_1_z), .w(practice_12_2_to_4_decoder_1_w));
  \平时作业3_D锁存器  \u_平时作业3_d锁存器_1  (
    .CLK(practice_12_2_to_4_decoder_1_w), .D(Write_Date[3]), .Q(\平时作业3_d锁存器_11_q [3]));  // open: Q_prime, Reset
  \平时作业3_D锁存器  \u_平时作业3_d锁存器_2  (
    .CLK(Write_Date[1]), .D(Write_Date[3]), .Q(\平时作业3_d锁存器_7_q_prime [3]));  // open: Q_prime, Reset
  \平时作业3_D锁存器  \u_平时作业3_d锁存器_3  (
    .CLK(practice_12_2_to_4_decoder_1_z), .D(Write_Date[3]), .Q(\平时作业3_d锁存器_15_q [3]));  // open: Q_prime, Reset
  \平时作业3_D锁存器  \u_平时作业3_d锁存器_4  (
    .CLK(practice_12_2_to_4_decoder_1_x), .D(Write_Date[3]), .Q(\平时作业3_d锁存器_16_q [3]));  // open: Q_prime, Reset
  \平时作业3_D锁存器  \u_平时作业3_d锁存器_5  (
    .CLK(practice_12_2_to_4_decoder_1_w), .D(Write_Date[2]), .Q(\平时作业3_d锁存器_11_q [2]));  // open: Q_prime, Reset
  \平时作业3_D锁存器  \u_平时作业3_d锁存器_6  (
    .CLK(practice_12_2_to_4_decoder_1_w), .D(Write_Date[1]), .Q(\平时作业3_d锁存器_11_q [1]));  // open: Q_prime, Reset
  \平时作业3_D锁存器  \u_平时作业3_d锁存器_7  (
    .CLK(Write_Date[1]), .D(Write_Date[1]), .Q(\平时作业3_d锁存器_7_q_prime [1]), .Q_prime(\平时作业3_d锁存器_7_q_prime [0]));  // open: Reset
  \平时作业3_D锁存器  \u_平时作业3_d锁存器_8  (
    .CLK(Write_Date[1]), .D(Write_Date[2]), .Q(\平时作业3_d锁存器_7_q_prime [2]));  // open: Q_prime, Reset
  \平时作业3_D锁存器  \u_平时作业3_d锁存器_9  (
    .CLK(practice_12_2_to_4_decoder_1_z), .D(Write_Date[2]), .Q(\平时作业3_d锁存器_15_q [2]));  // open: Q_prime, Reset
  \平时作业3_D锁存器  \u_平时作业3_d锁存器_10  (
    .CLK(practice_12_2_to_4_decoder_1_x), .D(Write_Date[2]), .Q(\平时作业3_d锁存器_16_q [2]));  // open: Q_prime, Reset
  \平时作业3_D锁存器  \u_平时作业3_d锁存器_11  (
    .CLK(practice_12_2_to_4_decoder_1_w), .D(Write_Date[0]), .Q(\平时作业3_d锁存器_11_q [0]));  // open: Q_prime, Reset
  \平时作业3_D锁存器  \u_平时作业3_d锁存器_12  (
    .CLK(Write_Date[1]), .D(Write_Date[0]), .Q(\平时作业3_d锁存器_12_q ));  // open: Q_prime, Reset
  \平时作业3_D锁存器  \u_平时作业3_d锁存器_13  (
    .CLK(practice_12_2_to_4_decoder_1_z), .D(Write_Date[1]), .Q(\平时作业3_d锁存器_15_q [1]));  // open: Q_prime, Reset
  \平时作业3_D锁存器  \u_平时作业3_d锁存器_14  (
    .CLK(practice_12_2_to_4_decoder_1_x), .D(Write_Date[1]), .Q(\平时作业3_d锁存器_16_q [1]));  // open: Q_prime, Reset
  \平时作业3_D锁存器  \u_平时作业3_d锁存器_15  (
    .CLK(practice_12_2_to_4_decoder_1_z), .D(Write_Date[0]), .Q(\平时作业3_d锁存器_15_q [0]));  // open: Q_prime, Reset
  \平时作业3_D锁存器  \u_平时作业3_d锁存器_16  (
    .CLK(practice_12_2_to_4_decoder_1_x), .D(Write_Date[0]), .Q(\平时作业3_d锁存器_16_q [0]));  // open: Q_prime, Reset
  Multiplexer #(.select(2), .width(4), .disabled("Z"), .enable("false")) multiplexer_1 (
    .in0(\平时作业3_d锁存器_11_q ), .in1(\平时作业3_d锁存器_7_q_prime ), .in2(\平时作业3_d锁存器_15_q ), .in3(\平时作业3_d锁存器_16_q ),
    .out(out_5), .sel(A_Address));
endmodule

module \快速乘法器的控制电路  (
  input  C1,
  input  C0,
  input  CJ,
  output X1,
  output X0,
  output CJ2
);

  wire and_1_out, and_2_out, and_3_out, and_4_out, and_5_out, and_6_out, and_7_out, not_1_out, not_2_out,
       not_3_out, not_4_out, not_5_out;

  not not_1 (not_1_out, C1);
  not not_2 (not_2_out, C0);
  not not_3 (not_3_out, CJ);
  not not_4 (not_4_out, C0);
  not not_5 (not_5_out, CJ);
  and and_1 (and_1_out, C1, CJ);
  and and_2 (and_2_out, C1, C0);
  and and_3 (and_3_out, not_1_out, C0, CJ);
  and and_4 (and_4_out, C1, not_2_out);
  and and_5 (and_5_out, C1, not_3_out);
  and and_6 (and_6_out, not_4_out, CJ);
  and and_7 (and_7_out, C0, not_5_out);
  or or_1 (CJ2, and_1_out, and_2_out);
  or or_2 (X1, and_3_out, and_4_out, and_5_out);
  or or_3 (X0, and_6_out, and_7_out);
endmodule

module \快速乘法器电路  (
  input  [7:0] in_1,
  input  [7:0] \乘数C ,
  input  in_3,
  output [15:0] out_4
);

  wire bitselector_4_out, bitselector_5_out, CLK, register_3_q, Restart, \快速乘法器的控制电路_1_x1 ;
  wire [1:0] bitselector_3_out, \快速乘法器的控制电路_1_cj2 ;
  wire [6:0] bitselector_1_out, bitselector_2_out;
  wire [8:0] bit_extender_2_out, multiplexer_2_out, register_2_q, shifter_3_out;
  wire [14:0] adder_1_out, bit_extender_1_out, multiplexer_1_out, multiplexer_3_out, negator_1_out,
       register_1_q, shifter_1_out, shifter_2_out;

  BitSelector #(.width(8), .group(7)) bitselector_1 (.in(in_1), .out(bitselector_1_out), .sel(1'b0));
  assign bit_extender_1_out = {{8{1'b0}}, bitselector_1_out};  // Bit_Extender bit_extender_1
  BitSelector #(.width(8), .group(7)) bitselector_2 (.in(\乘数C ), .out(bitselector_2_out), .sel(1'b0));
  Multiplexer #(.select(1), .width(15), .disabled("Z"), .enable("false")) multiplexer_1 (
    .in0(bit_extender_1_out), .in1(shifter_1_out), .out(multiplexer_1_out), .sel(in_3));
  Register #(.width(15), .trigger("rising"), .Select("low")) register_1 (
    .D(multiplexer_1_out), .Q(register_1_q), .clk(CLK), .clr(Restart));  // open: en
  assign bit_extender_2_out = {{2{1'b0}}, bitselector_2_out};  // Bit_Extender bit_extender_2
  Multiplexer #(.select(1), .width(9), .disabled("Z"), .enable("false")) multiplexer_2 (
    .in0(bit_extender_2_out), .in1(shifter_3_out), .out(multiplexer_2_out), .sel(in_3));
  Clock #(.highDuration(1), .lowDuration(1)) clock_1 (.out(CLK));
  Button button_1 (.out(Restart));
  Shifter #(.width(15), .shift("ll")) shifter_1 (.in(register_1_q), .\dist (4'b0010), .out(shifter_1_out));
  Register #(.width(9), .trigger("rising"), .Select("low")) register_2 (
    .D(multiplexer_2_out), .Q(register_2_q), .clk(CLK), .clr(Restart));  // open: en
  // Probe on in_1
  // Probe on \乘数C 
  Shifter #(.width(15), .shift("ll")) shifter_2 (.in(shifter_1_out), .\dist (4'b0001), .out(shifter_2_out));
  Negator #(.width(15)) negator_1 (.in(shifter_1_out), .out(negator_1_out));
  BitSelector #(.width(9), .group(2)) bitselector_3 (.in(register_2_q), .out(bitselector_3_out), .sel(3'b000));
  Shifter #(.width(9), .shift("lr")) shifter_3 (.in(register_2_q), .\dist (4'b0010), .out(shifter_3_out));
  BitSelector #(.width(8), .group(1)) bitselector_4 (.in(in_1), .out(bitselector_4_out), .sel(3'b111));
  BitSelector #(.width(8), .group(1)) bitselector_5 (.in(\乘数C ), .out(bitselector_5_out), .sel(3'b111));
  // Probe on out_4
  Multiplexer #(.select(2), .width(15), .disabled("Z"), .enable("false")) multiplexer_3 (
    .in0({15{1'b0}}), .in1(shifter_1_out), .in2(shifter_2_out), .in3(negator_1_out), .out(multiplexer_3_out),
    .sel(\快速乘法器的控制电路_1_cj2 ));
  \快速乘法器的控制电路  \u_快速乘法器的控制电路_1  (
    .C1(bitselector_3_out[0]), .C0(bitselector_3_out[1]), .CJ(register_3_q), .CJ2(\快速乘法器的控制电路_1_cj2 [0]),
    .X0(\快速乘法器的控制电路_1_cj2 [1]), .X1(\快速乘法器的控制电路_1_x1 ));
  Register #(.width(1), .trigger("rising"), .Select("low")) register_3 (
    .D(\快速乘法器的控制电路_1_x1 ), .Q(register_3_q), .clk(CLK), .clr(Restart));  // open: en
  xor xor_1 (out_4[15], bitselector_4_out, bitselector_5_out);
  Adder #(.width(15)) adder_1 (.a(multiplexer_3_out), .b(out_4[14:0]), .out(adder_1_out));  // open: cin, cout
  Register #(.width(15), .trigger("rising"), .Select("low")) register_4 (
    .D(adder_1_out), .Q(out_4[14:0]), .clk(CLK), .clr(Restart));  // open: en

  // Other names for the same wires on the sheet: Start = in_3

  // Notes on the sheet:
  //   被乘数B
  //   x
  //   2B
  //   -B
  //   =
endmodule
